// Logisim project cpu.circ as structural Verilog: 1 circuit, main circuit proc
module proc (
  input  irq,
  input  irq_2,
  input  [7:0] Wr,
  input  str,
  input  ld,
  input  [7:0] Ad,
  output irq_3,
  output ready,
  output [7:0] Dt
);

  wire and_1_out, and_2_out, and_3_out, and_4_out, button_1_out, cdm_8_1_data_code_prime, cdm_8_1_iack,
       cdm_8_1_load_st_prime, cdm_8_1_mem, cl, d_ff_1_q, decoder_1_out0, decoder_1_out1, decoder_2_out0,
       decoder_2_out1, decoder_3_out0, decoder_3_out1, multiplexer_3_out, multiplexer_4_out, not_1_out,
       not_2_out, or_1_out;
  wire [7:0] cdm_8_1_addr, cdm_8_1_data_out, cdm_8_1_pc, cdm_8_1_ps, cdm_8_1_r0, cdm_8_1_r1, cdm_8_1_r2,
       cdm_8_1_r3, cdm_8_1_sp, controlled_buffer_1_out, controlled_buffer_2_out, controlled_buffer_3_out,
       controlled_buffer_5_out, counter_1_q, multiplexer_1_out, multiplexer_2_out;

  D_Flip_Flop d_ff_1 (.clk(irq), .D(irq), .Q(d_ff_1_q), .reset(cdm_8_1_iack));  // open: Qn, preset, en
  Clock clock_1 (.out(cl));
  // Probe on cdm_8_1_r1
  // Probe on cdm_8_1_r0
  Button button_1 (.out(button_1_out));
  // Probe on cdm_8_1_r3
  // Probe on cdm_8_1_r2
  // Probe on cdm_8_1_pc
  // Probe on cdm_8_1_ps
  // Probe on cdm_8_1_sp
  Decoder #(.disabled(0)) decoder_1 (
    .out0(decoder_1_out0), .out1(decoder_1_out1), .sel(cdm_8_1_data_code_prime), .en(cdm_8_1_mem));
  not not_1 (not_1_out, cdm_8_1_load_st_prime);
  assign controlled_buffer_1_out = not_1_out ? cdm_8_1_data_out : 8'bz;  // Controlled_Buffer controlled_buffer_1
  CdM_8 cdm_8_1 (
    .data_code_prime(cdm_8_1_data_code_prime), .R0(cdm_8_1_r0), .R1(cdm_8_1_r1), .mem(cdm_8_1_mem),
    .R2(cdm_8_1_r2), .load_st_prime(cdm_8_1_load_st_prime), .R3(cdm_8_1_r3), .addr(cdm_8_1_addr),
    .PC(cdm_8_1_pc), .SP(cdm_8_1_sp), .data_out(cdm_8_1_data_out), .data_in(controlled_buffer_2_out),
    .PS(cdm_8_1_ps), .clk(cl), .rset(button_1_out), .IAck(cdm_8_1_iack), .IRQ(d_ff_1_q), .vector(3'b000));  // open: page, shadow
  assign controlled_buffer_2_out = cdm_8_1_load_st_prime ? controlled_buffer_1_out : 8'bz;  // Controlled_Buffer controlled_buffer_2
  and and_1 (and_1_out, cdm_8_1_addr[3], cdm_8_1_addr[4], cdm_8_1_addr[5], cdm_8_1_addr[6], cdm_8_1_addr[7], decoder_1_out1);
  and and_2 (and_2_out, decoder_1_out1, ~and_1_out);  // AND_Gate
  ROM rom_1 (.addr(cdm_8_1_addr), .data(controlled_buffer_1_out), .sel(decoder_1_out0));
  RAM ram_1 (
    .addr(cdm_8_1_addr), .data(controlled_buffer_1_out), .sel(and_2_out), .clk(cl), .ld(cdm_8_1_load_st_prime));  // open: clr
  // Probe on cdm_8_1_addr[2:0]
  // Probe on and_1_out
  // Probe on controlled_buffer_1_out
  // Probe on cdm_8_1_load_st_prime
  and and_3 (and_3_out, and_1_out, ~cdm_8_1_addr[2], ~cdm_8_1_addr[1], ~cdm_8_1_addr[0]);  // AND_Gate
  Counter #(.max('h35), .trigger("falling")) counter_1 (
    .Q(counter_1_q), .clk(and_3_out), .clr(decoder_3_out1));  // open: load, D, count, carry
  Multiplexer #(.width(8), .enable("false")) multiplexer_1 (
    .in0(counter_1_q), .in1(Ad), .out(multiplexer_1_out), .sel(ready));
  Multiplexer #(.width(8), .enable("false")) multiplexer_2 (
    .in0(controlled_buffer_3_out), .in1(Wr), .out(multiplexer_2_out), .sel(ready));
  or or_1 (or_1_out, and_3_out, ready);
  Multiplexer #(.enable("false")) multiplexer_3 (.in0(decoder_2_out0), .in1(str), .out(multiplexer_3_out), .sel(ready));
  Decoder #(.disabled(0)) decoder_2 (
    .out0(decoder_2_out0), .out1(decoder_2_out1), .sel(cdm_8_1_load_st_prime), .en(and_3_out));
  assign controlled_buffer_3_out = decoder_2_out0 ? controlled_buffer_1_out : 8'bz;  // Controlled_Buffer controlled_buffer_3
  assign controlled_buffer_1_out = decoder_2_out1 ? Dt : 8'bz;  // Controlled_Buffer controlled_buffer_4
  RAM #(.bus("separate")) ram_2 (
    .addr(multiplexer_1_out), .din(multiplexer_2_out), .data(Dt), .str(multiplexer_3_out), .sel(or_1_out),
    .clk(cl), .ld(multiplexer_4_out));  // open: clr
  Multiplexer #(.enable("false")) multiplexer_4 (.in0(decoder_2_out1), .in1(ld), .out(multiplexer_4_out), .sel(ready));
  and and_4 (and_4_out, and_1_out, ~cdm_8_1_addr[2], ~cdm_8_1_addr[1], cdm_8_1_addr[0]);  // AND_Gate
  Decoder #(.disabled(0)) decoder_3 (
    .out0(decoder_3_out0), .out1(decoder_3_out1), .sel(cdm_8_1_load_st_prime), .en(and_4_out));
  assign controlled_buffer_5_out = decoder_3_out0 ? controlled_buffer_1_out : 8'bz;  // Controlled_Buffer controlled_buffer_5
  not not_2 (not_2_out, controlled_buffer_5_out[0]);
  D_Flip_Flop d_ff_2 (.Q(ready), .preset(controlled_buffer_5_out[0]), .reset(not_2_out));  // open: clk, D, Qn, en

  // Notes on the sheet:
  //   contents of rom_1 (hex, n*v repeats v):
  //   cd ef c1 d1 a c1 d1 80 c1 d9 c5 ee d d0 f9 d1 1 a1 d5 ee d d0 f9 d1 0 a1 b0 d0 f8 d2 0 d3 aa ff d1
  //   36 79 e0 2d b1 ad 8e 8f ee 22 d3 aa ff d2 ab fa d1 ac f5 c2 c1 c3 d0 0 ba d1 8 74 e0 5b bf 7b e3 4f
  //   c7 c5 c6 a6 8d 8c d6 62 ee 59 c7 c5 a7 8d c1 d1 6 17 c3 8c ee 3c d6 80 d6 9b cc 3 d9 d2 8 72 e0 6f
  //   a7 d2 6 1b 8d 8c ee 62 d7 b0 d1 0 d2 6 76 e0 7f b2 ae 8f 8d 8c ee 73 d7 d0 ac f0 d1 0 d3 0 c0 c1 d2
  //   8 76 e0 98 d6 70 c5 8d c4 8c c0 c1 ee 89 c5 c4 d7 d0 f8 d2 0 d1 36 79 e0 a9 bb a3 8e ee 9f d7 30 60
  //   70 67*0 15 d
endmodule
