// Logisim project nameInput.circ as structural Verilog: 9 circuits, main circuit lb
module lb (
  input  CLOCK,
  input  [6:0] ascii,
  input  [7:0] score,
  input  enterName,
  input  start,
  output [3:0] out_6,
  output [3:0] out_7,
  output [3:0] out_8,
  output [6:0] out_9,
  output [6:0] out_10,
  output [6:0] out_11,
  output [6:0] out_12,
  output [6:0] out_13,
  output [6:0] out_14,
  output [6:0] out_15,
  output [6:0] out_16,
  output [6:0] out_17,
  output [6:0] out_18,
  output [6:0] out_19,
  output [6:0] out_20,
  output [6:0] out_21,
  output [6:0] out_22,
  output [6:0] out_23,
  output [6:0] out_24,
  output [6:0] out_25,
  output [6:0] out_26,
  output [6:0] out_27,
  output [6:0] out_28,
  output [6:0] out_29,
  output [6:0] out_30,
  output [6:0] out_31,
  output [6:0] out_32,
  output [6:0] out_33,
  output [6:0] out_34,
  output [6:0] out_35,
  output [6:0] out_36,
  output [6:0] out_37,
  output [6:0] out_38,
  output [6:0] out_39,
  output [6:0] out_40,
  output [3:0] out_41,
  output [3:0] out_42,
  output [3:0] out_43,
  output [6:0] out_44,
  output [6:0] out_45,
  output [6:0] out_46,
  output [6:0] out_47,
  output [6:0] out_48,
  output [6:0] out_49,
  output [6:0] out_50,
  output [6:0] out_51,
  output [6:0] out_52,
  output [6:0] out_53,
  output [6:0] out_54,
  output [6:0] out_55,
  output [6:0] out_56,
  output [6:0] out_57,
  output [6:0] out_58,
  output [6:0] out_59,
  output [6:0] out_60,
  output [6:0] out_61,
  output [6:0] out_62,
  output [6:0] out_63,
  output [6:0] out_64,
  output [6:0] out_65,
  output [6:0] out_66,
  output [6:0] out_67,
  output [6:0] out_68,
  output [6:0] out_69,
  output [6:0] out_70,
  output [6:0] out_71,
  output [6:0] out_72,
  output [6:0] out_73,
  output [6:0] out_74,
  output [6:0] out_75,
  output [3:0] out_76,
  output [3:0] out_77,
  output [3:0] out_78,
  output [6:0] out_79,
  output [6:0] out_80,
  output [6:0] out_81,
  output [6:0] out_82,
  output [6:0] out_83,
  output [6:0] out_84,
  output [6:0] out_85,
  output [6:0] out_86,
  output [6:0] out_87,
  output [6:0] out_88,
  output [6:0] out_89,
  output [6:0] out_90,
  output [6:0] out_91,
  output [6:0] out_92,
  output [6:0] out_93,
  output [6:0] out_94,
  output [6:0] out_95,
  output [6:0] out_96,
  output [6:0] out_97,
  output [6:0] out_98,
  output [6:0] out_99,
  output [6:0] out_100,
  output [6:0] out_101,
  output [6:0] out_102,
  output [6:0] out_103,
  output [6:0] out_104,
  output [6:0] out_105,
  output [6:0] out_106,
  output [6:0] out_107,
  output [6:0] out_108,
  output [6:0] out_109,
  output [6:0] out_110,
  output [3:0] out_111,
  output [3:0] out_112,
  output [3:0] out_113,
  output [6:0] out_114,
  output [6:0] out_115,
  output [6:0] out_116,
  output [6:0] out_117,
  output [6:0] out_118,
  output [6:0] out_119,
  output [6:0] out_120,
  output [6:0] out_121,
  output [6:0] out_122,
  output [6:0] out_123,
  output [6:0] out_124,
  output [6:0] out_125,
  output [6:0] out_126,
  output [6:0] out_127,
  output [6:0] out_128,
  output [6:0] out_129,
  output [6:0] out_130,
  output [6:0] out_131,
  output [6:0] out_132,
  output [6:0] out_133,
  output [6:0] out_134,
  output [6:0] out_135,
  output [6:0] out_136,
  output [6:0] out_137,
  output [6:0] out_138,
  output [6:0] out_139,
  output [6:0] out_140,
  output [6:0] out_141,
  output [6:0] out_142,
  output [6:0] out_143,
  output [6:0] out_144,
  output [6:0] out_145,
  output [3:0] out_146,
  output [3:0] out_147,
  output [3:0] out_148,
  output [6:0] out_149,
  output [6:0] out_150,
  output [6:0] out_151,
  output [6:0] out_152,
  output [6:0] out_153,
  output [6:0] out_154,
  output [6:0] out_155,
  output [6:0] out_156,
  output [6:0] out_157,
  output [6:0] out_158,
  output [6:0] out_159,
  output [6:0] out_160,
  output [6:0] out_161,
  output [6:0] out_162,
  output [6:0] out_163,
  output [6:0] out_164,
  output [6:0] out_165,
  output [6:0] out_166,
  output [6:0] out_167,
  output [6:0] out_168,
  output [6:0] out_169,
  output [6:0] out_170,
  output [6:0] out_171,
  output [6:0] out_172,
  output [6:0] out_173,
  output [6:0] out_174,
  output [6:0] out_175,
  output [6:0] out_176,
  output [6:0] out_177,
  output [6:0] out_178,
  output [6:0] out_179,
  output [6:0] out_180,
  output [3:0] out_181,
  output [3:0] out_182,
  output [3:0] out_183,
  output [6:0] out_184,
  output [6:0] out_185,
  output [6:0] out_186,
  output [6:0] out_187,
  output [6:0] out_188,
  output [6:0] out_189,
  output [6:0] out_190,
  output [6:0] out_191,
  output [6:0] out_192,
  output [6:0] out_193,
  output [6:0] out_194,
  output [6:0] out_195,
  output [6:0] out_196,
  output [6:0] out_197,
  output [6:0] out_198,
  output [6:0] out_199,
  output [6:0] out_200,
  output [6:0] out_201,
  output [6:0] out_202,
  output [6:0] out_203,
  output [6:0] out_204,
  output [6:0] out_205,
  output [6:0] out_206,
  output [6:0] out_207,
  output [6:0] out_208,
  output [6:0] out_209,
  output [6:0] out_210,
  output [6:0] out_211,
  output [6:0] out_212,
  output [6:0] out_213,
  output [6:0] out_214,
  output [6:0] out_215,
  output [3:0] out_216,
  output [3:0] out_217,
  output [3:0] out_218,
  output [6:0] out_219,
  output [6:0] out_220,
  output [6:0] out_221,
  output [6:0] out_222,
  output [6:0] out_223,
  output [6:0] out_224,
  output [6:0] out_225,
  output [6:0] out_226,
  output [6:0] out_227,
  output [6:0] out_228,
  output [6:0] out_229,
  output [6:0] out_230,
  output [6:0] out_231,
  output [6:0] out_232,
  output [6:0] out_233,
  output [6:0] out_234,
  output [6:0] out_235,
  output [6:0] out_236,
  output [6:0] out_237,
  output [6:0] out_238,
  output [6:0] out_239,
  output [6:0] out_240,
  output [6:0] out_241,
  output [6:0] out_242,
  output [6:0] out_243,
  output [6:0] out_244,
  output [6:0] out_245,
  output [6:0] out_246,
  output [6:0] out_247,
  output [6:0] out_248,
  output [6:0] out_249,
  output [6:0] out_250,
  output [3:0] out_251,
  output [3:0] out_252,
  output [3:0] out_253,
  output [6:0] out_254,
  output [6:0] out_255,
  output [6:0] out_256,
  output [6:0] out_257,
  output [6:0] out_258,
  output [6:0] out_259,
  output [6:0] out_260,
  output [6:0] out_261,
  output [6:0] out_262,
  output [6:0] out_263,
  output [6:0] out_264,
  output [6:0] out_265,
  output [6:0] out_266,
  output [6:0] out_267,
  output [6:0] out_268,
  output [6:0] out_269,
  output [6:0] out_270,
  output [6:0] out_271,
  output [6:0] out_272,
  output [6:0] out_273,
  output [6:0] out_274,
  output [6:0] out_275,
  output [6:0] out_276,
  output [6:0] out_277,
  output [6:0] out_278,
  output [6:0] out_279,
  output [6:0] out_280,
  output [6:0] out_281,
  output [6:0] out_282,
  output [6:0] out_283,
  output [6:0] out_284,
  output [6:0] out_285,
  output kbclk
);

  wire _1, _2, _3, _4, _5, _6, _7, _8, and_1_out, and_2_out, and_3_out, and_4_out, and_5_out, button_1_out,
       button_2_out, button_4_out, button_5_out, clock_1_out, clockdelay2_1_bus_0_3, clockdelay_1_bus_0_3,
       clockdelay_2_bus_0_3, clockdelay_4_bus_0_3, comparator_1_eq, comparator_3_eq, comparator_5_eq,
       comparator_6_eq, comparator_6_gt, controlled_buffer_1_out, controlled_buffer_2_out,
       controlled_buffer_3_out, controlled_buffer_4_out, controlled_buffer_5_out, controlled_buffer_6_out,
       controlled_buffer_7_out, controlled_buffer_8_out, controlled_buffer_17_out, controlled_buffer_18_out,
       controlled_buffer_21_out, controlled_buffer_27_out, counter_3_p2, counter_4_carry, d_ff_1_qn,
       d_ff_2_q, d_ff_2_qn, d_ff_3_q, d_ff_3_qn, d_ff_4_q, d_ff_4_qn, d_ff_5_q, d_ff_6_q, d_ff_6_qn,
       decoder_2_out0, decoder_2_out1, decoder_3_out1, decoder_3_out3, impulse_1_bus_0_2, impulse_2_bus_0_2,
       impulse_3_bus_0_2, impulse_4_bus_0_2, impulse_5_bus_0_2, LBFLAG, lbImp, ldLeaderB, nor_1_out,
       nor_2_out, nor_3_out, not_1_out, or_1_out, or_2_bus_0_3, or_3_out, or_4_out, or_5_out, or_6_out,
       or_7_out, or_9_out, or_10_out, preload, proc_1_ready, proccesorFlag, pull_resistor_1_node,
       pull_resistor_2_node, pull_resistor_3_node, sigdel_1_signal_2, undriven;
  wire [2:0] bitselector_9_out, bitselector_10_out, controlled_buffer_29_out, controlled_buffer_31_out,
       counter_3_p3, counter_6_q, subtractor_2_out;
  wire [6:0] bitselector_1_out, bitselector_2_out, bitselector_3_out, bitselector_4_out, bitselector_5_out,
       bitselector_6_out, bitselector_7_out, bitselector_8_out, ram_2_data;
  wire [7:0] bit_extender_1_out, controlled_buffer_9_out, controlled_buffer_10_out, controlled_buffer_11_out,
       controlled_buffer_12_out, controlled_buffer_13_out, controlled_buffer_14_out,
       controlled_buffer_15_out, controlled_buffer_16_out, controlled_buffer_19_out,
       controlled_buffer_24_out, counter_2_q, counter_5_q, divider_1_out, lbCounter, lbData,
       multiplexer_1_out, multiplier_1_out, proc_1_dt, register_1_q, register_2_q, register_3_q,
       register_4_q, register_5_q, register_6_q, register_7_q, register_8_q, register_9_q, rom_1_data,
       subtractor_1_out;

  assign controlled_buffer_1_out = _1 ? and_1_out : 1'bz;  // Controlled_Buffer controlled_buffer_1
  assign controlled_buffer_2_out = _2 ? and_1_out : 1'bz;  // Controlled_Buffer controlled_buffer_2
  assign controlled_buffer_3_out = _3 ? and_1_out : 1'bz;  // Controlled_Buffer controlled_buffer_3
  assign controlled_buffer_4_out = _4 ? and_1_out : 1'bz;  // Controlled_Buffer controlled_buffer_4
  assign controlled_buffer_5_out = _5 ? and_1_out : 1'bz;  // Controlled_Buffer controlled_buffer_5
  assign controlled_buffer_6_out = _6 ? and_1_out : 1'bz;  // Controlled_Buffer controlled_buffer_6
  assign controlled_buffer_7_out = _7 ? and_1_out : 1'bz;  // Controlled_Buffer controlled_buffer_7
  assign controlled_buffer_8_out = _8 ? and_1_out : 1'bz;  // Controlled_Buffer controlled_buffer_8
  Register register_1 (.D(lbData), .Q(register_1_q), .clk(controlled_buffer_1_out), .clr(button_1_out));  // open: en
  bcd bcd_1 (.bus_0(register_1_q), .bus_0_2(out_6), .bus_0_3(out_8), .bus_0_4(out_7));
  Register register_2 (.D(lbData), .Q(register_2_q), .clk(controlled_buffer_2_out), .clr(button_1_out));  // open: en
  bcd bcd_2 (.bus_0(register_2_q), .bus_0_2(out_41), .bus_0_3(out_43), .bus_0_4(out_42));
  Register register_3 (.D(lbData), .Q(register_3_q), .clk(controlled_buffer_3_out), .clr(button_1_out));  // open: en
  bcd bcd_3 (.bus_0(register_3_q), .bus_0_2(out_76), .bus_0_3(out_78), .bus_0_4(out_77));
  Register register_4 (.D(lbData), .Q(register_4_q), .clk(controlled_buffer_4_out), .clr(button_1_out));  // open: en
  bcd bcd_4 (.bus_0(register_4_q), .bus_0_2(out_111), .bus_0_3(out_113), .bus_0_4(out_112));
  Register register_5 (.D(lbData), .Q(register_5_q), .clk(controlled_buffer_5_out), .clr(button_1_out));  // open: en
  bcd bcd_5 (.bus_0(register_5_q), .bus_0_2(out_146), .bus_0_3(out_148), .bus_0_4(out_147));
  Register register_6 (.D(lbData), .Q(register_6_q), .clk(controlled_buffer_6_out), .clr(button_1_out));  // open: en
  bcd bcd_6 (.bus_0(register_6_q), .bus_0_2(out_181), .bus_0_3(out_183), .bus_0_4(out_182));
  Register register_7 (.D(lbData), .Q(register_7_q), .clk(controlled_buffer_7_out), .clr(button_1_out));  // open: en
  bcd bcd_7 (.bus_0(register_7_q), .bus_0_2(out_216), .bus_0_3(out_218), .bus_0_4(out_217));
  Register register_8 (.D(lbData), .Q(register_8_q), .clk(controlled_buffer_8_out), .clr(button_1_out));  // open: en
  bcd bcd_8 (.bus_0(register_8_q), .bus_0_2(out_251), .bus_0_3(out_253), .bus_0_4(out_252));
  Button button_1 (.out(button_1_out));
  lettersDrawer lettersdrawer_1 (
    .clk(button_1_out), .bus_0(bitselector_9_out), .bus_0_2(bitselector_1_out), .out_4(out_9),
    .out_5(out_10), .out_6(out_11), .out_7(out_12), .out_8(out_13), .out_9(out_14), .out_10(out_15),
    .out_11(out_16), .out_12(out_17), .out_13(out_18), .out_14(out_19), .out_15(out_20), .out_16(out_21),
    .out_17(out_22), .out_18(out_23), .out_19(out_24), .out_20(out_25), .out_21(out_26), .out_22(out_27),
    .out_23(out_28), .out_24(out_29), .out_25(out_30), .out_26(out_31), .out_27(out_32), .out_28(out_33),
    .out_29(out_34), .out_30(out_35), .out_31(out_36), .out_32(out_37), .out_33(out_38), .out_34(out_39),
    .out_35(out_40));
  lettersDrawer lettersdrawer_2 (
    .clk(button_1_out), .bus_0(bitselector_9_out), .bus_0_2(bitselector_2_out), .out_4(out_44),
    .out_5(out_45), .out_6(out_46), .out_7(out_47), .out_8(out_48), .out_9(out_49), .out_10(out_50),
    .out_11(out_51), .out_12(out_52), .out_13(out_53), .out_14(out_54), .out_15(out_55), .out_16(out_56),
    .out_17(out_57), .out_18(out_58), .out_19(out_59), .out_20(out_60), .out_21(out_61), .out_22(out_62),
    .out_23(out_63), .out_24(out_64), .out_25(out_65), .out_26(out_66), .out_27(out_67), .out_28(out_68),
    .out_29(out_69), .out_30(out_70), .out_31(out_71), .out_32(out_72), .out_33(out_73), .out_34(out_74),
    .out_35(out_75));
  lettersDrawer lettersdrawer_3 (
    .clk(button_1_out), .bus_0(bitselector_9_out), .bus_0_2(bitselector_3_out), .out_4(out_79),
    .out_5(out_80), .out_6(out_81), .out_7(out_82), .out_8(out_83), .out_9(out_84), .out_10(out_85),
    .out_11(out_86), .out_12(out_87), .out_13(out_88), .out_14(out_89), .out_15(out_90), .out_16(out_91),
    .out_17(out_92), .out_18(out_93), .out_19(out_94), .out_20(out_95), .out_21(out_96), .out_22(out_97),
    .out_23(out_98), .out_24(out_99), .out_25(out_100), .out_26(out_101), .out_27(out_102), .out_28(out_103),
    .out_29(out_104), .out_30(out_105), .out_31(out_106), .out_32(out_107), .out_33(out_108),
    .out_34(out_109), .out_35(out_110));
  lettersDrawer lettersdrawer_4 (
    .clk(button_1_out), .bus_0(bitselector_9_out), .bus_0_2(bitselector_4_out), .out_4(out_114),
    .out_5(out_115), .out_6(out_116), .out_7(out_117), .out_8(out_118), .out_9(out_119), .out_10(out_120),
    .out_11(out_121), .out_12(out_122), .out_13(out_123), .out_14(out_124), .out_15(out_125),
    .out_16(out_126), .out_17(out_127), .out_18(out_128), .out_19(out_129), .out_20(out_130),
    .out_21(out_131), .out_22(out_132), .out_23(out_133), .out_24(out_134), .out_25(out_135),
    .out_26(out_136), .out_27(out_137), .out_28(out_138), .out_29(out_139), .out_30(out_140),
    .out_31(out_141), .out_32(out_142), .out_33(out_143), .out_34(out_144), .out_35(out_145));
  lettersDrawer lettersdrawer_5 (
    .clk(button_1_out), .bus_0(bitselector_9_out), .bus_0_2(bitselector_5_out), .out_4(out_149),
    .out_5(out_150), .out_6(out_151), .out_7(out_152), .out_8(out_153), .out_9(out_154), .out_10(out_155),
    .out_11(out_156), .out_12(out_157), .out_13(out_158), .out_14(out_159), .out_15(out_160),
    .out_16(out_161), .out_17(out_162), .out_18(out_163), .out_19(out_164), .out_20(out_165),
    .out_21(out_166), .out_22(out_167), .out_23(out_168), .out_24(out_169), .out_25(out_170),
    .out_26(out_171), .out_27(out_172), .out_28(out_173), .out_29(out_174), .out_30(out_175),
    .out_31(out_176), .out_32(out_177), .out_33(out_178), .out_34(out_179), .out_35(out_180));
  lettersDrawer lettersdrawer_6 (
    .clk(button_1_out), .bus_0(bitselector_9_out), .bus_0_2(bitselector_6_out), .out_4(out_184),
    .out_5(out_185), .out_6(out_186), .out_7(out_187), .out_8(out_188), .out_9(out_189), .out_10(out_190),
    .out_11(out_191), .out_12(out_192), .out_13(out_193), .out_14(out_194), .out_15(out_195),
    .out_16(out_196), .out_17(out_197), .out_18(out_198), .out_19(out_199), .out_20(out_200),
    .out_21(out_201), .out_22(out_202), .out_23(out_203), .out_24(out_204), .out_25(out_205),
    .out_26(out_206), .out_27(out_207), .out_28(out_208), .out_29(out_209), .out_30(out_210),
    .out_31(out_211), .out_32(out_212), .out_33(out_213), .out_34(out_214), .out_35(out_215));
  lettersDrawer lettersdrawer_7 (
    .clk(button_1_out), .bus_0(bitselector_9_out), .bus_0_2(bitselector_7_out), .out_4(out_219),
    .out_5(out_220), .out_6(out_221), .out_7(out_222), .out_8(out_223), .out_9(out_224), .out_10(out_225),
    .out_11(out_226), .out_12(out_227), .out_13(out_228), .out_14(out_229), .out_15(out_230),
    .out_16(out_231), .out_17(out_232), .out_18(out_233), .out_19(out_234), .out_20(out_235),
    .out_21(out_236), .out_22(out_237), .out_23(out_238), .out_24(out_239), .out_25(out_240),
    .out_26(out_241), .out_27(out_242), .out_28(out_243), .out_29(out_244), .out_30(out_245),
    .out_31(out_246), .out_32(out_247), .out_33(out_248), .out_34(out_249), .out_35(out_250));
  lettersDrawer lettersdrawer_8 (
    .clk(button_1_out), .bus_0(bitselector_9_out), .bus_0_2(bitselector_8_out), .out_4(out_254),
    .out_5(out_255), .out_6(out_256), .out_7(out_257), .out_8(out_258), .out_9(out_259), .out_10(out_260),
    .out_11(out_261), .out_12(out_262), .out_13(out_263), .out_14(out_264), .out_15(out_265),
    .out_16(out_266), .out_17(out_267), .out_18(out_268), .out_19(out_269), .out_20(out_270),
    .out_21(out_271), .out_22(out_272), .out_23(out_273), .out_24(out_274), .out_25(out_275),
    .out_26(out_276), .out_27(out_277), .out_28(out_278), .out_29(out_279), .out_30(out_280),
    .out_31(out_281), .out_32(out_282), .out_33(out_283), .out_34(out_284), .out_35(out_285));
  assign controlled_buffer_9_out = _1 ? lbData : 8'bz;  // Controlled_Buffer controlled_buffer_9
  BitSelector #(.group(7)) bitselector_1 (.in(controlled_buffer_9_out), .out(bitselector_1_out), .sel(1'b0));
  BitSelector #(.group(7)) bitselector_2 (.in(controlled_buffer_10_out), .out(bitselector_2_out), .sel(1'b0));
  assign controlled_buffer_10_out = _2 ? lbData : 8'bz;  // Controlled_Buffer controlled_buffer_10
  BitSelector #(.group(7)) bitselector_3 (.in(controlled_buffer_11_out), .out(bitselector_3_out), .sel(1'b0));
  assign controlled_buffer_11_out = _3 ? lbData : 8'bz;  // Controlled_Buffer controlled_buffer_11
  assign controlled_buffer_12_out = _4 ? lbData : 8'bz;  // Controlled_Buffer controlled_buffer_12
  BitSelector #(.group(7)) bitselector_4 (.in(controlled_buffer_12_out), .out(bitselector_4_out), .sel(1'b0));
  assign controlled_buffer_13_out = _5 ? lbData : 8'bz;  // Controlled_Buffer controlled_buffer_13
  BitSelector #(.group(7)) bitselector_5 (.in(controlled_buffer_13_out), .out(bitselector_5_out), .sel(1'b0));
  assign controlled_buffer_14_out = _6 ? lbData : 8'bz;  // Controlled_Buffer controlled_buffer_14
  BitSelector #(.group(7)) bitselector_6 (.in(controlled_buffer_14_out), .out(bitselector_6_out), .sel(1'b0));
  BitSelector #(.group(7)) bitselector_7 (.in(controlled_buffer_15_out), .out(bitselector_7_out), .sel(1'b0));
  assign controlled_buffer_15_out = _7 ? lbData : 8'bz;  // Controlled_Buffer controlled_buffer_15
  assign controlled_buffer_16_out = _8 ? lbData : 8'bz;  // Controlled_Buffer controlled_buffer_16
  BitSelector #(.group(7)) bitselector_8 (.in(controlled_buffer_16_out), .out(bitselector_8_out), .sel(1'b0));
  and and_1 (and_1_out, CLOCK, ldLeaderB, comparator_1_eq);
  Comparator #(.width(3)) comparator_1 (.a(bitselector_9_out), .b(3'b000), .eq(comparator_1_eq));  // open: gt, lt
  // Probe on bitselector_9_out
  BitSelector #(.group(3)) bitselector_9 (.in(subtractor_1_out), .out(bitselector_9_out), .sel(2'b00));
  BitSelector #(.group(3)) bitselector_10 (.in(divider_1_out), .out(bitselector_10_out), .sel(2'b00));
  Decoder #(.select(3), .enable("false")) decoder_1 (
    .out0(_1), .out1(_2), .out2(_3), .out3(_4), .out4(_5), .out5(_6), .out6(_7), .out7(_8),
    .sel(bitselector_10_out));
  Counter counter_1 (.Q(lbCounter), .clk(clockdelay_1_bus_0_3), .clr(d_ff_1_qn));  // open: load, D, count, carry
  clockDelay clockdelay_1 (.bus_0(d_ff_1_qn), .bus_0_2(controlled_buffer_17_out), .bus_0_3(clockdelay_1_bus_0_3));
  assign controlled_buffer_17_out = ldLeaderB ? CLOCK : 1'bz;  // Controlled_Buffer controlled_buffer_17
  // Probe on divider_1_out
  Divider divider_1 (.a(lbCounter), .b(8'h6), .out(divider_1_out));  // open: upper, rem
  // Probe on subtractor_1_out
  Subtractor subtractor_1 (.a(lbCounter), .b(multiplier_1_out), .out(subtractor_1_out));  // open: bin, bout
  Multiplier multiplier_1 (.a(8'h6), .b(divider_1_out), .out(multiplier_1_out));  // open: cin, cout
  or or_1 (or_1_out, LBFLAG, enterName, impulse_1_bus_0_2);
  impulse impulse_1 (.bus_0_2(impulse_1_bus_0_2), .bus_0(preload));
  Comparator comparator_2 (.a(lbCounter), .b(8'h2f), .eq(lbImp));  // open: gt, lt
  D_Flip_Flop d_ff_1 (.clk(or_1_out), .D(or_1_out), .Q(ldLeaderB), .Qn(d_ff_1_qn), .reset(lbImp));  // open: preset, en
  Clock clock_1 (.out(clock_1_out));
  clockDelay2 clockdelay2_1 (.bus_0(d_ff_2_qn), .bus_0_2(CLOCK), .bus_0_3(clockdelay2_1_bus_0_3));
  Button button_2 (.out(button_2_out));
  Decoder #(.enable("false")) decoder_2 (.out0(decoder_2_out0), .out1(decoder_2_out1), .sel(ldLeaderB));
  D_Flip_Flop d_ff_2 (
    .clk(d_ff_6_q), .D(d_ff_6_q), .Q(d_ff_2_q), .Qn(d_ff_2_qn), .reset(clockdelay2_1_bus_0_3));  // open: preset, en
  Counter counter_2 (
    .load(d_ff_2_q), .D(8'h30), .count(d_ff_2_qn), .Q(counter_2_q), .clk(or_2_bus_0_3), .clr(nor_1_out));  // open: carry
  \or  or_2 (.bus_0_3(or_2_bus_0_3), .bus_0(d_ff_2_q), .bus_0_2(clockdelay_2_bus_0_3));
  clockDelay clockdelay_2 (.bus_0(nor_2_out), .bus_0_2(controlled_buffer_18_out), .bus_0_3(clockdelay_2_bus_0_3));
  assign controlled_buffer_18_out = or_3_out ? CLOCK : 1'bz;  // Controlled_Buffer controlled_buffer_18
  or or_3 (or_3_out, d_ff_6_q, d_ff_4_q, d_ff_3_q);
  Decoder #(.select(3), .enable("false")) decoder_3 (
    .out1(decoder_3_out1), .out2(proccesorFlag), .out3(decoder_3_out3), .out4(LBFLAG), .sel(counter_3_p3));  // open: out0, out5, out6, out7
  // Counter #(.width(3), .max('h5)) counter_3: pin names not known; wires that end beside it: button_2_out, counter_3_p2, counter_3_p3, lbImp
  assign controlled_buffer_19_out = decoder_2_out1 ? lbCounter : 8'bz;  // Controlled_Buffer controlled_buffer_19
  assign controlled_buffer_19_out = decoder_2_out0 ? counter_2_q : 8'bz;  // Controlled_Buffer controlled_buffer_20
  Multiplexer #(.width(8), .disabled(0)) multiplexer_1 (
    .in0(controlled_buffer_19_out), .in1(counter_5_q), .out(multiplexer_1_out), .sel(not_1_out));  // open: en
  nor nor_1 (nor_1_out, d_ff_4_q, d_ff_6_q, d_ff_3_q);
  nor nor_2 (nor_2_out, d_ff_6_q, d_ff_4_q, d_ff_3_q);
  Button button_3 ();  // open: out
  sigDel sigdel_1 (.cl(CLOCK), .signal(decoder_3_out1), .signal_2(sigdel_1_signal_2));
  assign controlled_buffer_21_out = preload ? undriven : 1'bz;  // Controlled_Buffer controlled_buffer_21
  or or_4 (or_4_out, d_ff_3_q, not_1_out, d_ff_6_q);
  or or_5 (or_5_out, decoder_2_out1, d_ff_3_q, not_1_out, d_ff_6_q, d_ff_4_q);
  D_Flip_Flop d_ff_3 (
    .clk(decoder_3_out3), .D(decoder_3_out3), .Q(d_ff_3_q), .Qn(d_ff_3_qn), .reset(comparator_3_eq));  // open: preset, en
  D_Flip_Flop d_ff_4 (
    .clk(sigdel_1_signal_2), .D(sigdel_1_signal_2), .Q(d_ff_4_q), .Qn(d_ff_4_qn), .reset(pull_resistor_2_node));  // open: preset, en
  RAM #(.bus("separate")) ram_1 (
    .addr(multiplexer_1_out), .din(controlled_buffer_24_out), .data(lbData), .str(or_4_out), .sel(or_5_out),
    .clk(or_6_out), .ld(or_7_out), .clr(button_4_out));
  or or_6 (or_6_out, pull_resistor_3_node, clockdelay_2_bus_0_3);
  or or_7 (or_7_out, d_ff_4_q, decoder_2_out1);
  impulse impulse_2 (.bus_0_2(impulse_2_bus_0_2), .bus_0(d_ff_4_qn));
  impulse impulse_3 (.bus_0_2(impulse_3_bus_0_2), .bus_0(d_ff_3_qn));
  Button button_4 (.out(button_4_out));
  or or_8 (counter_3_p2, impulse_3_bus_0_2, impulse_2_bus_0_2, impulse_4_bus_0_2, impulse_5_bus_0_2);
  impulse impulse_4 (.bus_0_2(impulse_4_bus_0_2), .bus_0(d_ff_6_qn));
  Pull_Resistor pull_resistor_1 (.node(pull_resistor_1_node));
  assign pull_resistor_1_node = counter_4_carry ? proc_1_ready : 1'bz;  // Controlled_Buffer controlled_buffer_22
  Comparator comparator_3 (.a(counter_2_q), .b(8'h36), .eq(comparator_3_eq));  // open: gt, lt
  Counter #(.width(2), .max('h2), .ongoal("stay")) counter_4 (
    .carry(counter_4_carry), .clk(proc_1_ready));  // open: load, D, count, Q, clr
  Pull_Resistor pull_resistor_2 (.node(pull_resistor_2_node));
  Comparator comparator_4 (.a(counter_2_q), .b(8'h36), .eq(pull_resistor_2_node));  // open: gt, lt
  impulse impulse_5 (.bus_0_2(impulse_5_bus_0_2), .bus_0(pull_resistor_1_node));
  proc proc_1 (
    .Ad(counter_2_q), .Wr(lbData), .str(d_ff_4_q), .ld(d_ff_3_q), .Dt(proc_1_dt), .ready(proc_1_ready),
    .irq(proccesorFlag), .cl(CLOCK));
  Pull_Resistor pull_resistor_3 (.node(pull_resistor_3_node));
  and and_2 (and_2_out, not_1_out, CLOCK);
  assign pull_resistor_3_node = not_1_out ? and_2_out : 1'bz;  // Controlled_Buffer controlled_buffer_23
  assign controlled_buffer_24_out = d_ff_3_q ? proc_1_dt : 8'bz;  // Controlled_Buffer controlled_buffer_24
  assign controlled_buffer_24_out = not_1_out ? rom_1_data : 8'bz;  // Controlled_Buffer controlled_buffer_25
  assign controlled_buffer_24_out = comparator_6_gt ? bit_extender_1_out : 8'bz;  // Controlled_Buffer controlled_buffer_26
  assign bit_extender_1_out = {{1{1'b0}}, ram_2_data};  // Bit_Extender bit_extender_1
  Counter #(.max('h2f), .ongoal("stay")) counter_5 (
    .Q(counter_5_q), .carry(preload), .clk(CLOCK), .clr(button_5_out));  // open: load, D, count
  Button button_5 (.out(button_5_out));
  not not_1 (not_1_out, preload);
  D_Flip_Flop d_ff_5 (.clk(enterName), .D(enterName), .Q(d_ff_5_q), .reset(comparator_5_eq));  // open: Qn, preset, en
  clockDelay clockdelay_3 (.bus_0(comparator_5_eq), .bus_0_2(controlled_buffer_27_out), .bus_0_3(kbclk));
  assign controlled_buffer_27_out = d_ff_5_q ? CLOCK : 1'bz;  // Controlled_Buffer controlled_buffer_27
  // Probe on ascii
  ROM rom_1 (.addr(counter_5_q), .data(rom_1_data));  // open: sel
  Comparator #(.width(3)) comparator_5 (.a(3'b110), .b(counter_6_q), .eq(comparator_5_eq));  // open: gt, lt
  or or_9 (or_9_out, and_5_out, and_3_out);
  nor nor_3 (nor_3_out, ~comparator_5_eq, d_ff_6_q);  // NOR_Gate
  and and_3 (and_3_out, kbclk, ~comparator_5_eq);  // AND_Gate
  assign controlled_buffer_24_out = and_4_out ? register_9_q : 8'bz;  // Controlled_Buffer controlled_buffer_28
  and and_4 (and_4_out, comparator_6_eq, d_ff_6_q);
  Comparator #(.width(3), .mode("unsigned")) comparator_6 (
    .a(counter_6_q), .b(3'b000), .gt(comparator_6_gt), .eq(comparator_6_eq));  // open: lt
  Counter #(.width(3), .max('h7)) counter_6 (
    .Q(counter_6_q), .clk(or_9_out), .clr(nor_3_out));  // open: load, D, count, carry
  assign controlled_buffer_29_out = d_ff_5_q ? counter_6_q : 3'bz;  // Controlled_Buffer controlled_buffer_29
  assign controlled_buffer_29_out = comparator_6_gt ? controlled_buffer_31_out : 3'bz;  // Controlled_Buffer controlled_buffer_30
  or or_10 (or_10_out, d_ff_5_q, d_ff_6_q);
  Subtractor #(.width(3)) subtractor_2 (.a(counter_6_q), .b(3'b001), .out(subtractor_2_out));  // open: bin, bout
  assign controlled_buffer_31_out = d_ff_6_q ? subtractor_2_out : 3'bz;  // Controlled_Buffer controlled_buffer_31
  Pull_Resistor pull_resistor_4 (.node(kbclk));
  RAM #(.addrWidth(3), .dataWidth(7), .bus("separate")) ram_2 (
    .addr(controlled_buffer_29_out), .din(ascii), .data(ram_2_data), .str(d_ff_5_q), .sel(or_10_out),
    .clk(kbclk), .ld(d_ff_6_q));  // open: clr
  and and_5 (and_5_out, clockdelay_4_bus_0_3, d_ff_6_q);
  clockDelay clockdelay_4 (.bus_0(d_ff_6_qn), .bus_0_2(CLOCK), .bus_0_3(clockdelay_4_bus_0_3));
  D_Flip_Flop d_ff_6 (
    .clk(start), .D(start), .Q(d_ff_6_q), .Qn(d_ff_6_qn), .reset(comparator_5_eq));  // open: preset, en
  Register register_9 (.D(score), .Q(register_9_q), .clk(d_ff_6_q));  // open: en, clr

  // Other names for the same wires on the sheet: cl = CLOCK; ENTER = enterName; keyboardCL = kbclk;
  //   scoreVal[7:0] = score; STARTPROCESS = start

  // Notes on the sheet:
  //   enter
  //   clear name field
  //   выгрузить
  //   загрузить
  //   enter
  //   contents of rom_1 (hex, n*v repeats v):
  //   4 5*67 3 5*67 2 5*67
  //   load in lb
endmodule

module clockDelay (
  input  bus_0,
  input  bus_0_2,
  output bus_0_3
);

  wire comparator_1_eq, comparator_1_lt, controlled_buffer_1_out;
  wire [7:0] counter_1_q;

  assign controlled_buffer_1_out = comparator_1_lt ? bus_0_2 : 1'bz;  // Controlled_Buffer controlled_buffer_1
  Counter counter_1 (.Q(counter_1_q), .clk(controlled_buffer_1_out), .clr(bus_0));  // open: load, D, count, carry
  Comparator comparator_1 (.a(counter_1_q), .b(8'h2), .eq(comparator_1_eq), .lt(comparator_1_lt));  // open: gt
  assign bus_0_3 = comparator_1_eq ? bus_0_2 : 1'bz;  // Controlled_Buffer controlled_buffer_2
  Pull_Resistor pull_resistor_1 (.node(bus_0_3));
endmodule

module \or  (
  input  bus_0,
  input  bus_0_2,
  output bus_0_3
);

  or or_1 (bus_0_3, bus_0, bus_0_2);
endmodule

module clockDelay2 (
  input  bus_0,
  input  bus_0_2,
  output bus_0_3
);

  wire comparator_1_eq, comparator_1_lt, controlled_buffer_1_out;
  wire [7:0] counter_1_q;

  assign controlled_buffer_1_out = comparator_1_lt ? bus_0_2 : 1'bz;  // Controlled_Buffer controlled_buffer_1
  Counter counter_1 (.Q(counter_1_q), .clk(controlled_buffer_1_out), .clr(bus_0));  // open: load, D, count, carry
  Comparator comparator_1 (.a(counter_1_q), .b(8'h1), .eq(comparator_1_eq), .lt(comparator_1_lt));  // open: gt
  Pull_Resistor pull_resistor_1 (.node(bus_0_3));
  assign bus_0_3 = comparator_1_eq ? bus_0_2 : 1'bz;  // Controlled_Buffer controlled_buffer_2
endmodule

module bcd (
  input  [7:0] bus_0,
  output [3:0] bus_0_2,
  output [3:0] bus_0_3,
  output [3:0] bus_0_4
);

  wire [7:0] divider_1_out;
  wire [7:4] divider_1_rem, divider_2_out, divider_2_rem;

  // Probe on bus_0
  Divider divider_1 (.a(bus_0), .b(8'ha), .out(divider_1_out), .rem({divider_1_rem, bus_0_3}));  // open: upper
  // Probe on {divider_2_out, bus_0_2}
  Divider divider_2 (
    .a(divider_1_out), .b(8'ha), .out({divider_2_out, bus_0_2}), .rem({divider_2_rem, bus_0_4}));  // open: upper
  // Probe on {divider_2_rem, bus_0_4}
  // Probe on bus_0_3
endmodule

module lettersDrawer (
  input  [2:0] bus_0,
  input  [6:0] bus_0_2,
  input  clk,
  output [6:0] out_4,
  output [6:0] out_5,
  output [6:0] out_6,
  output [6:0] out_7,
  output [6:0] out_8,
  output [6:0] out_9,
  output [6:0] out_10,
  output [6:0] out_11,
  output [6:0] out_12,
  output [6:0] out_13,
  output [6:0] out_14,
  output [6:0] out_15,
  output [6:0] out_16,
  output [6:0] out_17,
  output [6:0] out_18,
  output [6:0] out_19,
  output [6:0] out_20,
  output [6:0] out_21,
  output [6:0] out_22,
  output [6:0] out_23,
  output [6:0] out_24,
  output [6:0] out_25,
  output [6:0] out_26,
  output [6:0] out_27,
  output [6:0] out_28,
  output [6:0] out_29,
  output [6:0] out_30,
  output [6:0] out_31,
  output [6:0] out_32,
  output [6:0] out_33,
  output [6:0] out_34,
  output [6:0] out_35
);

  wire decoder_1_out1, decoder_1_out2, decoder_1_out3, decoder_1_out4, decoder_1_out5, nor_1_out;
  wire [6:0] controlled_buffer_1_out, register_1_q, register_2_q, register_3_q, register_4_q, register_5_q;

  getLetter getletter_1 (
    .a_2(out_4[5:1]), .a_3(out_5[5:1]), .a_4(out_6[5:1]), .a_5(out_7[5:1]), .a_6(out_8[5:1]), .a(register_1_q));
  Register #(.width(7)) register_1 (.D(bus_0_2), .Q(register_1_q), .clk(decoder_1_out1), .clr(clk));  // open: en
  getLetter getletter_2 (
    .a_2(out_10[5:1]), .a_3(out_11[5:1]), .a_4(out_12[5:1]), .a_5(out_13[5:1]), .a_6(out_14[5:1]),
    .a(register_2_q));
  Register #(.width(7)) register_2 (.D(bus_0_2), .Q(register_2_q), .clk(decoder_1_out2), .clr(clk));  // open: en
  getLetter getletter_3 (
    .a_2(out_16[5:1]), .a_3(out_17[5:1]), .a_4(out_18[5:1]), .a_5(out_19[5:1]), .a_6(out_20[5:1]),
    .a(register_3_q));
  Register #(.width(7)) register_3 (.D(bus_0_2), .Q(register_3_q), .clk(decoder_1_out3), .clr(clk));  // open: en
  getLetter getletter_4 (
    .a_2(out_22[5:1]), .a_3(out_23[5:1]), .a_4(out_24[5:1]), .a_5(out_25[5:1]), .a_6(out_26[5:1]),
    .a(register_4_q));
  Register #(.width(7)) register_4 (.D(bus_0_2), .Q(register_4_q), .clk(decoder_1_out4), .clr(clk));  // open: en
  getLetter getletter_5 (
    .a_2(out_28[5:1]), .a_3(out_29[5:1]), .a_4(out_30[5:1]), .a_5(out_31[5:1]), .a_6(out_32[5:1]),
    .a(register_5_q));
  Register #(.width(7)) register_5 (.D(bus_0_2), .Q(register_5_q), .clk(decoder_1_out5), .clr(clk));  // open: en
  assign controlled_buffer_1_out = nor_1_out ? {7{1'b0}} : 7'bz;  // Controlled_Buffer controlled_buffer_1
  nor nor_1 (nor_1_out, decoder_1_out5, decoder_1_out4, decoder_1_out3, decoder_1_out2, decoder_1_out1);
  Decoder #(.select(3), .enable("false")) decoder_1 (
    .out1(decoder_1_out1), .out2(decoder_1_out2), .out3(decoder_1_out3), .out4(decoder_1_out4),
    .out5(decoder_1_out5), .sel(bus_0));  // open: out0, out6, out7

  assign {out_4[6], out_4[0]} = 2'b00;
  assign {out_5[6], out_5[0]} = 2'b00;
  assign {out_6[6], out_6[0]} = 2'b00;
  assign {out_7[6], out_7[0]} = 2'b00;
  assign {out_8[6], out_8[0]} = 2'b00;
  assign out_9 = {7{1'b0}};
  assign {out_10[6], out_10[0]} = 2'b00;
  assign {out_11[6], out_11[0]} = 2'b00;
  assign {out_12[6], out_12[0]} = 2'b00;
  assign {out_13[6], out_13[0]} = 2'b00;
  assign {out_14[6], out_14[0]} = 2'b00;
  assign out_15 = {7{1'b0}};
  assign {out_16[6], out_16[0]} = 2'b00;
  assign {out_17[6], out_17[0]} = 2'b00;
  assign {out_18[6], out_18[0]} = 2'b00;
  assign {out_19[6], out_19[0]} = 2'b00;
  assign {out_20[6], out_20[0]} = 2'b00;
  assign out_21 = {7{1'b0}};
  assign {out_22[6], out_22[0]} = 2'b00;
  assign {out_23[6], out_23[0]} = 2'b00;
  assign {out_24[6], out_24[0]} = 2'b00;
  assign {out_25[6], out_25[0]} = 2'b00;
  assign {out_26[6], out_26[0]} = 2'b00;
  assign out_27 = {7{1'b0}};
  assign {out_28[6], out_28[0]} = 2'b00;
  assign {out_29[6], out_29[0]} = 2'b00;
  assign {out_30[6], out_30[0]} = 2'b00;
  assign {out_31[6], out_31[0]} = 2'b00;
  assign {out_32[6], out_32[0]} = 2'b00;
  assign out_33 = {7{1'b0}};
  assign out_34 = {7{1'b0}};
  assign out_35 = {7{1'b0}};
endmodule

module getLetter (
  input  [6:0] a,
  output [4:0] a_2,
  output [4:0] a_3,
  output [4:0] a_4,
  output [4:0] a_5,
  output [4:0] a_6
);

  wire button_1_out, comparator_1_eq, comparator_2_eq, comparator_3_eq, comparator_4_eq, comparator_5_eq,
       comparator_6_eq, comparator_7_eq, comparator_8_eq, comparator_9_eq, comparator_10_eq,
       comparator_11_eq, comparator_12_eq, comparator_13_eq, comparator_14_eq, comparator_15_eq,
       comparator_16_eq, comparator_17_eq, comparator_18_eq, comparator_19_eq, comparator_20_eq,
       comparator_21_eq, comparator_22_eq, comparator_23_eq, comparator_24_eq, comparator_25_eq,
       comparator_26_eq, comparator_27_eq;
  wire [6:0] keyboard_1_data;

  Comparator #(.width(7)) comparator_1 (.a(a), .b(7'b1100001), .eq(comparator_1_eq));  // open: gt, lt
  Comparator #(.width(7)) comparator_2 (.a(a), .b(7'b1100010), .eq(comparator_2_eq));  // open: gt, lt
  Comparator #(.width(7)) comparator_3 (.a(a), .b(7'b1100011), .eq(comparator_3_eq));  // open: gt, lt
  Comparator #(.width(7)) comparator_4 (.a(a), .b(7'b1100100), .eq(comparator_4_eq));  // open: gt, lt
  Comparator #(.width(7)) comparator_5 (.a(a), .b(7'b1100101), .eq(comparator_5_eq));  // open: gt, lt
  Comparator #(.width(7)) comparator_6 (.a(a), .b(7'b1100110), .eq(comparator_6_eq));  // open: gt, lt
  Comparator #(.width(7)) comparator_7 (.a(a), .b(7'b1100111), .eq(comparator_7_eq));  // open: gt, lt
  Comparator #(.width(7)) comparator_8 (.a(a), .b(7'b1101000), .eq(comparator_8_eq));  // open: gt, lt
  Comparator #(.width(7)) comparator_9 (.a(a), .b(7'b1101001), .eq(comparator_9_eq));  // open: gt, lt
  Comparator #(.width(7)) comparator_10 (.a(a), .b(7'b1101010), .eq(comparator_10_eq));  // open: gt, lt
  Comparator #(.width(7)) comparator_11 (.a(a), .b(7'b1101011), .eq(comparator_11_eq));  // open: gt, lt
  Comparator #(.width(7)) comparator_12 (.a(a), .b(7'b1101100), .eq(comparator_12_eq));  // open: gt, lt
  Comparator #(.width(7)) comparator_13 (.a(a), .b(7'b1101101), .eq(comparator_13_eq));  // open: gt, lt
  assign {a_6, a_5, a_4, a_3, a_2} = comparator_1_eq ? 25'h1fa529f : 25'bz;  // Controlled_Buffer controlled_buffer_1
  assign {a_6, a_5, a_4, a_3, a_2} = comparator_2_eq ? 25'head6bf : 25'bz;  // Controlled_Buffer controlled_buffer_2
  assign {a_6, a_5, a_4, a_3, a_2} = comparator_3_eq ? 25'h118c63f : 25'bz;  // Controlled_Buffer controlled_buffer_3
  assign {a_6, a_5, a_4, a_3, a_2} = comparator_4_eq ? 25'he8c63f : 25'bz;  // Controlled_Buffer controlled_buffer_4
  assign {a_6, a_5, a_4, a_3, a_2} = comparator_5_eq ? 25'h11ad6bf : 25'bz;  // Controlled_Buffer controlled_buffer_5
  assign {a_6, a_5, a_4, a_3, a_2} = comparator_6_eq ? 25'h10a529f : 25'bz;  // Controlled_Buffer controlled_buffer_6
  assign {a_6, a_5, a_4, a_3, a_2} = comparator_7_eq ? 25'h17ad63f : 25'bz;  // Controlled_Buffer controlled_buffer_7
  assign {a_6, a_5, a_4, a_3, a_2} = comparator_8_eq ? 25'h1f2109f : 25'bz;  // Controlled_Buffer controlled_buffer_8
  assign {a_6, a_5, a_4, a_3, a_2} = comparator_9_eq ? 25'h118fe31 : 25'bz;  // Controlled_Buffer controlled_buffer_9
  assign {a_6, a_5, a_4, a_3, a_2} = comparator_10_eq ? 25'h138fe10 : 25'bz;  // Controlled_Buffer controlled_buffer_10
  assign {a_6, a_5, a_4, a_3, a_2} = comparator_11_eq ? 25'h115289f : 25'bz;  // Controlled_Buffer controlled_buffer_11
  assign {a_6, a_5, a_4, a_3, a_2} = comparator_12_eq ? 25'h10843f : 25'bz;  // Controlled_Buffer controlled_buffer_12
  assign {a_6, a_5, a_4, a_3, a_2} = comparator_13_eq ? 25'h1f4111f : 25'bz;  // Controlled_Buffer controlled_buffer_13
  assign {a_6, a_5, a_4, a_3, a_2} = comparator_14_eq ? {25{1'b0}} : 25'bz;  // Controlled_Buffer controlled_buffer_14
  assign {a_6, a_5, a_4, a_3, a_2} = comparator_15_eq ? 25'h1041d10 : 25'bz;  // Controlled_Buffer controlled_buffer_15
  assign {a_6, a_5, a_4, a_3, a_2} = comparator_16_eq ? 25'h1151151 : 25'bz;  // Controlled_Buffer controlled_buffer_16
  assign {a_6, a_5, a_4, a_3, a_2} = comparator_17_eq ? 25'h1f1105f : 25'bz;  // Controlled_Buffer controlled_buffer_17
  assign {a_6, a_5, a_4, a_3, a_2} = comparator_18_eq ? 25'h18304d8 : 25'bz;  // Controlled_Buffer controlled_buffer_18
  assign {a_6, a_5, a_4, a_3, a_2} = comparator_19_eq ? 25'h1f0843f : 25'bz;  // Controlled_Buffer controlled_buffer_19
  assign {a_6, a_5, a_4, a_3, a_2} = comparator_20_eq ? 25'h1087e10 : 25'bz;  // Controlled_Buffer controlled_buffer_20
  assign {a_6, a_5, a_4, a_3, a_2} = comparator_21_eq ? 25'h17ad6bd : 25'bz;  // Controlled_Buffer controlled_buffer_21
  assign {a_6, a_5, a_4, a_3, a_2} = comparator_22_eq ? 25'h1cada9f : 25'bz;  // Controlled_Buffer controlled_buffer_22
  assign {a_6, a_5, a_4, a_3, a_2} = comparator_23_eq ? 25'h1f9c63f : 25'bz;  // Controlled_Buffer controlled_buffer_23
  assign {a_6, a_5, a_4, a_3, a_2} = comparator_24_eq ? 25'h1ca528f : 25'bz;  // Controlled_Buffer controlled_buffer_24
  assign {a_6, a_5, a_4, a_3, a_2} = comparator_25_eq ? 25'he8c62e : 25'bz;  // Controlled_Buffer controlled_buffer_25
  assign {a_6, a_5, a_4, a_3, a_2} = comparator_26_eq ? 25'h1f1111f : 25'bz;  // Controlled_Buffer controlled_buffer_26
  assign {a_6, a_5, a_4, a_3, a_2} = comparator_27_eq ? 25'h11cd671 : 25'bz;  // Controlled_Buffer controlled_buffer_27
  Comparator #(.width(7)) comparator_14 (.a(a), .b({7{1'b0}}), .eq(comparator_14_eq));  // open: gt, lt
  Comparator #(.width(7)) comparator_15 (.a(a), .b(7'b1111001), .eq(comparator_15_eq));  // open: gt, lt
  Comparator #(.width(7)) comparator_16 (.a(a), .b(7'b1111000), .eq(comparator_16_eq));  // open: gt, lt
  Comparator #(.width(7)) comparator_17 (.a(a), .b(7'b1110111), .eq(comparator_17_eq));  // open: gt, lt
  Comparator #(.width(7)) comparator_18 (.a(a), .b(7'b1110110), .eq(comparator_18_eq));  // open: gt, lt
  Comparator #(.width(7)) comparator_19 (.a(a), .b(7'b1110101), .eq(comparator_19_eq));  // open: gt, lt
  Comparator #(.width(7)) comparator_20 (.a(a), .b(7'b1110100), .eq(comparator_20_eq));  // open: gt, lt
  Comparator #(.width(7)) comparator_21 (.a(a), .b(7'b1110011), .eq(comparator_21_eq));  // open: gt, lt
  Comparator #(.width(7)) comparator_22 (.a(a), .b(7'b1110010), .eq(comparator_22_eq));  // open: gt, lt
  Comparator #(.width(7)) comparator_23 (.a(a), .b(7'b1110001), .eq(comparator_23_eq));  // open: gt, lt
  Comparator #(.width(7)) comparator_24 (.a(a), .b(7'b1110000), .eq(comparator_24_eq));  // open: gt, lt
  Comparator #(.width(7)) comparator_25 (.a(a), .b(7'b1101111), .eq(comparator_25_eq));  // open: gt, lt
  Comparator #(.width(7)) comparator_26 (.a(a), .b(7'b1101110), .eq(comparator_26_eq));  // open: gt, lt
  Comparator #(.width(7)) comparator_27 (.a(a), .b(7'b1111010), .eq(comparator_27_eq));  // open: gt, lt
  Keyboard keyboard_1 (.clr(button_1_out), .data(keyboard_1_data));  // open: clk, re, avail
  Button button_1 (.out(button_1_out));
  // Probe on keyboard_1_data

  // Notes on the sheet:
  //   a
  //   b
  //   e
  //   g
  //   h
  //   i
  //   j
  //   k
  //   l
  //   m
  //   c
  //   d
  //   f
  //   x
  //   r
  //   p
  //   o
  //   0
  //   y
  //   w
  //   v
  //   u
  //   t
  //   s
  //   q
  //   n
  //   z
endmodule

module impulse (
  input  bus_0,
  output bus_0_2
);

  wire buffer_1_out;

  D_Flip_Flop d_ff_1 (.clk(bus_0), .D(bus_0), .Q(bus_0_2), .reset(buffer_1_out));  // open: Qn, preset, en
  buf buffer_1 (buffer_1_out, bus_0);

  // Notes on the sheet:
  //   buffer_1 drives only 1 and floats otherwise
endmodule

module sigDel (
  input  cl,
  input  signal,
  output signal_2
);

  wire comparator_1_eq, not_1_out, not_2_out;
  wire [1:0] counter_1_q;

  Counter #(.width(2), .max('h3)) counter_1 (
    .count(not_1_out), .Q(counter_1_q), .clk(cl), .clr(not_2_out));  // open: load, D, carry
  not not_1 (not_1_out, comparator_1_eq);
  not not_2 (not_2_out, signal);
  Comparator #(.width(2)) comparator_1 (.a(counter_1_q), .b(2'b10), .eq(comparator_1_eq));  // open: gt, lt
  Pull_Resistor pull_resistor_1 (.node(signal_2));
  assign signal_2 = comparator_1_eq ? signal : 1'bz;  // Controlled_Buffer controlled_buffer_1
endmodule
