// Logisim project uklonist.circ as structural Verilog: 18 circuits, main circuit main
module main (
);

  wire _1, _2, _3, _4, _5, _6, _7, _8, and_1_out, and_2_out, and_3_out, and_4_out, and_5_out, and_6_out,
       attack_controller_1_out_7, button_1_out, button_2_out, button_3_out, button_4_out, button_6_out,
       button_7_out, button_9_out, button_10_out, cl, clock_1_out, clockdelay2_1_bus_0_3,
       clockdelay_1_bus_0_3, clockdelay_2_bus_0_3, clockdelay_4_bus_0_3, colision_drawer_1_out_17,
       comparator_2_eq, comparator_4_eq, comparator_5_eq, comparator_6_eq, comparator_7_eq, comparator_7_gt,
       controlled_buffer_1_out, controlled_buffer_2_out, controlled_buffer_3_out, controlled_buffer_4_out,
       controlled_buffer_5_out, controlled_buffer_6_out, controlled_buffer_7_out, controlled_buffer_8_out,
       controlled_buffer_9_out, controlled_buffer_18_out, controlled_buffer_19_out, controlled_buffer_24_out,
       d_ff_1_q, d_ff_2_q, d_ff_3_qn, d_ff_4_q, d_ff_4_qn, d_ff_5_q, d_ff_6_q, d_ff_7_q, d_ff_8_q, d_ff_9_q,
       d_ff_9_qn, decoder_2_out0, decoder_2_out1, decoder_3_out1, decoder_3_out3, ENTER, impulse_1_bus_0_2,
       impulse_2_bus_0_2, impulse_3_bus_0_2, impulse_4_bus_0_2, impulse_5_bus_0_2, keyboardCL, LBFLAG, lbImp,
       ldLeaderB, nor_1_out, nor_2_out, nor_3_out, not_1_out, or_1_bus_0_3, or_2_out, or_3_out, or_4_out,
       or_5_out, or_6_out, or_7_out, or_8_out, proc_1_p5, proccesorFlag, sigdel_1_signal_2,
       sigdel_2_signal_2, STARTPROCESS;
  wire [1:0] joystick_1_x, joystick_1_y;
  wire [2:0] bitselector_9_out, bitselector_10_out, controlled_buffer_26_out, controlled_buffer_28_out,
       counter_4_q, counter_5_q, subtractor_2_out;
  wire [3:0] bcd_1_bus_0_2, bcd_1_bus_0_3, bcd_1_bus_0_4, bcd_2_bus_0_2, bcd_2_bus_0_3, bcd_2_bus_0_4,
       bcd_3_bus_0_2, bcd_3_bus_0_3, bcd_3_bus_0_4, bcd_4_bus_0_2, bcd_4_bus_0_3, bcd_4_bus_0_4,
       bcd_5_bus_0_2, bcd_5_bus_0_3, bcd_5_bus_0_4, bcd_6_bus_0_2, bcd_6_bus_0_3, bcd_6_bus_0_4,
       bcd_7_bus_0_2, bcd_7_bus_0_3, bcd_7_bus_0_4, bcd_8_bus_0_2, bcd_8_bus_0_3, bcd_8_bus_0_4,
       character_module_1_out_6, character_module_1_out_7, character_module_1_out_8,
       character_module_1_out_9, character_module_1_out_10, input_handeler_1_out_12, score_1_out_3,
       score_1_out_4, score_1_out_5;
  wire [4:0] counter_1_q;
  wire [5:0] character_module_1_x, character_module_1_y;
  wire [6:0] ascii, bitselector_1_out, bitselector_2_out, bitselector_3_out, bitselector_4_out,
       bitselector_5_out, bitselector_6_out, bitselector_7_out, bitselector_8_out, keyboard_1_data,
       lettersdrawer_1_out_4, lettersdrawer_1_out_5, lettersdrawer_1_out_6, lettersdrawer_1_out_7,
       lettersdrawer_1_out_8, lettersdrawer_1_out_9, lettersdrawer_1_out_10, lettersdrawer_1_out_11,
       lettersdrawer_1_out_12, lettersdrawer_1_out_13, lettersdrawer_1_out_14, lettersdrawer_1_out_15,
       lettersdrawer_1_out_16, lettersdrawer_1_out_17, lettersdrawer_1_out_18, lettersdrawer_1_out_19,
       lettersdrawer_1_out_20, lettersdrawer_1_out_21, lettersdrawer_1_out_22, lettersdrawer_1_out_23,
       lettersdrawer_1_out_24, lettersdrawer_1_out_25, lettersdrawer_1_out_26, lettersdrawer_1_out_27,
       lettersdrawer_1_out_28, lettersdrawer_1_out_29, lettersdrawer_1_out_30, lettersdrawer_1_out_31,
       lettersdrawer_1_out_32, lettersdrawer_1_out_33, lettersdrawer_1_out_34, lettersdrawer_1_out_35,
       lettersdrawer_2_out_4, lettersdrawer_2_out_5, lettersdrawer_2_out_6, lettersdrawer_2_out_7,
       lettersdrawer_2_out_8, lettersdrawer_2_out_9, lettersdrawer_2_out_10, lettersdrawer_2_out_11,
       lettersdrawer_2_out_12, lettersdrawer_2_out_13, lettersdrawer_2_out_14, lettersdrawer_2_out_15,
       lettersdrawer_2_out_16, lettersdrawer_2_out_17, lettersdrawer_2_out_18, lettersdrawer_2_out_19,
       lettersdrawer_2_out_20, lettersdrawer_2_out_21, lettersdrawer_2_out_22, lettersdrawer_2_out_23,
       lettersdrawer_2_out_24, lettersdrawer_2_out_25, lettersdrawer_2_out_26, lettersdrawer_2_out_27,
       lettersdrawer_2_out_28, lettersdrawer_2_out_29, lettersdrawer_2_out_30, lettersdrawer_2_out_31,
       lettersdrawer_2_out_32, lettersdrawer_2_out_33, lettersdrawer_2_out_34, lettersdrawer_2_out_35,
       lettersdrawer_3_out_4, lettersdrawer_3_out_5, lettersdrawer_3_out_6, lettersdrawer_3_out_7,
       lettersdrawer_3_out_8, lettersdrawer_3_out_9, lettersdrawer_3_out_10, lettersdrawer_3_out_11,
       lettersdrawer_3_out_12, lettersdrawer_3_out_13, lettersdrawer_3_out_14, lettersdrawer_3_out_15,
       lettersdrawer_3_out_16, lettersdrawer_3_out_17, lettersdrawer_3_out_18, lettersdrawer_3_out_19,
       lettersdrawer_3_out_20, lettersdrawer_3_out_21, lettersdrawer_3_out_22, lettersdrawer_3_out_23,
       lettersdrawer_3_out_24, lettersdrawer_3_out_25, lettersdrawer_3_out_26, lettersdrawer_3_out_27,
       lettersdrawer_3_out_28, lettersdrawer_3_out_29, lettersdrawer_3_out_30, lettersdrawer_3_out_31,
       lettersdrawer_3_out_32, lettersdrawer_3_out_33, lettersdrawer_3_out_34, lettersdrawer_3_out_35,
       lettersdrawer_4_out_4, lettersdrawer_4_out_5, lettersdrawer_4_out_6, lettersdrawer_4_out_7,
       lettersdrawer_4_out_8, lettersdrawer_4_out_9, lettersdrawer_4_out_10, lettersdrawer_4_out_11,
       lettersdrawer_4_out_12, lettersdrawer_4_out_13, lettersdrawer_4_out_14, lettersdrawer_4_out_15,
       lettersdrawer_4_out_16, lettersdrawer_4_out_17, lettersdrawer_4_out_18, lettersdrawer_4_out_19,
       lettersdrawer_4_out_20, lettersdrawer_4_out_21, lettersdrawer_4_out_22, lettersdrawer_4_out_23,
       lettersdrawer_4_out_24, lettersdrawer_4_out_25, lettersdrawer_4_out_26, lettersdrawer_4_out_27,
       lettersdrawer_4_out_28, lettersdrawer_4_out_29, lettersdrawer_4_out_30, lettersdrawer_4_out_31,
       lettersdrawer_4_out_32, lettersdrawer_4_out_33, lettersdrawer_4_out_34, lettersdrawer_4_out_35,
       lettersdrawer_5_out_4, lettersdrawer_5_out_5, lettersdrawer_5_out_6, lettersdrawer_5_out_7,
       lettersdrawer_5_out_8, lettersdrawer_5_out_9, lettersdrawer_5_out_10, lettersdrawer_5_out_11,
       lettersdrawer_5_out_12, lettersdrawer_5_out_13, lettersdrawer_5_out_14, lettersdrawer_5_out_15,
       lettersdrawer_5_out_16, lettersdrawer_5_out_17, lettersdrawer_5_out_18, lettersdrawer_5_out_19,
       lettersdrawer_5_out_20, lettersdrawer_5_out_21, lettersdrawer_5_out_22, lettersdrawer_5_out_23,
       lettersdrawer_5_out_24, lettersdrawer_5_out_25, lettersdrawer_5_out_26, lettersdrawer_5_out_27,
       lettersdrawer_5_out_28, lettersdrawer_5_out_29, lettersdrawer_5_out_30, lettersdrawer_5_out_31,
       lettersdrawer_5_out_32, lettersdrawer_5_out_33, lettersdrawer_5_out_34, lettersdrawer_5_out_35,
       lettersdrawer_6_out_4, lettersdrawer_6_out_5, lettersdrawer_6_out_6, lettersdrawer_6_out_7,
       lettersdrawer_6_out_8, lettersdrawer_6_out_9, lettersdrawer_6_out_10, lettersdrawer_6_out_11,
       lettersdrawer_6_out_12, lettersdrawer_6_out_13, lettersdrawer_6_out_14, lettersdrawer_6_out_15,
       lettersdrawer_6_out_16, lettersdrawer_6_out_17, lettersdrawer_6_out_18, lettersdrawer_6_out_19,
       lettersdrawer_6_out_20, lettersdrawer_6_out_21, lettersdrawer_6_out_22, lettersdrawer_6_out_23,
       lettersdrawer_6_out_24, lettersdrawer_6_out_25, lettersdrawer_6_out_26, lettersdrawer_6_out_27,
       lettersdrawer_6_out_28, lettersdrawer_6_out_29, lettersdrawer_6_out_30, lettersdrawer_6_out_31,
       lettersdrawer_6_out_32, lettersdrawer_6_out_33, lettersdrawer_6_out_34, lettersdrawer_6_out_35,
       lettersdrawer_7_out_4, lettersdrawer_7_out_5, lettersdrawer_7_out_6, lettersdrawer_7_out_7,
       lettersdrawer_7_out_8, lettersdrawer_7_out_9, lettersdrawer_7_out_10, lettersdrawer_7_out_11,
       lettersdrawer_7_out_12, lettersdrawer_7_out_13, lettersdrawer_7_out_14, lettersdrawer_7_out_15,
       lettersdrawer_7_out_16, lettersdrawer_7_out_17, lettersdrawer_7_out_18, lettersdrawer_7_out_19,
       lettersdrawer_7_out_20, lettersdrawer_7_out_21, lettersdrawer_7_out_22, lettersdrawer_7_out_23,
       lettersdrawer_7_out_24, lettersdrawer_7_out_25, lettersdrawer_7_out_26, lettersdrawer_7_out_27,
       lettersdrawer_7_out_28, lettersdrawer_7_out_29, lettersdrawer_7_out_30, lettersdrawer_7_out_31,
       lettersdrawer_7_out_32, lettersdrawer_7_out_33, lettersdrawer_7_out_34, lettersdrawer_7_out_35,
       lettersdrawer_8_out_4, lettersdrawer_8_out_5, lettersdrawer_8_out_6, lettersdrawer_8_out_7,
       lettersdrawer_8_out_8, lettersdrawer_8_out_9, lettersdrawer_8_out_10, lettersdrawer_8_out_11,
       lettersdrawer_8_out_12, lettersdrawer_8_out_13, lettersdrawer_8_out_14, lettersdrawer_8_out_15,
       lettersdrawer_8_out_16, lettersdrawer_8_out_17, lettersdrawer_8_out_18, lettersdrawer_8_out_19,
       lettersdrawer_8_out_20, lettersdrawer_8_out_21, lettersdrawer_8_out_22, lettersdrawer_8_out_23,
       lettersdrawer_8_out_24, lettersdrawer_8_out_25, lettersdrawer_8_out_26, lettersdrawer_8_out_27,
       lettersdrawer_8_out_28, lettersdrawer_8_out_29, lettersdrawer_8_out_30, lettersdrawer_8_out_31,
       lettersdrawer_8_out_32, lettersdrawer_8_out_33, lettersdrawer_8_out_34, lettersdrawer_8_out_35,
       ram_2_data;
  wire [7:0] adder_1_out, bit_extender_1_out, controlled_buffer_10_out, controlled_buffer_11_out,
       controlled_buffer_12_out, controlled_buffer_13_out, controlled_buffer_14_out,
       controlled_buffer_15_out, controlled_buffer_16_out, controlled_buffer_17_out,
       controlled_buffer_20_out, controlled_buffer_22_out, counter_3_q, divider_1_out, divider_2_rem,
       lbCounter, lbData, multiplier_1_out, proc_1_p4, register_1_q, register_2_q, register_3_q,
       register_4_q, register_5_q, register_6_q, register_7_q, register_8_q, register_9_q, register_10_q,
       scoreVal, subtractor_1_out;
  wire [31:0] attack_controller_1_out_6, borders_1_out_2, borders_1_out_3, borders_1_out_4, borders_1_out_5,
       buffer2_0_1_out_3, buffer2_0_1_out_4, buffer2_0_1_out_5, buffer2_0_1_out_6, buffer2_0_1_out_7,
       buffer2_0_1_out_8, buffer2_0_1_out_9, buffer2_0_1_out_10, buffer2_0_1_out_11, buffer2_0_1_out_12,
       buffer2_0_1_out_13, buffer2_0_1_out_14, buffer2_0_1_out_15, buffer2_0_1_out_16, buffer2_0_1_out_17,
       buffer2_0_1_out_18, buffer2_0_1_out_19, buffer2_0_1_out_20, buffer2_0_1_out_21, buffer2_0_1_out_22,
       buffer2_0_1_out_23, buffer2_0_1_out_24, buffer2_0_1_out_25, buffer2_0_1_out_26, buffer2_0_1_out_27,
       buffer2_0_1_out_28, buffer2_0_1_out_29, buffer2_0_1_out_30, buffer2_0_1_out_31, buffer2_0_1_out_32,
       buffer2_0_1_out_33, buffer2_0_1_out_34, buffer2_0_2_out_3, buffer2_0_2_out_4, buffer2_0_2_out_5,
       buffer2_0_2_out_6, buffer2_0_2_out_7, buffer2_0_2_out_8, buffer2_0_2_out_9, buffer2_0_2_out_10,
       buffer2_0_2_out_11, buffer2_0_2_out_12, buffer2_0_2_out_13, buffer2_0_2_out_14, buffer2_0_2_out_15,
       buffer2_0_2_out_16, buffer2_0_2_out_17, buffer2_0_2_out_18, buffer2_0_2_out_19, buffer2_0_2_out_20,
       buffer2_0_2_out_21, buffer2_0_2_out_22, buffer2_0_2_out_23, buffer2_0_2_out_24, buffer2_0_2_out_25,
       buffer2_0_2_out_26, buffer2_0_2_out_27, buffer2_0_2_out_28, buffer2_0_2_out_29, buffer2_0_2_out_30,
       buffer2_0_2_out_31, buffer2_0_2_out_32, buffer2_0_2_out_33, buffer2_0_2_out_34,
       buffer2_0_mirr_1_out_3, buffer2_0_mirr_1_out_4, buffer2_0_mirr_1_out_5, buffer2_0_mirr_1_out_6,
       buffer2_0_mirr_1_out_7, buffer2_0_mirr_1_out_8, buffer2_0_mirr_1_out_9, buffer2_0_mirr_1_out_10,
       buffer2_0_mirr_1_out_11, buffer2_0_mirr_1_out_12, buffer2_0_mirr_1_out_13, buffer2_0_mirr_1_out_14,
       buffer2_0_mirr_1_out_15, buffer2_0_mirr_1_out_16, buffer2_0_mirr_1_out_17, buffer2_0_mirr_1_out_18,
       buffer2_0_mirr_1_out_19, buffer2_0_mirr_1_out_20, buffer2_0_mirr_1_out_21, buffer2_0_mirr_1_out_22,
       buffer2_0_mirr_1_out_23, buffer2_0_mirr_1_out_24, buffer2_0_mirr_1_out_25, buffer2_0_mirr_1_out_26,
       buffer2_0_mirr_1_out_27, buffer2_0_mirr_1_out_28, buffer2_0_mirr_1_out_29, buffer2_0_mirr_1_out_30,
       buffer2_0_mirr_1_out_31, buffer2_0_mirr_1_out_32, buffer2_0_mirr_1_out_33, buffer2_0_mirr_1_out_34,
       buffer2_0_mirr_2_out_3, buffer2_0_mirr_2_out_4, buffer2_0_mirr_2_out_5, buffer2_0_mirr_2_out_6,
       buffer2_0_mirr_2_out_7, buffer2_0_mirr_2_out_8, buffer2_0_mirr_2_out_9, buffer2_0_mirr_2_out_10,
       buffer2_0_mirr_2_out_11, buffer2_0_mirr_2_out_12, buffer2_0_mirr_2_out_13, buffer2_0_mirr_2_out_14,
       buffer2_0_mirr_2_out_15, buffer2_0_mirr_2_out_16, buffer2_0_mirr_2_out_17, buffer2_0_mirr_2_out_18,
       buffer2_0_mirr_2_out_19, buffer2_0_mirr_2_out_20, buffer2_0_mirr_2_out_21, buffer2_0_mirr_2_out_22,
       buffer2_0_mirr_2_out_23, buffer2_0_mirr_2_out_24, buffer2_0_mirr_2_out_25, buffer2_0_mirr_2_out_26,
       buffer2_0_mirr_2_out_27, buffer2_0_mirr_2_out_28, buffer2_0_mirr_2_out_29, buffer2_0_mirr_2_out_30,
       buffer2_0_mirr_2_out_31, buffer2_0_mirr_2_out_32, buffer2_0_mirr_2_out_33, buffer2_0_mirr_2_out_34,
       bullet_gpu_1_out_8, bullet_gpu_1_out_9, bullet_gpu_1_out_10, bullet_gpu_1_out_11,
       colision_drawer_1_out_13, colision_drawer_1_out_14, colision_drawer_1_out_15, colision_drawer_1_out_16;

  Clock clock_1 (.out(clock_1_out));
  and and_1 (and_1_out, d_ff_1_q, not_1_out);
  assign controlled_buffer_1_out = and_1_out ? clock_1_out : 1'bz;  // Controlled_Buffer controlled_buffer_1
  Counter #(.width(5), .max('h1f)) counter_1 (
    .Q(counter_1_q), .clk(controlled_buffer_1_out));  // open: load, D, count, carry, clr
  Pull_Resistor pull_resistor_1 (.node(controlled_buffer_1_out));
  not not_1 (not_1_out, STARTPROCESS);
  borders borders_1 (
    .in_1(counter_1_q), .out_2(borders_1_out_2), .out_3(borders_1_out_3), .out_4(borders_1_out_4),
    .out_5(borders_1_out_5));
  and and_2 (and_2_out, counter_1_q[0], ~counter_1_q[1], ~counter_1_q[2], ~counter_1_q[3], ~counter_1_q[4]);  // AND_Gate
  D_Flip_Flop d_ff_1 (.clk(ENTER), .D(ENTER), .Q(d_ff_1_q), .reset(STARTPROCESS));  // open: Qn, preset, en
  attack_controller attack_controller_1 (
    .in_4(counter_1_q), .out_6(attack_controller_1_out_6), .out_7(attack_controller_1_out_7),
    .in_2(controlled_buffer_1_out), .in_5(d_ff_2_q));  // open: in_1, in_3
  D_Flip_Flop #(.trigger("high")) d_ff_2 (.clk(and_2_out), .D(d_ff_1_q), .Q(d_ff_2_q));  // open: Qn, preset, en, reset
  bullet_GPU bullet_gpu_1 (
    .clock32(counter_1_q), .in_4(borders_1_out_2), .in_5(borders_1_out_3), .in_6(borders_1_out_4),
    .in_7(borders_1_out_5), .out_8(bullet_gpu_1_out_8), .out_9(bullet_gpu_1_out_9),
    .out_10(bullet_gpu_1_out_10), .out_11(bullet_gpu_1_out_11), .in_1(attack_controller_1_out_6),
    .in_2(attack_controller_1_out_7));
  character_module character_module_1 (
    .x(character_module_1_x), .y(character_module_1_y), .out_6(character_module_1_out_6),
    .out_7(character_module_1_out_7), .out_8(character_module_1_out_8), .out_9(character_module_1_out_9),
    .wasd(input_handeler_1_out_12), .clock32(counter_1_q), .in_1(colision_drawer_1_out_17),
    .out_10(character_module_1_out_10));
  Comparator #(.width(4)) comparator_1 (.a(character_module_1_out_10), .b(4'b0000), .eq(STARTPROCESS));  // open: gt, lt
  colision_drawer colision_drawer_1 (
    .in_1(bullet_gpu_1_out_8), .clock32(counter_1_q), .in_3(bullet_gpu_1_out_9), .y(character_module_1_y),
    .in_5(bullet_gpu_1_out_10), .in_6(bullet_gpu_1_out_11), .x(character_module_1_x),
    .in_8(character_module_1_out_6), .in_9(character_module_1_out_7), .in_10(character_module_1_out_8),
    .in_11(character_module_1_out_9), .out_13(colision_drawer_1_out_13), .out_14(colision_drawer_1_out_14),
    .out_15(colision_drawer_1_out_15), .out_16(colision_drawer_1_out_16), .out_17(colision_drawer_1_out_17),
    .clock(controlled_buffer_1_out));
  Hex_Digit_Display hex_digit_display_1 (.value(character_module_1_out_10));  // open: dp
  DotMatrix #(.inputtype("row"), .matrixcols(32), .matrixrows(32), .persist(63)) dotmatrix_1 (
    .row0(buffer2_0_mirr_1_out_34), .row1(buffer2_0_mirr_1_out_33), .row2(buffer2_0_mirr_1_out_32),
    .row3(buffer2_0_mirr_1_out_31), .row4(buffer2_0_mirr_1_out_30), .row5(buffer2_0_mirr_1_out_29),
    .row6(buffer2_0_mirr_1_out_28), .row7(buffer2_0_mirr_1_out_27), .row8(buffer2_0_mirr_1_out_26),
    .row9(buffer2_0_mirr_1_out_25), .row10(buffer2_0_mirr_1_out_24), .row11(buffer2_0_mirr_1_out_23),
    .row12(buffer2_0_mirr_1_out_22), .row13(buffer2_0_mirr_1_out_21), .row14(buffer2_0_mirr_1_out_20),
    .row15(buffer2_0_mirr_1_out_19), .row16(buffer2_0_mirr_1_out_18), .row17(buffer2_0_mirr_1_out_17),
    .row18(buffer2_0_mirr_1_out_16), .row19(buffer2_0_mirr_1_out_15), .row20(buffer2_0_mirr_1_out_14),
    .row21(buffer2_0_mirr_1_out_13), .row22(buffer2_0_mirr_1_out_12), .row23(buffer2_0_mirr_1_out_11),
    .row24(buffer2_0_mirr_1_out_10), .row25(buffer2_0_mirr_1_out_9), .row26(buffer2_0_mirr_1_out_8),
    .row27(buffer2_0_mirr_1_out_7), .row28(buffer2_0_mirr_1_out_6), .row29(buffer2_0_mirr_1_out_5),
    .row30(buffer2_0_mirr_1_out_4), .row31(buffer2_0_mirr_1_out_3));
  buffer2_0_mirr buffer2_0_mirr_1 (
    .clock32(counter_1_q), .out_3(buffer2_0_mirr_1_out_3), .out_4(buffer2_0_mirr_1_out_4),
    .out_5(buffer2_0_mirr_1_out_5), .out_6(buffer2_0_mirr_1_out_6), .out_7(buffer2_0_mirr_1_out_7),
    .out_8(buffer2_0_mirr_1_out_8), .out_9(buffer2_0_mirr_1_out_9), .out_10(buffer2_0_mirr_1_out_10),
    .out_11(buffer2_0_mirr_1_out_11), .out_12(buffer2_0_mirr_1_out_12), .out_13(buffer2_0_mirr_1_out_13),
    .out_14(buffer2_0_mirr_1_out_14), .out_15(buffer2_0_mirr_1_out_15), .out_16(buffer2_0_mirr_1_out_16),
    .out_17(buffer2_0_mirr_1_out_17), .out_18(buffer2_0_mirr_1_out_18), .out_19(buffer2_0_mirr_1_out_19),
    .out_20(buffer2_0_mirr_1_out_20), .out_21(buffer2_0_mirr_1_out_21), .out_22(buffer2_0_mirr_1_out_22),
    .out_23(buffer2_0_mirr_1_out_23), .out_24(buffer2_0_mirr_1_out_24), .out_25(buffer2_0_mirr_1_out_25),
    .out_26(buffer2_0_mirr_1_out_26), .out_27(buffer2_0_mirr_1_out_27), .out_28(buffer2_0_mirr_1_out_28),
    .out_29(buffer2_0_mirr_1_out_29), .out_30(buffer2_0_mirr_1_out_30), .out_31(buffer2_0_mirr_1_out_31),
    .out_32(buffer2_0_mirr_1_out_32), .out_33(buffer2_0_mirr_1_out_33), .out_34(buffer2_0_mirr_1_out_34),
    .in_2(colision_drawer_1_out_14));
  DotMatrix #(.inputtype("row"), .matrixcols(32), .matrixrows(32), .persist(63)) dotmatrix_2 (
    .row0(buffer2_0_mirr_2_out_34), .row1(buffer2_0_mirr_2_out_33), .row2(buffer2_0_mirr_2_out_32),
    .row3(buffer2_0_mirr_2_out_31), .row4(buffer2_0_mirr_2_out_30), .row5(buffer2_0_mirr_2_out_29),
    .row6(buffer2_0_mirr_2_out_28), .row7(buffer2_0_mirr_2_out_27), .row8(buffer2_0_mirr_2_out_26),
    .row9(buffer2_0_mirr_2_out_25), .row10(buffer2_0_mirr_2_out_24), .row11(buffer2_0_mirr_2_out_23),
    .row12(buffer2_0_mirr_2_out_22), .row13(buffer2_0_mirr_2_out_21), .row14(buffer2_0_mirr_2_out_20),
    .row15(buffer2_0_mirr_2_out_19), .row16(buffer2_0_mirr_2_out_18), .row17(buffer2_0_mirr_2_out_17),
    .row18(buffer2_0_mirr_2_out_16), .row19(buffer2_0_mirr_2_out_15), .row20(buffer2_0_mirr_2_out_14),
    .row21(buffer2_0_mirr_2_out_13), .row22(buffer2_0_mirr_2_out_12), .row23(buffer2_0_mirr_2_out_11),
    .row24(buffer2_0_mirr_2_out_10), .row25(buffer2_0_mirr_2_out_9), .row26(buffer2_0_mirr_2_out_8),
    .row27(buffer2_0_mirr_2_out_7), .row28(buffer2_0_mirr_2_out_6), .row29(buffer2_0_mirr_2_out_5),
    .row30(buffer2_0_mirr_2_out_4), .row31(buffer2_0_mirr_2_out_3));
  buffer2_0_mirr buffer2_0_mirr_2 (
    .clock32(counter_1_q), .out_3(buffer2_0_mirr_2_out_3), .out_4(buffer2_0_mirr_2_out_4),
    .out_5(buffer2_0_mirr_2_out_5), .out_6(buffer2_0_mirr_2_out_6), .out_7(buffer2_0_mirr_2_out_7),
    .out_8(buffer2_0_mirr_2_out_8), .out_9(buffer2_0_mirr_2_out_9), .out_10(buffer2_0_mirr_2_out_10),
    .out_11(buffer2_0_mirr_2_out_11), .out_12(buffer2_0_mirr_2_out_12), .out_13(buffer2_0_mirr_2_out_13),
    .out_14(buffer2_0_mirr_2_out_14), .out_15(buffer2_0_mirr_2_out_15), .out_16(buffer2_0_mirr_2_out_16),
    .out_17(buffer2_0_mirr_2_out_17), .out_18(buffer2_0_mirr_2_out_18), .out_19(buffer2_0_mirr_2_out_19),
    .out_20(buffer2_0_mirr_2_out_20), .out_21(buffer2_0_mirr_2_out_21), .out_22(buffer2_0_mirr_2_out_22),
    .out_23(buffer2_0_mirr_2_out_23), .out_24(buffer2_0_mirr_2_out_24), .out_25(buffer2_0_mirr_2_out_25),
    .out_26(buffer2_0_mirr_2_out_26), .out_27(buffer2_0_mirr_2_out_27), .out_28(buffer2_0_mirr_2_out_28),
    .out_29(buffer2_0_mirr_2_out_29), .out_30(buffer2_0_mirr_2_out_30), .out_31(buffer2_0_mirr_2_out_31),
    .out_32(buffer2_0_mirr_2_out_32), .out_33(buffer2_0_mirr_2_out_33), .out_34(buffer2_0_mirr_2_out_34),
    .in_2(colision_drawer_1_out_15));
  _7_Segment_Display u_7_segment_display_1 (.g(1'b1), .f(1'b1), .b(1'b1), .e(1'b1), .c(1'b1));  // open: a, d, dp
  _7_Segment_Display u_7_segment_display_2 (.g(1'b1), .f(1'b1), .a(1'b1), .b(1'b1), .e(1'b1));  // open: d, c, dp
  Keyboard keyboard_1 (.clk(controlled_buffer_1_out), .data(keyboard_1_data));  // open: re, clr, avail
  input_handeler input_handeler_1 (
    .in_2(keyboard_1_data), .d(button_3_out), .s(button_4_out), .a(button_2_out), .w(button_1_out),
    .out_9(input_handeler_1_out_12[3]), .out_10(input_handeler_1_out_12[2]),
    .out_11(input_handeler_1_out_12[1]), .out_12(input_handeler_1_out_12[0]), .clock32(counter_1_q),
    .vert(joystick_1_y), .hoz(joystick_1_x));
  Joystick #(.bits(2)) joystick_1 (.x(joystick_1_x), .y(joystick_1_y));
  Hex_Digit_Display hex_digit_display_2 (.value(score_1_out_4));  // open: dp
  score score_1 (
    .in_1(counter_1_q), .bus_0(scoreVal), .out_3(score_1_out_3), .out_4(score_1_out_4), .out_5(score_1_out_5));
  Hex_Digit_Display hex_digit_display_3 (.value(score_1_out_3));  // open: dp
  Hex_Digit_Display hex_digit_display_4 (.value(score_1_out_5));  // open: dp
  DotMatrix #(.inputtype("row"), .matrixcols(32), .matrixrows(32), .persist(63)) dotmatrix_3 (
    .row0(buffer2_0_1_out_34), .row1(buffer2_0_1_out_33), .row2(buffer2_0_1_out_32),
    .row3(buffer2_0_1_out_31), .row4(buffer2_0_1_out_30), .row5(buffer2_0_1_out_29),
    .row6(buffer2_0_1_out_28), .row7(buffer2_0_1_out_27), .row8(buffer2_0_1_out_26),
    .row9(buffer2_0_1_out_25), .row10(buffer2_0_1_out_24), .row11(buffer2_0_1_out_23),
    .row12(buffer2_0_1_out_22), .row13(buffer2_0_1_out_21), .row14(buffer2_0_1_out_20),
    .row15(buffer2_0_1_out_19), .row16(buffer2_0_1_out_18), .row17(buffer2_0_1_out_17),
    .row18(buffer2_0_1_out_16), .row19(buffer2_0_1_out_15), .row20(buffer2_0_1_out_14),
    .row21(buffer2_0_1_out_13), .row22(buffer2_0_1_out_12), .row23(buffer2_0_1_out_11),
    .row24(buffer2_0_1_out_10), .row25(buffer2_0_1_out_9), .row26(buffer2_0_1_out_8),
    .row27(buffer2_0_1_out_7), .row28(buffer2_0_1_out_6), .row29(buffer2_0_1_out_5),
    .row30(buffer2_0_1_out_4), .row31(buffer2_0_1_out_3));
  DotMatrix #(.inputtype("row"), .matrixcols(32), .matrixrows(32), .persist(63)) dotmatrix_4 (
    .row0(buffer2_0_2_out_34), .row1(buffer2_0_2_out_33), .row2(buffer2_0_2_out_32),
    .row3(buffer2_0_2_out_31), .row4(buffer2_0_2_out_30), .row5(buffer2_0_2_out_29),
    .row6(buffer2_0_2_out_28), .row7(buffer2_0_2_out_27), .row8(buffer2_0_2_out_26),
    .row9(buffer2_0_2_out_25), .row10(buffer2_0_2_out_24), .row11(buffer2_0_2_out_23),
    .row12(buffer2_0_2_out_22), .row13(buffer2_0_2_out_21), .row14(buffer2_0_2_out_20),
    .row15(buffer2_0_2_out_19), .row16(buffer2_0_2_out_18), .row17(buffer2_0_2_out_17),
    .row18(buffer2_0_2_out_16), .row19(buffer2_0_2_out_15), .row20(buffer2_0_2_out_14),
    .row21(buffer2_0_2_out_13), .row22(buffer2_0_2_out_12), .row23(buffer2_0_2_out_11),
    .row24(buffer2_0_2_out_10), .row25(buffer2_0_2_out_9), .row26(buffer2_0_2_out_8),
    .row27(buffer2_0_2_out_7), .row28(buffer2_0_2_out_6), .row29(buffer2_0_2_out_5),
    .row30(buffer2_0_2_out_4), .row31(buffer2_0_2_out_3));
  Button button_1 (.out(button_1_out));
  Button button_2 (.out(button_2_out));
  Button button_3 (.out(button_3_out));
  Button button_4 (.out(button_4_out));
  _7_Segment_Display u_7_segment_display_3 (.g(1'b1), .f(1'b1), .a(1'b1), .d(1'b1), .c(1'b1));  // open: b, e, dp
  _7_Segment_Display u_7_segment_display_4 (.f(1'b1), .a(1'b1), .e(1'b1), .d(1'b1));  // open: g, b, c, dp
  Button button_5 (.out(ENTER));
  _7_Segment_Display u_7_segment_display_5 (.f(1'b1), .a(1'b1), .b(1'b1), .e(1'b1), .d(1'b1), .c(1'b1));  // open: g, dp
  _7_Segment_Display u_7_segment_display_6 (.f(1'b1), .a(1'b1), .e(1'b1));  // open: g, b, d, c, dp
  Keyboard keyboard_2 (.clk(keyboardCL), .clr(button_6_out), .data(ascii));  // open: re, avail
  Button button_6 (.out(button_6_out));
  _7_Segment_Display u_7_segment_display_7 (.g(1'b1), .f(1'b1), .a(1'b1), .e(1'b1), .d(1'b1));  // open: b, c, dp
  buffer2_0 buffer2_0_1 (
    .clock32(counter_1_q), .out_3(buffer2_0_1_out_3), .out_4(buffer2_0_1_out_4), .out_5(buffer2_0_1_out_5),
    .out_6(buffer2_0_1_out_6), .out_7(buffer2_0_1_out_7), .out_8(buffer2_0_1_out_8),
    .out_9(buffer2_0_1_out_9), .out_10(buffer2_0_1_out_10), .out_11(buffer2_0_1_out_11),
    .out_12(buffer2_0_1_out_12), .out_13(buffer2_0_1_out_13), .out_14(buffer2_0_1_out_14),
    .out_15(buffer2_0_1_out_15), .out_16(buffer2_0_1_out_16), .out_17(buffer2_0_1_out_17),
    .out_18(buffer2_0_1_out_18), .out_19(buffer2_0_1_out_19), .out_20(buffer2_0_1_out_20),
    .out_21(buffer2_0_1_out_21), .out_22(buffer2_0_1_out_22), .out_23(buffer2_0_1_out_23),
    .out_24(buffer2_0_1_out_24), .out_25(buffer2_0_1_out_25), .out_26(buffer2_0_1_out_26),
    .out_27(buffer2_0_1_out_27), .out_28(buffer2_0_1_out_28), .out_29(buffer2_0_1_out_29),
    .out_30(buffer2_0_1_out_30), .out_31(buffer2_0_1_out_31), .out_32(buffer2_0_1_out_32),
    .out_33(buffer2_0_1_out_33), .out_34(buffer2_0_1_out_34), .in_2(colision_drawer_1_out_13));
  buffer2_0 buffer2_0_2 (
    .clock32(counter_1_q), .out_3(buffer2_0_2_out_3), .out_4(buffer2_0_2_out_4), .out_5(buffer2_0_2_out_5),
    .out_6(buffer2_0_2_out_6), .out_7(buffer2_0_2_out_7), .out_8(buffer2_0_2_out_8),
    .out_9(buffer2_0_2_out_9), .out_10(buffer2_0_2_out_10), .out_11(buffer2_0_2_out_11),
    .out_12(buffer2_0_2_out_12), .out_13(buffer2_0_2_out_13), .out_14(buffer2_0_2_out_14),
    .out_15(buffer2_0_2_out_15), .out_16(buffer2_0_2_out_16), .out_17(buffer2_0_2_out_17),
    .out_18(buffer2_0_2_out_18), .out_19(buffer2_0_2_out_19), .out_20(buffer2_0_2_out_20),
    .out_21(buffer2_0_2_out_21), .out_22(buffer2_0_2_out_22), .out_23(buffer2_0_2_out_23),
    .out_24(buffer2_0_2_out_24), .out_25(buffer2_0_2_out_25), .out_26(buffer2_0_2_out_26),
    .out_27(buffer2_0_2_out_27), .out_28(buffer2_0_2_out_28), .out_29(buffer2_0_2_out_29),
    .out_30(buffer2_0_2_out_30), .out_31(buffer2_0_2_out_31), .out_32(buffer2_0_2_out_32),
    .out_33(buffer2_0_2_out_33), .out_34(buffer2_0_2_out_34), .in_2(colision_drawer_1_out_16));
  assign controlled_buffer_2_out = _1 ? and_3_out : 1'bz;  // Controlled_Buffer controlled_buffer_2
  assign controlled_buffer_3_out = _2 ? and_3_out : 1'bz;  // Controlled_Buffer controlled_buffer_3
  assign controlled_buffer_4_out = _3 ? and_3_out : 1'bz;  // Controlled_Buffer controlled_buffer_4
  assign controlled_buffer_5_out = _4 ? and_3_out : 1'bz;  // Controlled_Buffer controlled_buffer_5
  assign controlled_buffer_6_out = _5 ? and_3_out : 1'bz;  // Controlled_Buffer controlled_buffer_6
  assign controlled_buffer_7_out = _6 ? and_3_out : 1'bz;  // Controlled_Buffer controlled_buffer_7
  assign controlled_buffer_8_out = _7 ? and_3_out : 1'bz;  // Controlled_Buffer controlled_buffer_8
  assign controlled_buffer_9_out = _8 ? and_3_out : 1'bz;  // Controlled_Buffer controlled_buffer_9
  Hex_Digit_Display hex_digit_display_5 (.value(bcd_1_bus_0_2));  // open: dp
  Register register_1 (.D(lbData), .Q(register_1_q), .clk(controlled_buffer_2_out), .clr(button_7_out));  // open: en
  bcd bcd_1 (.bus_0(register_1_q), .bus_0_2(bcd_1_bus_0_2), .bus_0_3(bcd_1_bus_0_3), .bus_0_4(bcd_1_bus_0_4));
  Hex_Digit_Display hex_digit_display_6 (.value(bcd_2_bus_0_2));  // open: dp
  Register register_2 (.D(lbData), .Q(register_2_q), .clk(controlled_buffer_3_out), .clr(button_7_out));  // open: en
  bcd bcd_2 (.bus_0(register_2_q), .bus_0_2(bcd_2_bus_0_2), .bus_0_3(bcd_2_bus_0_3), .bus_0_4(bcd_2_bus_0_4));
  Hex_Digit_Display hex_digit_display_7 (.value(bcd_3_bus_0_2));  // open: dp
  Register register_3 (.D(lbData), .Q(register_3_q), .clk(controlled_buffer_4_out), .clr(button_7_out));  // open: en
  bcd bcd_3 (.bus_0(register_3_q), .bus_0_2(bcd_3_bus_0_2), .bus_0_3(bcd_3_bus_0_3), .bus_0_4(bcd_3_bus_0_4));
  Hex_Digit_Display hex_digit_display_8 (.value(bcd_4_bus_0_2));  // open: dp
  Register register_4 (.D(lbData), .Q(register_4_q), .clk(controlled_buffer_5_out), .clr(button_7_out));  // open: en
  bcd bcd_4 (.bus_0(register_4_q), .bus_0_2(bcd_4_bus_0_2), .bus_0_3(bcd_4_bus_0_3), .bus_0_4(bcd_4_bus_0_4));
  Hex_Digit_Display hex_digit_display_9 (.value(bcd_5_bus_0_2));  // open: dp
  Register register_5 (.D(lbData), .Q(register_5_q), .clk(controlled_buffer_6_out), .clr(button_7_out));  // open: en
  bcd bcd_5 (.bus_0(register_5_q), .bus_0_2(bcd_5_bus_0_2), .bus_0_3(bcd_5_bus_0_3), .bus_0_4(bcd_5_bus_0_4));
  Hex_Digit_Display hex_digit_display_10 (.value(bcd_6_bus_0_2));  // open: dp
  Register register_6 (.D(lbData), .Q(register_6_q), .clk(controlled_buffer_7_out), .clr(button_7_out));  // open: en
  bcd bcd_6 (.bus_0(register_6_q), .bus_0_2(bcd_6_bus_0_2), .bus_0_3(bcd_6_bus_0_3), .bus_0_4(bcd_6_bus_0_4));
  Hex_Digit_Display hex_digit_display_11 (.value(bcd_7_bus_0_2));  // open: dp
  Register register_7 (.D(lbData), .Q(register_7_q), .clk(controlled_buffer_8_out), .clr(button_7_out));  // open: en
  bcd bcd_7 (.bus_0(register_7_q), .bus_0_2(bcd_7_bus_0_2), .bus_0_3(bcd_7_bus_0_3), .bus_0_4(bcd_7_bus_0_4));
  Hex_Digit_Display hex_digit_display_12 (.value(bcd_8_bus_0_2));  // open: dp
  Register register_8 (.D(lbData), .Q(register_8_q), .clk(controlled_buffer_9_out), .clr(button_7_out));  // open: en
  bcd bcd_8 (.bus_0(register_8_q), .bus_0_2(bcd_8_bus_0_2), .bus_0_3(bcd_8_bus_0_3), .bus_0_4(bcd_8_bus_0_4));
  Hex_Digit_Display hex_digit_display_13 (.value(bcd_1_bus_0_3));  // open: dp
  Hex_Digit_Display hex_digit_display_14 (.value(bcd_1_bus_0_4));  // open: dp
  Hex_Digit_Display hex_digit_display_15 (.value(bcd_2_bus_0_4));  // open: dp
  Hex_Digit_Display hex_digit_display_16 (.value(bcd_2_bus_0_3));  // open: dp
  Hex_Digit_Display hex_digit_display_17 (.value(bcd_3_bus_0_4));  // open: dp
  Hex_Digit_Display hex_digit_display_18 (.value(bcd_3_bus_0_3));  // open: dp
  Hex_Digit_Display hex_digit_display_19 (.value(bcd_4_bus_0_3));  // open: dp
  Hex_Digit_Display hex_digit_display_20 (.value(bcd_4_bus_0_4));  // open: dp
  Hex_Digit_Display hex_digit_display_21 (.value(bcd_5_bus_0_3));  // open: dp
  Hex_Digit_Display hex_digit_display_22 (.value(bcd_5_bus_0_4));  // open: dp
  Hex_Digit_Display hex_digit_display_23 (.value(bcd_6_bus_0_4));  // open: dp
  Hex_Digit_Display hex_digit_display_24 (.value(bcd_6_bus_0_3));  // open: dp
  Hex_Digit_Display hex_digit_display_25 (.value(bcd_7_bus_0_3));  // open: dp
  Hex_Digit_Display hex_digit_display_26 (.value(bcd_7_bus_0_4));  // open: dp
  Hex_Digit_Display hex_digit_display_27 (.value(bcd_8_bus_0_3));  // open: dp
  Hex_Digit_Display hex_digit_display_28 (.value(bcd_8_bus_0_4));  // open: dp
  DotMatrix #(.matrixcols(32)) dotmatrix_5 (
    .col0(lettersdrawer_1_out_4), .col1(lettersdrawer_1_out_5), .col2(lettersdrawer_1_out_6),
    .col3(lettersdrawer_1_out_7), .col4(lettersdrawer_1_out_8), .col5(lettersdrawer_1_out_9),
    .col6(lettersdrawer_1_out_10), .col7(lettersdrawer_1_out_11), .col8(lettersdrawer_1_out_12),
    .col9(lettersdrawer_1_out_13), .col10(lettersdrawer_1_out_14), .col11(lettersdrawer_1_out_15),
    .col12(lettersdrawer_1_out_16), .col13(lettersdrawer_1_out_17), .col14(lettersdrawer_1_out_18),
    .col15(lettersdrawer_1_out_19), .col16(lettersdrawer_1_out_20), .col17(lettersdrawer_1_out_21),
    .col18(lettersdrawer_1_out_22), .col19(lettersdrawer_1_out_23), .col20(lettersdrawer_1_out_24),
    .col21(lettersdrawer_1_out_25), .col22(lettersdrawer_1_out_26), .col23(lettersdrawer_1_out_27),
    .col24(lettersdrawer_1_out_28), .col25(lettersdrawer_1_out_29), .col26(lettersdrawer_1_out_30),
    .col27(lettersdrawer_1_out_31), .col28(lettersdrawer_1_out_32), .col29(lettersdrawer_1_out_33),
    .col30(lettersdrawer_1_out_34), .col31(lettersdrawer_1_out_35));
  DotMatrix #(.matrixcols(32)) dotmatrix_6 (
    .col0(lettersdrawer_2_out_4), .col1(lettersdrawer_2_out_5), .col2(lettersdrawer_2_out_6),
    .col3(lettersdrawer_2_out_7), .col4(lettersdrawer_2_out_8), .col5(lettersdrawer_2_out_9),
    .col6(lettersdrawer_2_out_10), .col7(lettersdrawer_2_out_11), .col8(lettersdrawer_2_out_12),
    .col9(lettersdrawer_2_out_13), .col10(lettersdrawer_2_out_14), .col11(lettersdrawer_2_out_15),
    .col12(lettersdrawer_2_out_16), .col13(lettersdrawer_2_out_17), .col14(lettersdrawer_2_out_18),
    .col15(lettersdrawer_2_out_19), .col16(lettersdrawer_2_out_20), .col17(lettersdrawer_2_out_21),
    .col18(lettersdrawer_2_out_22), .col19(lettersdrawer_2_out_23), .col20(lettersdrawer_2_out_24),
    .col21(lettersdrawer_2_out_25), .col22(lettersdrawer_2_out_26), .col23(lettersdrawer_2_out_27),
    .col24(lettersdrawer_2_out_28), .col25(lettersdrawer_2_out_29), .col26(lettersdrawer_2_out_30),
    .col27(lettersdrawer_2_out_31), .col28(lettersdrawer_2_out_32), .col29(lettersdrawer_2_out_33),
    .col30(lettersdrawer_2_out_34), .col31(lettersdrawer_2_out_35));
  DotMatrix #(.matrixcols(32)) dotmatrix_7 (
    .col0(lettersdrawer_3_out_4), .col1(lettersdrawer_3_out_5), .col2(lettersdrawer_3_out_6),
    .col3(lettersdrawer_3_out_7), .col4(lettersdrawer_3_out_8), .col5(lettersdrawer_3_out_9),
    .col6(lettersdrawer_3_out_10), .col7(lettersdrawer_3_out_11), .col8(lettersdrawer_3_out_12),
    .col9(lettersdrawer_3_out_13), .col10(lettersdrawer_3_out_14), .col11(lettersdrawer_3_out_15),
    .col12(lettersdrawer_3_out_16), .col13(lettersdrawer_3_out_17), .col14(lettersdrawer_3_out_18),
    .col15(lettersdrawer_3_out_19), .col16(lettersdrawer_3_out_20), .col17(lettersdrawer_3_out_21),
    .col18(lettersdrawer_3_out_22), .col19(lettersdrawer_3_out_23), .col20(lettersdrawer_3_out_24),
    .col21(lettersdrawer_3_out_25), .col22(lettersdrawer_3_out_26), .col23(lettersdrawer_3_out_27),
    .col24(lettersdrawer_3_out_28), .col25(lettersdrawer_3_out_29), .col26(lettersdrawer_3_out_30),
    .col27(lettersdrawer_3_out_31), .col28(lettersdrawer_3_out_32), .col29(lettersdrawer_3_out_33),
    .col30(lettersdrawer_3_out_34), .col31(lettersdrawer_3_out_35));
  DotMatrix #(.matrixcols(32)) dotmatrix_8 (
    .col0(lettersdrawer_4_out_4), .col1(lettersdrawer_4_out_5), .col2(lettersdrawer_4_out_6),
    .col3(lettersdrawer_4_out_7), .col4(lettersdrawer_4_out_8), .col5(lettersdrawer_4_out_9),
    .col6(lettersdrawer_4_out_10), .col7(lettersdrawer_4_out_11), .col8(lettersdrawer_4_out_12),
    .col9(lettersdrawer_4_out_13), .col10(lettersdrawer_4_out_14), .col11(lettersdrawer_4_out_15),
    .col12(lettersdrawer_4_out_16), .col13(lettersdrawer_4_out_17), .col14(lettersdrawer_4_out_18),
    .col15(lettersdrawer_4_out_19), .col16(lettersdrawer_4_out_20), .col17(lettersdrawer_4_out_21),
    .col18(lettersdrawer_4_out_22), .col19(lettersdrawer_4_out_23), .col20(lettersdrawer_4_out_24),
    .col21(lettersdrawer_4_out_25), .col22(lettersdrawer_4_out_26), .col23(lettersdrawer_4_out_27),
    .col24(lettersdrawer_4_out_28), .col25(lettersdrawer_4_out_29), .col26(lettersdrawer_4_out_30),
    .col27(lettersdrawer_4_out_31), .col28(lettersdrawer_4_out_32), .col29(lettersdrawer_4_out_33),
    .col30(lettersdrawer_4_out_34), .col31(lettersdrawer_4_out_35));
  DotMatrix #(.matrixcols(32)) dotmatrix_9 (
    .col0(lettersdrawer_5_out_4), .col1(lettersdrawer_5_out_5), .col2(lettersdrawer_5_out_6),
    .col3(lettersdrawer_5_out_7), .col4(lettersdrawer_5_out_8), .col5(lettersdrawer_5_out_9),
    .col6(lettersdrawer_5_out_10), .col7(lettersdrawer_5_out_11), .col8(lettersdrawer_5_out_12),
    .col9(lettersdrawer_5_out_13), .col10(lettersdrawer_5_out_14), .col11(lettersdrawer_5_out_15),
    .col12(lettersdrawer_5_out_16), .col13(lettersdrawer_5_out_17), .col14(lettersdrawer_5_out_18),
    .col15(lettersdrawer_5_out_19), .col16(lettersdrawer_5_out_20), .col17(lettersdrawer_5_out_21),
    .col18(lettersdrawer_5_out_22), .col19(lettersdrawer_5_out_23), .col20(lettersdrawer_5_out_24),
    .col21(lettersdrawer_5_out_25), .col22(lettersdrawer_5_out_26), .col23(lettersdrawer_5_out_27),
    .col24(lettersdrawer_5_out_28), .col25(lettersdrawer_5_out_29), .col26(lettersdrawer_5_out_30),
    .col27(lettersdrawer_5_out_31), .col28(lettersdrawer_5_out_32), .col29(lettersdrawer_5_out_33),
    .col30(lettersdrawer_5_out_34), .col31(lettersdrawer_5_out_35));
  DotMatrix #(.matrixcols(32)) dotmatrix_10 (
    .col0(lettersdrawer_6_out_4), .col1(lettersdrawer_6_out_5), .col2(lettersdrawer_6_out_6),
    .col3(lettersdrawer_6_out_7), .col4(lettersdrawer_6_out_8), .col5(lettersdrawer_6_out_9),
    .col6(lettersdrawer_6_out_10), .col7(lettersdrawer_6_out_11), .col8(lettersdrawer_6_out_12),
    .col9(lettersdrawer_6_out_13), .col10(lettersdrawer_6_out_14), .col11(lettersdrawer_6_out_15),
    .col12(lettersdrawer_6_out_16), .col13(lettersdrawer_6_out_17), .col14(lettersdrawer_6_out_18),
    .col15(lettersdrawer_6_out_19), .col16(lettersdrawer_6_out_20), .col17(lettersdrawer_6_out_21),
    .col18(lettersdrawer_6_out_22), .col19(lettersdrawer_6_out_23), .col20(lettersdrawer_6_out_24),
    .col21(lettersdrawer_6_out_25), .col22(lettersdrawer_6_out_26), .col23(lettersdrawer_6_out_27),
    .col24(lettersdrawer_6_out_28), .col25(lettersdrawer_6_out_29), .col26(lettersdrawer_6_out_30),
    .col27(lettersdrawer_6_out_31), .col28(lettersdrawer_6_out_32), .col29(lettersdrawer_6_out_33),
    .col30(lettersdrawer_6_out_34), .col31(lettersdrawer_6_out_35));
  DotMatrix #(.matrixcols(32)) dotmatrix_11 (
    .col0(lettersdrawer_7_out_4), .col1(lettersdrawer_7_out_5), .col2(lettersdrawer_7_out_6),
    .col3(lettersdrawer_7_out_7), .col4(lettersdrawer_7_out_8), .col5(lettersdrawer_7_out_9),
    .col6(lettersdrawer_7_out_10), .col7(lettersdrawer_7_out_11), .col8(lettersdrawer_7_out_12),
    .col9(lettersdrawer_7_out_13), .col10(lettersdrawer_7_out_14), .col11(lettersdrawer_7_out_15),
    .col12(lettersdrawer_7_out_16), .col13(lettersdrawer_7_out_17), .col14(lettersdrawer_7_out_18),
    .col15(lettersdrawer_7_out_19), .col16(lettersdrawer_7_out_20), .col17(lettersdrawer_7_out_21),
    .col18(lettersdrawer_7_out_22), .col19(lettersdrawer_7_out_23), .col20(lettersdrawer_7_out_24),
    .col21(lettersdrawer_7_out_25), .col22(lettersdrawer_7_out_26), .col23(lettersdrawer_7_out_27),
    .col24(lettersdrawer_7_out_28), .col25(lettersdrawer_7_out_29), .col26(lettersdrawer_7_out_30),
    .col27(lettersdrawer_7_out_31), .col28(lettersdrawer_7_out_32), .col29(lettersdrawer_7_out_33),
    .col30(lettersdrawer_7_out_34), .col31(lettersdrawer_7_out_35));
  DotMatrix #(.matrixcols(32)) dotmatrix_12 (
    .col0(lettersdrawer_8_out_4), .col1(lettersdrawer_8_out_5), .col2(lettersdrawer_8_out_6),
    .col3(lettersdrawer_8_out_7), .col4(lettersdrawer_8_out_8), .col5(lettersdrawer_8_out_9),
    .col6(lettersdrawer_8_out_10), .col7(lettersdrawer_8_out_11), .col8(lettersdrawer_8_out_12),
    .col9(lettersdrawer_8_out_13), .col10(lettersdrawer_8_out_14), .col11(lettersdrawer_8_out_15),
    .col12(lettersdrawer_8_out_16), .col13(lettersdrawer_8_out_17), .col14(lettersdrawer_8_out_18),
    .col15(lettersdrawer_8_out_19), .col16(lettersdrawer_8_out_20), .col17(lettersdrawer_8_out_21),
    .col18(lettersdrawer_8_out_22), .col19(lettersdrawer_8_out_23), .col20(lettersdrawer_8_out_24),
    .col21(lettersdrawer_8_out_25), .col22(lettersdrawer_8_out_26), .col23(lettersdrawer_8_out_27),
    .col24(lettersdrawer_8_out_28), .col25(lettersdrawer_8_out_29), .col26(lettersdrawer_8_out_30),
    .col27(lettersdrawer_8_out_31), .col28(lettersdrawer_8_out_32), .col29(lettersdrawer_8_out_33),
    .col30(lettersdrawer_8_out_34), .col31(lettersdrawer_8_out_35));
  Button button_7 (.out(button_7_out));
  lettersDrawer lettersdrawer_1 (
    .clk(button_7_out), .bus_0(bitselector_9_out), .bus_0_2(bitselector_1_out),
    .out_4(lettersdrawer_1_out_4), .out_5(lettersdrawer_1_out_5), .out_6(lettersdrawer_1_out_6),
    .out_7(lettersdrawer_1_out_7), .out_8(lettersdrawer_1_out_8), .out_9(lettersdrawer_1_out_9),
    .out_10(lettersdrawer_1_out_10), .out_11(lettersdrawer_1_out_11), .out_12(lettersdrawer_1_out_12),
    .out_13(lettersdrawer_1_out_13), .out_14(lettersdrawer_1_out_14), .out_15(lettersdrawer_1_out_15),
    .out_16(lettersdrawer_1_out_16), .out_17(lettersdrawer_1_out_17), .out_18(lettersdrawer_1_out_18),
    .out_19(lettersdrawer_1_out_19), .out_20(lettersdrawer_1_out_20), .out_21(lettersdrawer_1_out_21),
    .out_22(lettersdrawer_1_out_22), .out_23(lettersdrawer_1_out_23), .out_24(lettersdrawer_1_out_24),
    .out_25(lettersdrawer_1_out_25), .out_26(lettersdrawer_1_out_26), .out_27(lettersdrawer_1_out_27),
    .out_28(lettersdrawer_1_out_28), .out_29(lettersdrawer_1_out_29), .out_30(lettersdrawer_1_out_30),
    .out_31(lettersdrawer_1_out_31), .out_32(lettersdrawer_1_out_32), .out_33(lettersdrawer_1_out_33),
    .out_34(lettersdrawer_1_out_34), .out_35(lettersdrawer_1_out_35));
  BitSelector #(.group(7)) bitselector_1 (.in(controlled_buffer_10_out), .out(bitselector_1_out), .sel(1'b0));
  lettersDrawer lettersdrawer_2 (
    .clk(button_7_out), .bus_0(bitselector_9_out), .bus_0_2(bitselector_2_out),
    .out_4(lettersdrawer_2_out_4), .out_5(lettersdrawer_2_out_5), .out_6(lettersdrawer_2_out_6),
    .out_7(lettersdrawer_2_out_7), .out_8(lettersdrawer_2_out_8), .out_9(lettersdrawer_2_out_9),
    .out_10(lettersdrawer_2_out_10), .out_11(lettersdrawer_2_out_11), .out_12(lettersdrawer_2_out_12),
    .out_13(lettersdrawer_2_out_13), .out_14(lettersdrawer_2_out_14), .out_15(lettersdrawer_2_out_15),
    .out_16(lettersdrawer_2_out_16), .out_17(lettersdrawer_2_out_17), .out_18(lettersdrawer_2_out_18),
    .out_19(lettersdrawer_2_out_19), .out_20(lettersdrawer_2_out_20), .out_21(lettersdrawer_2_out_21),
    .out_22(lettersdrawer_2_out_22), .out_23(lettersdrawer_2_out_23), .out_24(lettersdrawer_2_out_24),
    .out_25(lettersdrawer_2_out_25), .out_26(lettersdrawer_2_out_26), .out_27(lettersdrawer_2_out_27),
    .out_28(lettersdrawer_2_out_28), .out_29(lettersdrawer_2_out_29), .out_30(lettersdrawer_2_out_30),
    .out_31(lettersdrawer_2_out_31), .out_32(lettersdrawer_2_out_32), .out_33(lettersdrawer_2_out_33),
    .out_34(lettersdrawer_2_out_34), .out_35(lettersdrawer_2_out_35));
  BitSelector #(.group(7)) bitselector_2 (.in(controlled_buffer_11_out), .out(bitselector_2_out), .sel(1'b0));
  lettersDrawer lettersdrawer_3 (
    .clk(button_7_out), .bus_0(bitselector_9_out), .bus_0_2(bitselector_3_out),
    .out_4(lettersdrawer_3_out_4), .out_5(lettersdrawer_3_out_5), .out_6(lettersdrawer_3_out_6),
    .out_7(lettersdrawer_3_out_7), .out_8(lettersdrawer_3_out_8), .out_9(lettersdrawer_3_out_9),
    .out_10(lettersdrawer_3_out_10), .out_11(lettersdrawer_3_out_11), .out_12(lettersdrawer_3_out_12),
    .out_13(lettersdrawer_3_out_13), .out_14(lettersdrawer_3_out_14), .out_15(lettersdrawer_3_out_15),
    .out_16(lettersdrawer_3_out_16), .out_17(lettersdrawer_3_out_17), .out_18(lettersdrawer_3_out_18),
    .out_19(lettersdrawer_3_out_19), .out_20(lettersdrawer_3_out_20), .out_21(lettersdrawer_3_out_21),
    .out_22(lettersdrawer_3_out_22), .out_23(lettersdrawer_3_out_23), .out_24(lettersdrawer_3_out_24),
    .out_25(lettersdrawer_3_out_25), .out_26(lettersdrawer_3_out_26), .out_27(lettersdrawer_3_out_27),
    .out_28(lettersdrawer_3_out_28), .out_29(lettersdrawer_3_out_29), .out_30(lettersdrawer_3_out_30),
    .out_31(lettersdrawer_3_out_31), .out_32(lettersdrawer_3_out_32), .out_33(lettersdrawer_3_out_33),
    .out_34(lettersdrawer_3_out_34), .out_35(lettersdrawer_3_out_35));
  BitSelector #(.group(7)) bitselector_3 (.in(controlled_buffer_12_out), .out(bitselector_3_out), .sel(1'b0));
  lettersDrawer lettersdrawer_4 (
    .clk(button_7_out), .bus_0(bitselector_9_out), .bus_0_2(bitselector_4_out),
    .out_4(lettersdrawer_4_out_4), .out_5(lettersdrawer_4_out_5), .out_6(lettersdrawer_4_out_6),
    .out_7(lettersdrawer_4_out_7), .out_8(lettersdrawer_4_out_8), .out_9(lettersdrawer_4_out_9),
    .out_10(lettersdrawer_4_out_10), .out_11(lettersdrawer_4_out_11), .out_12(lettersdrawer_4_out_12),
    .out_13(lettersdrawer_4_out_13), .out_14(lettersdrawer_4_out_14), .out_15(lettersdrawer_4_out_15),
    .out_16(lettersdrawer_4_out_16), .out_17(lettersdrawer_4_out_17), .out_18(lettersdrawer_4_out_18),
    .out_19(lettersdrawer_4_out_19), .out_20(lettersdrawer_4_out_20), .out_21(lettersdrawer_4_out_21),
    .out_22(lettersdrawer_4_out_22), .out_23(lettersdrawer_4_out_23), .out_24(lettersdrawer_4_out_24),
    .out_25(lettersdrawer_4_out_25), .out_26(lettersdrawer_4_out_26), .out_27(lettersdrawer_4_out_27),
    .out_28(lettersdrawer_4_out_28), .out_29(lettersdrawer_4_out_29), .out_30(lettersdrawer_4_out_30),
    .out_31(lettersdrawer_4_out_31), .out_32(lettersdrawer_4_out_32), .out_33(lettersdrawer_4_out_33),
    .out_34(lettersdrawer_4_out_34), .out_35(lettersdrawer_4_out_35));
  BitSelector #(.group(7)) bitselector_4 (.in(controlled_buffer_13_out), .out(bitselector_4_out), .sel(1'b0));
  lettersDrawer lettersdrawer_5 (
    .clk(button_7_out), .bus_0(bitselector_9_out), .bus_0_2(bitselector_5_out),
    .out_4(lettersdrawer_5_out_4), .out_5(lettersdrawer_5_out_5), .out_6(lettersdrawer_5_out_6),
    .out_7(lettersdrawer_5_out_7), .out_8(lettersdrawer_5_out_8), .out_9(lettersdrawer_5_out_9),
    .out_10(lettersdrawer_5_out_10), .out_11(lettersdrawer_5_out_11), .out_12(lettersdrawer_5_out_12),
    .out_13(lettersdrawer_5_out_13), .out_14(lettersdrawer_5_out_14), .out_15(lettersdrawer_5_out_15),
    .out_16(lettersdrawer_5_out_16), .out_17(lettersdrawer_5_out_17), .out_18(lettersdrawer_5_out_18),
    .out_19(lettersdrawer_5_out_19), .out_20(lettersdrawer_5_out_20), .out_21(lettersdrawer_5_out_21),
    .out_22(lettersdrawer_5_out_22), .out_23(lettersdrawer_5_out_23), .out_24(lettersdrawer_5_out_24),
    .out_25(lettersdrawer_5_out_25), .out_26(lettersdrawer_5_out_26), .out_27(lettersdrawer_5_out_27),
    .out_28(lettersdrawer_5_out_28), .out_29(lettersdrawer_5_out_29), .out_30(lettersdrawer_5_out_30),
    .out_31(lettersdrawer_5_out_31), .out_32(lettersdrawer_5_out_32), .out_33(lettersdrawer_5_out_33),
    .out_34(lettersdrawer_5_out_34), .out_35(lettersdrawer_5_out_35));
  BitSelector #(.group(7)) bitselector_5 (.in(controlled_buffer_14_out), .out(bitselector_5_out), .sel(1'b0));
  lettersDrawer lettersdrawer_6 (
    .clk(button_7_out), .bus_0(bitselector_9_out), .bus_0_2(bitselector_6_out),
    .out_4(lettersdrawer_6_out_4), .out_5(lettersdrawer_6_out_5), .out_6(lettersdrawer_6_out_6),
    .out_7(lettersdrawer_6_out_7), .out_8(lettersdrawer_6_out_8), .out_9(lettersdrawer_6_out_9),
    .out_10(lettersdrawer_6_out_10), .out_11(lettersdrawer_6_out_11), .out_12(lettersdrawer_6_out_12),
    .out_13(lettersdrawer_6_out_13), .out_14(lettersdrawer_6_out_14), .out_15(lettersdrawer_6_out_15),
    .out_16(lettersdrawer_6_out_16), .out_17(lettersdrawer_6_out_17), .out_18(lettersdrawer_6_out_18),
    .out_19(lettersdrawer_6_out_19), .out_20(lettersdrawer_6_out_20), .out_21(lettersdrawer_6_out_21),
    .out_22(lettersdrawer_6_out_22), .out_23(lettersdrawer_6_out_23), .out_24(lettersdrawer_6_out_24),
    .out_25(lettersdrawer_6_out_25), .out_26(lettersdrawer_6_out_26), .out_27(lettersdrawer_6_out_27),
    .out_28(lettersdrawer_6_out_28), .out_29(lettersdrawer_6_out_29), .out_30(lettersdrawer_6_out_30),
    .out_31(lettersdrawer_6_out_31), .out_32(lettersdrawer_6_out_32), .out_33(lettersdrawer_6_out_33),
    .out_34(lettersdrawer_6_out_34), .out_35(lettersdrawer_6_out_35));
  BitSelector #(.group(7)) bitselector_6 (.in(controlled_buffer_15_out), .out(bitselector_6_out), .sel(1'b0));
  lettersDrawer lettersdrawer_7 (
    .clk(button_7_out), .bus_0(bitselector_9_out), .bus_0_2(bitselector_7_out),
    .out_4(lettersdrawer_7_out_4), .out_5(lettersdrawer_7_out_5), .out_6(lettersdrawer_7_out_6),
    .out_7(lettersdrawer_7_out_7), .out_8(lettersdrawer_7_out_8), .out_9(lettersdrawer_7_out_9),
    .out_10(lettersdrawer_7_out_10), .out_11(lettersdrawer_7_out_11), .out_12(lettersdrawer_7_out_12),
    .out_13(lettersdrawer_7_out_13), .out_14(lettersdrawer_7_out_14), .out_15(lettersdrawer_7_out_15),
    .out_16(lettersdrawer_7_out_16), .out_17(lettersdrawer_7_out_17), .out_18(lettersdrawer_7_out_18),
    .out_19(lettersdrawer_7_out_19), .out_20(lettersdrawer_7_out_20), .out_21(lettersdrawer_7_out_21),
    .out_22(lettersdrawer_7_out_22), .out_23(lettersdrawer_7_out_23), .out_24(lettersdrawer_7_out_24),
    .out_25(lettersdrawer_7_out_25), .out_26(lettersdrawer_7_out_26), .out_27(lettersdrawer_7_out_27),
    .out_28(lettersdrawer_7_out_28), .out_29(lettersdrawer_7_out_29), .out_30(lettersdrawer_7_out_30),
    .out_31(lettersdrawer_7_out_31), .out_32(lettersdrawer_7_out_32), .out_33(lettersdrawer_7_out_33),
    .out_34(lettersdrawer_7_out_34), .out_35(lettersdrawer_7_out_35));
  BitSelector #(.group(7)) bitselector_7 (.in(controlled_buffer_16_out), .out(bitselector_7_out), .sel(1'b0));
  lettersDrawer lettersdrawer_8 (
    .clk(button_7_out), .bus_0(bitselector_9_out), .bus_0_2(bitselector_8_out),
    .out_4(lettersdrawer_8_out_4), .out_5(lettersdrawer_8_out_5), .out_6(lettersdrawer_8_out_6),
    .out_7(lettersdrawer_8_out_7), .out_8(lettersdrawer_8_out_8), .out_9(lettersdrawer_8_out_9),
    .out_10(lettersdrawer_8_out_10), .out_11(lettersdrawer_8_out_11), .out_12(lettersdrawer_8_out_12),
    .out_13(lettersdrawer_8_out_13), .out_14(lettersdrawer_8_out_14), .out_15(lettersdrawer_8_out_15),
    .out_16(lettersdrawer_8_out_16), .out_17(lettersdrawer_8_out_17), .out_18(lettersdrawer_8_out_18),
    .out_19(lettersdrawer_8_out_19), .out_20(lettersdrawer_8_out_20), .out_21(lettersdrawer_8_out_21),
    .out_22(lettersdrawer_8_out_22), .out_23(lettersdrawer_8_out_23), .out_24(lettersdrawer_8_out_24),
    .out_25(lettersdrawer_8_out_25), .out_26(lettersdrawer_8_out_26), .out_27(lettersdrawer_8_out_27),
    .out_28(lettersdrawer_8_out_28), .out_29(lettersdrawer_8_out_29), .out_30(lettersdrawer_8_out_30),
    .out_31(lettersdrawer_8_out_31), .out_32(lettersdrawer_8_out_32), .out_33(lettersdrawer_8_out_33),
    .out_34(lettersdrawer_8_out_34), .out_35(lettersdrawer_8_out_35));
  BitSelector #(.group(7)) bitselector_8 (.in(controlled_buffer_17_out), .out(bitselector_8_out), .sel(1'b0));
  assign controlled_buffer_10_out = _1 ? lbData : 8'bz;  // Controlled_Buffer controlled_buffer_10
  assign controlled_buffer_11_out = _2 ? lbData : 8'bz;  // Controlled_Buffer controlled_buffer_11
  assign controlled_buffer_12_out = _3 ? lbData : 8'bz;  // Controlled_Buffer controlled_buffer_12
  assign controlled_buffer_13_out = _4 ? lbData : 8'bz;  // Controlled_Buffer controlled_buffer_13
  assign controlled_buffer_14_out = _5 ? lbData : 8'bz;  // Controlled_Buffer controlled_buffer_14
  assign controlled_buffer_15_out = _6 ? lbData : 8'bz;  // Controlled_Buffer controlled_buffer_15
  assign controlled_buffer_16_out = _7 ? lbData : 8'bz;  // Controlled_Buffer controlled_buffer_16
  assign controlled_buffer_17_out = _8 ? lbData : 8'bz;  // Controlled_Buffer controlled_buffer_17
  and and_3 (and_3_out, cl, ldLeaderB, comparator_2_eq);
  Comparator #(.width(3)) comparator_2 (.a(bitselector_9_out), .b(3'b000), .eq(comparator_2_eq));  // open: gt, lt
  // Probe on bitselector_9_out
  BitSelector #(.group(3)) bitselector_9 (.in(subtractor_1_out), .out(bitselector_9_out), .sel(2'b00));
  BitSelector #(.group(3)) bitselector_10 (.in(divider_1_out), .out(bitselector_10_out), .sel(2'b00));
  Decoder #(.select(3), .enable("false")) decoder_1 (
    .out0(_1), .out1(_2), .out2(_3), .out3(_4), .out4(_5), .out5(_6), .out6(_7), .out7(_8),
    .sel(bitselector_10_out));
  Counter counter_2 (.Q(lbCounter), .clk(clockdelay_1_bus_0_3), .clr(d_ff_3_qn));  // open: load, D, count, carry
  clockDelay clockdelay_1 (.bus_0(d_ff_3_qn), .bus_0_2(controlled_buffer_18_out), .bus_0_3(clockdelay_1_bus_0_3));
  assign controlled_buffer_18_out = ldLeaderB ? cl : 1'bz;  // Controlled_Buffer controlled_buffer_18
  Clock clock_2 (.out(cl));
  // Probe on subtractor_1_out
  // Probe on divider_1_out
  Divider divider_1 (.a(lbCounter), .b(8'h6), .out(divider_1_out));  // open: upper, rem
  Register #(.trigger("falling")) register_9 (.D(divider_2_rem), .Q(register_9_q), .clk(d_ff_9_q));  // open: en, clr
  Subtractor subtractor_1 (.a(lbCounter), .b(multiplier_1_out), .out(subtractor_1_out));  // open: bin, bout
  Multiplier multiplier_1 (.a(8'h6), .b(divider_1_out), .out(multiplier_1_out));  // open: cin, cout
  Divider divider_2 (.a(adder_1_out), .b(8'h30), .rem(divider_2_rem));  // open: out, upper
  Adder adder_1 (.a(register_9_q), .b(8'h6), .out(adder_1_out));  // open: cin, cout
  Comparator comparator_3 (.a(lbCounter), .b(8'h2f), .eq(lbImp));  // open: gt, lt
  D_Flip_Flop d_ff_3 (.clk(LBFLAG), .D(LBFLAG), .Q(ldLeaderB), .Qn(d_ff_3_qn), .reset(lbImp));  // open: preset, en
  D_Flip_Flop d_ff_4 (
    .clk(d_ff_9_q), .D(d_ff_9_q), .Q(d_ff_4_q), .Qn(d_ff_4_qn), .reset(clockdelay2_1_bus_0_3));  // open: preset, en
  clockDelay2 clockdelay2_1 (.bus_0(d_ff_4_qn), .bus_0_2(cl), .bus_0_3(clockdelay2_1_bus_0_3));
  \or  or_1 (.bus_0_3(or_1_bus_0_3), .bus_0(d_ff_4_q), .bus_0_2(clockdelay_2_bus_0_3));
  clockDelay clockdelay_2 (.bus_0(nor_2_out), .bus_0_2(controlled_buffer_19_out), .bus_0_3(clockdelay_2_bus_0_3));
  assign controlled_buffer_19_out = or_2_out ? cl : 1'bz;  // Controlled_Buffer controlled_buffer_19
  Button button_8 ();  // open: out
  Decoder #(.enable("false")) decoder_2 (.out0(decoder_2_out0), .out1(decoder_2_out1), .sel(ldLeaderB));
  assign controlled_buffer_20_out = decoder_2_out1 ? lbCounter : 8'bz;  // Controlled_Buffer controlled_buffer_20
  assign controlled_buffer_20_out = decoder_2_out0 ? counter_3_q : 8'bz;  // Controlled_Buffer controlled_buffer_21
  Counter counter_3 (
    .load(d_ff_4_q), .D(register_9_q), .count(d_ff_4_qn), .Q(counter_3_q), .clk(or_1_bus_0_3), .clr(nor_1_out));  // open: carry
  nor nor_1 (nor_1_out, d_ff_6_q, d_ff_9_q, d_ff_5_q);
  nor nor_2 (nor_2_out, d_ff_6_q, d_ff_9_q, d_ff_5_q);
  or or_2 (or_2_out, d_ff_6_q, d_ff_9_q, d_ff_5_q);
  D_Flip_Flop d_ff_5 (
    .clk(decoder_3_out3), .D(decoder_3_out3), .Q(d_ff_5_q), .reset(comparator_4_eq));  // open: Qn, preset, en
  or or_3 (or_3_out, d_ff_5_q, d_ff_9_q);
  or or_4 (or_4_out, decoder_2_out1, d_ff_5_q, d_ff_9_q, d_ff_6_q);
  D_Flip_Flop d_ff_6 (
    .clk(sigdel_1_signal_2), .D(sigdel_1_signal_2), .Q(d_ff_6_q), .reset(comparator_5_eq));  // open: Qn, preset, en
  Button button_9 (.out(button_9_out));
  RAM #(.bus("separate")) ram_1 (
    .addr(controlled_buffer_20_out), .din(controlled_buffer_22_out), .data(lbData), .str(or_3_out),
    .sel(or_4_out), .clk(clockdelay_2_bus_0_3), .ld(or_5_out), .clr(button_10_out));
  or or_5 (or_5_out, d_ff_6_q, decoder_2_out1);
  or or_6 (or_6_out, impulse_1_bus_0_2, impulse_4_bus_0_2, impulse_2_bus_0_2, impulse_3_bus_0_2, impulse_5_bus_0_2);
  impulse impulse_1 (.bus_0_2(impulse_1_bus_0_2), .bus_0(comparator_4_eq));
  impulse impulse_2 (.bus_0_2(impulse_2_bus_0_2), .bus_0(d_ff_9_qn));
  impulse impulse_3 (.bus_0_2(impulse_3_bus_0_2), .bus_0(sigdel_2_signal_2));
  impulse impulse_4 (.bus_0_2(impulse_4_bus_0_2), .bus_0(comparator_5_eq));
  Button button_10 (.out(button_10_out));
  Decoder #(.select(3), .enable("false")) decoder_3 (
    .out1(decoder_3_out1), .out2(proccesorFlag), .out3(decoder_3_out3), .out4(LBFLAG), .sel(counter_4_q));  // open: out0, out5, out6, out7
  Counter #(.width(3), .max('h5)) counter_4 (
    .Q(counter_4_q), .clk(or_6_out), .clr(lbImp));  // open: load, D, count, carry
  impulse impulse_5 (.bus_0_2(impulse_5_bus_0_2), .bus_0(lbImp));
  D_Flip_Flop d_ff_7 (.clk(proccesorFlag), .D(proccesorFlag), .Q(d_ff_7_q), .reset(lbImp));  // open: Qn, preset, en
  Comparator comparator_4 (.a(counter_3_q), .b({8{1'b1}}), .eq(comparator_4_eq));  // open: gt, lt
  Pull_Resistor pull_resistor_2 (.node(comparator_4_eq));
  sigDel sigdel_1 (.cl(cl), .signal(decoder_3_out1), .signal_2(sigdel_1_signal_2));
  sigDel sigdel_2 (.cl(cl), .signal(d_ff_7_q), .signal_2(sigdel_2_signal_2));
  Comparator comparator_5 (.a(counter_3_q), .b({8{1'b1}}), .eq(comparator_5_eq));  // open: gt, lt
  Pull_Resistor pull_resistor_3 (.node(comparator_5_eq));
  assign controlled_buffer_22_out = d_ff_5_q ? proc_1_p4 : 8'bz;  // Controlled_Buffer controlled_buffer_22
  assign controlled_buffer_22_out = comparator_7_gt ? bit_extender_1_out : 8'bz;  // Controlled_Buffer controlled_buffer_23
  // proc proc_1: pin names not known; wires that end beside it: lbData, d_ff_6_q, d_ff_5_q, proc_1_p4, proc_1_p5, proc_1_p5
  assign bit_extender_1_out = {{1{1'b0}}, ram_2_data};  // Bit_Extender bit_extender_1
  D_Flip_Flop d_ff_8 (.clk(ENTER), .D(ENTER), .Q(d_ff_8_q), .reset(comparator_6_eq));  // open: Qn, preset, en
  clockDelay clockdelay_3 (.bus_0(comparator_6_eq), .bus_0_2(controlled_buffer_24_out), .bus_0_3(keyboardCL));
  assign controlled_buffer_24_out = d_ff_8_q ? cl : 1'bz;  // Controlled_Buffer controlled_buffer_24
  or or_7 (or_7_out, and_6_out, and_4_out);
  // Probe on ascii
  Comparator #(.width(3)) comparator_6 (.a(3'b110), .b(counter_5_q), .eq(comparator_6_eq));  // open: gt, lt
  Counter #(.width(3), .max('h7)) counter_5 (
    .Q(counter_5_q), .clk(or_7_out), .clr(nor_3_out));  // open: load, D, count, carry
  nor nor_3 (nor_3_out, ~comparator_6_eq, d_ff_9_q);  // NOR_Gate
  and and_4 (and_4_out, keyboardCL, ~comparator_6_eq);  // AND_Gate
  assign controlled_buffer_22_out = and_5_out ? register_10_q : 8'bz;  // Controlled_Buffer controlled_buffer_25
  and and_5 (and_5_out, comparator_7_eq, d_ff_9_q);
  Comparator #(.width(3), .mode("unsigned")) comparator_7 (
    .a(counter_5_q), .b(3'b000), .gt(comparator_7_gt), .eq(comparator_7_eq));  // open: lt
  Subtractor #(.width(3)) subtractor_2 (.a(counter_5_q), .b(3'b001), .out(subtractor_2_out));  // open: bin, bout
  assign controlled_buffer_26_out = d_ff_8_q ? counter_5_q : 3'bz;  // Controlled_Buffer controlled_buffer_26
  assign controlled_buffer_26_out = comparator_7_gt ? controlled_buffer_28_out : 3'bz;  // Controlled_Buffer controlled_buffer_27
  or or_8 (or_8_out, d_ff_8_q, d_ff_9_q);
  Pull_Resistor pull_resistor_4 (.node(keyboardCL));
  assign controlled_buffer_28_out = d_ff_9_q ? subtractor_2_out : 3'bz;  // Controlled_Buffer controlled_buffer_28
  RAM #(.addrWidth(3), .dataWidth(7), .bus("separate")) ram_2 (
    .addr(controlled_buffer_26_out), .din(ascii), .data(ram_2_data), .str(d_ff_8_q), .sel(or_8_out),
    .clk(keyboardCL), .ld(d_ff_9_q));  // open: clr
  clockDelay clockdelay_4 (.bus_0(d_ff_9_qn), .bus_0_2(cl), .bus_0_3(clockdelay_4_bus_0_3));
  D_Flip_Flop d_ff_9 (
    .clk(STARTPROCESS), .D(STARTPROCESS), .Q(d_ff_9_q), .Qn(d_ff_9_qn), .reset(comparator_6_eq));  // open: preset, en
  and and_6 (and_6_out, clockdelay_4_bus_0_3, d_ff_9_q);
  Register register_10 (.D(scoreVal), .Q(register_10_q), .clk(d_ff_9_q));  // open: en, clr

  // Notes on the sheet:
  //   enter
  //   clear name field
  //   for tests
  //   выгрузить
  //   загрузить
  //   enter
  //   load in lb
endmodule

module borders (
  input  [4:0] in_1,
  output [31:0] out_2,
  output [31:0] out_3,
  output [31:0] out_4,
  output [31:0] out_5
);

  wire [4:0] buffer_1_out, buffer_2_out;

  assign buffer_1_out = in_1;  // Buffer buffer_1, 5 bits wide
  assign buffer_2_out = buffer_1_out;  // Buffer buffer_2, 5 bits wide
  ROM #(.addrWidth(5), .dataWidth(32)) rom_1 (.addr(buffer_2_out), .data(out_2));  // open: sel
  ROM #(.addrWidth(5), .dataWidth(32)) rom_2 (.addr(buffer_2_out), .data(out_3));  // open: sel
  ROM #(.addrWidth(5), .dataWidth(32)) rom_3 (.addr(buffer_2_out), .data(out_4));  // open: sel
  ROM #(.addrWidth(5), .dataWidth(32)) rom_4 (.addr(buffer_2_out), .data(out_5));  // open: sel

  // Notes on the sheet:
  //   contents of rom_1 (hex, n*v repeats v):
  //   8*0 ffffff00 23*100
  //   contents of rom_2 (hex, n*v repeats v):
  //   8*0 ffffff 23*800000
  //   contents of rom_3 (hex, n*v repeats v):
  //   23*800000 ffffff
  //   contents of rom_4 (hex, n*v repeats v):
  //   23*100 ffffff00
endmodule

module input_handeler (
  input  [4:0] clock32,
  input  [6:0] in_2,
  input  d,
  input  s,
  input  a,
  input  w,
  input  [1:0] vert,
  input  [1:0] hoz,
  output out_9,
  output out_10,
  output out_11,
  output out_12
);

  wire and_1_out, and_2_out, and_3_out, and_4_out, and_5_out, buffer_1_out, comparator_1_gt, comparator_1_lt,
       comparator_2_gt, comparator_2_lt, d_ff_1_q, d_ff_2_q, d_ff_3_q, d_ff_4_q, or_1_out, or_2_out,
       or_3_out, or_4_out, or_5_out, or_6_out, or_7_out, or_8_out;

  and and_1 (and_1_out, in_2[0], ~in_2[1], ~in_2[2]);  // AND_Gate
  or or_1 (or_1_out, and_1_out, comparator_2_lt, a);
  Comparator #(.width(2), .mode("unsigned")) comparator_1 (
    .a(vert), .b(2'b10), .gt(comparator_1_gt), .lt(comparator_1_lt));  // open: eq
  Comparator #(.width(2), .mode("unsigned")) comparator_2 (
    .a(hoz), .b(2'b10), .gt(comparator_2_gt), .lt(comparator_2_lt));  // open: eq
  and and_2 (and_2_out, in_2[0], in_2[1], ~in_2[2]);  // AND_Gate
  and and_3 (and_3_out, ~in_2[0], ~in_2[1], in_2[2]);  // AND_Gate
  or or_2 (or_2_out, and_2_out, comparator_1_gt, s);
  and and_4 (and_4_out, ~clock32[0], ~clock32[1], ~clock32[2], ~clock32[3], ~clock32[4]);  // AND_Gate
  and and_5 (and_5_out, in_2[0], in_2[1], in_2[2]);
  or or_3 (or_3_out, and_3_out, comparator_2_gt, d);
  buf buffer_1 (buffer_1_out, and_4_out);
  or or_4 (or_4_out, and_5_out, comparator_1_lt, w);
  D_Flip_Flop d_ff_1 (.clk(or_5_out), .D(or_3_out), .Q(d_ff_1_q));  // open: Qn, preset, en, reset
  or or_5 (or_5_out, buffer_1_out, or_3_out);
  or or_6 (or_6_out, buffer_1_out, or_2_out);
  D_Flip_Flop d_ff_2 (.clk(or_6_out), .D(or_2_out), .Q(d_ff_2_q));  // open: Qn, preset, en, reset
  or or_7 (or_7_out, buffer_1_out, or_1_out);
  D_Flip_Flop d_ff_3 (.clk(or_7_out), .D(or_1_out), .Q(d_ff_3_q));  // open: Qn, preset, en, reset
  D_Flip_Flop d_ff_4 (.clk(or_8_out), .D(or_4_out), .Q(d_ff_4_q));  // open: Qn, preset, en, reset
  or or_8 (or_8_out, buffer_1_out, or_4_out);
  D_Flip_Flop d_ff_5 (.clk(and_4_out), .D(d_ff_1_q), .Q(out_9));  // open: Qn, preset, en, reset
  D_Flip_Flop d_ff_6 (.clk(and_4_out), .D(d_ff_2_q), .Q(out_10));  // open: Qn, preset, en, reset
  D_Flip_Flop d_ff_7 (.clk(and_4_out), .D(d_ff_3_q), .Q(out_11));  // open: Qn, preset, en, reset
  D_Flip_Flop d_ff_8 (.clk(and_4_out), .D(d_ff_4_q), .Q(out_12));  // open: Qn, preset, en, reset
endmodule

module colision_drawer (
  input  [31:0] in_1,
  input  [4:0] clock32,
  input  [31:0] in_3,
  input  [5:0] y,
  input  [31:0] in_5,
  input  [31:0] in_6,
  input  [5:0] x,
  input  [3:0] in_8,
  input  [3:0] in_9,
  input  [3:0] in_10,
  input  [3:0] in_11,
  input  clock,
  output [31:0] out_13,
  output [31:0] out_14,
  output [31:0] out_15,
  output [31:0] out_16,
  output out_17
);

  wire and_1_out, and_2_out, buffer_1_out, buffer_2_out, comparator_1_eq, comparator_2_eq, comparator_3_eq,
       comparator_4_eq, comparator_5_eq, comparator_6_eq, comparator_7_eq, comparator_8_eq,
       controlled_inverter_1_out, controlled_inverter_2_out, controlled_inverter_3_out,
       controlled_inverter_4_out, d_ff_1_q, d_ff_2_q, d_ff_4_q, demultiplexer_1_out0, demultiplexer_1_out1,
       demultiplexer_2_out0, demultiplexer_2_out1, demultiplexer_3_out0, demultiplexer_3_out1, or_1_out,
       or_2_out, or_9_out, or_10_out, priority_encoder_1_p1, priority_encoder_1_p6, priority_encoder_1_p7,
       subtractor_1_bout, subtractor_2_bout, subtractor_3_bout, subtractor_4_bout, subtractor_5_bout,
       subtractor_6_bout, subtractor_8_bout, subtractor_9_bout;
  wire [1:0] multiplexer_6_out, priority_encoder_1_p4;
  wire [3:0] multiplexer_1_out;
  wire [4:0] bit_extender_1_out, bit_extender_3_out, bit_extender_5_out, multiplexer_7_out,
       multiplexer_8_out, multiplexer_9_out, subtractor_6_out, subtractor_7_out, subtractor_8_out,
       subtractor_9_out;
  wire [5:0] adder_1_out, adder_2_out, adder_3_out, multiplexer_2_out, multiplexer_3_out, multiplexer_4_out,
       multiplexer_5_out, subtractor_1_out, subtractor_2_out, subtractor_3_out, subtractor_4_out,
       subtractor_5_out;
  wire [31:0] bit_extender_2_out, bit_extender_4_out, multiplexer_10_out, multiplexer_11_out,
       multiplexer_12_out, or_3_out, or_4_out, or_5_out, or_6_out, or_7_out, or_8_out, register_1_q,
       register_2_q, register_3_q, register_4_q, register_5_q, register_6_q, register_7_q, register_8_q,
       shifter_1_out, shifter_2_out, shifter_3_out, shifter_4_out, shifter_5_out, shifter_6_out,
       shifter_7_out, xor_1_out, xor_2_out, xor_3_out, xor_4_out;

  Adder #(.width(6)) adder_1 (.a(y), .b(6'b000001), .out(adder_1_out));  // open: cin, cout
  Adder #(.width(6)) adder_2 (.a(y), .b(6'b000010), .out(adder_2_out));  // open: cin, cout
  Adder #(.width(6)) adder_3 (.a(y), .b(6'b000011), .out(adder_3_out));  // open: cin, cout
  Multiplexer #(.select(2), .width(4), .enable("false")) multiplexer_1 (
    .in0(in_8), .in1(in_9), .in2(in_10), .in3(in_11), .out(multiplexer_1_out), .sel(multiplexer_6_out));
  and and_1 (and_1_out, x[5], x[4], x[3], x[2]);
  Multiplexer #(.width(6), .enable("false")) multiplexer_2 (
    .in0(subtractor_1_out), .in1(y), .out(multiplexer_2_out), .sel(subtractor_1_bout));
  Subtractor #(.width(6)) subtractor_1 (
    .a(y), .b(6'b100000), .out(subtractor_1_out), .bout(subtractor_1_bout));  // open: bin
  Multiplexer #(.width(6), .enable("false")) multiplexer_3 (
    .in0(subtractor_2_out), .in1(adder_1_out), .out(multiplexer_3_out), .sel(subtractor_2_bout));
  Subtractor #(.width(6)) subtractor_2 (
    .a(adder_1_out), .b(6'b100000), .out(subtractor_2_out), .bout(subtractor_2_bout));  // open: bin
  Subtractor #(.width(6)) subtractor_3 (
    .a(adder_2_out), .b(6'b100000), .out(subtractor_3_out), .bout(subtractor_3_bout));  // open: bin
  Multiplexer #(.width(6), .enable("false")) multiplexer_4 (
    .in0(subtractor_3_out), .in1(adder_2_out), .out(multiplexer_4_out), .sel(subtractor_3_bout));
  Multiplexer #(.width(6), .enable("false")) multiplexer_5 (
    .in0(subtractor_4_out), .in1(adder_3_out), .out(multiplexer_5_out), .sel(subtractor_4_bout));
  Subtractor #(.width(6)) subtractor_4 (
    .a(adder_3_out), .b(6'b100000), .out(subtractor_4_out), .bout(subtractor_4_bout));  // open: bin
  // Probe on multiplexer_6_out
  Multiplexer #(.width(2), .enable("false")) multiplexer_6 (
    .in0(priority_encoder_1_p4), .in1(2'b00), .out(multiplexer_6_out), .sel(priority_encoder_1_p1));
  // Probe on multiplexer_1_out
  Subtractor #(.width(6)) subtractor_5 (
    .a(x), .b(6'b011101), .out(subtractor_5_out), .bout(subtractor_5_bout));  // open: bin
  Comparator #(.width(6), .mode("unsigned")) comparator_1 (
    .a(multiplexer_2_out), .b({1'b0, clock32}), .eq(comparator_1_eq));  // open: gt, lt
  Comparator #(.width(6), .mode("unsigned")) comparator_2 (
    .a(multiplexer_3_out), .b({1'b0, clock32}), .eq(comparator_2_eq));  // open: gt, lt
  Comparator #(.width(6), .mode("unsigned")) comparator_3 (
    .a(multiplexer_4_out), .b({1'b0, clock32}), .eq(comparator_3_eq));  // open: gt, lt
  Comparator #(.width(6), .mode("unsigned")) comparator_4 (
    .a(multiplexer_5_out), .b({1'b0, clock32}), .eq(comparator_4_eq));  // open: gt, lt
  // Priority_Encoder #(.select(2)) priority_encoder_1: pin names not known; wires that end beside it: priority_encoder_1_p1, comparator_1_eq, comparator_2_eq, priority_encoder_1_p4, comparator_3_eq, priority_encoder_1_p6, priority_encoder_1_p7
  Bit_Extender #(.in_width(6), .out_width(5)) bit_extender_1 (.in(x), .out(bit_extender_1_out));
  assign bit_extender_2_out = {{28{1'b0}}, multiplexer_1_out};  // Bit_Extender bit_extender_2
  Shifter #(.width(32)) shifter_1 (.in(bit_extender_2_out), .\dist (5'b01110), .out(shifter_1_out));
  Bit_Extender #(.in_width(6), .out_width(5)) bit_extender_3 (.in(subtractor_5_out), .out(bit_extender_3_out));
  assign bit_extender_4_out = {{28{1'b0}}, multiplexer_1_out};  // Bit_Extender bit_extender_4
  Shifter #(.width(32)) shifter_2 (.in(bit_extender_4_out), .\dist (5'b01110), .out(shifter_2_out));
  Shifter #(.width(32), .shift("lr")) shifter_3 (
    .in(bit_extender_4_out), .\dist (bit_extender_5_out), .out(shifter_3_out));
  assign bit_extender_5_out = {{3{1'b0}}, x[1:0]};  // Bit_Extender bit_extender_5
  Demultiplexer #(.enable("false")) demultiplexer_1 (
    .out0(demultiplexer_1_out0), .out1(demultiplexer_1_out1), .in(comparator_1_eq), .sel(subtractor_1_bout));
  Demultiplexer #(.enable("false")) demultiplexer_2 (
    .out0(demultiplexer_2_out0), .out1(demultiplexer_2_out1), .in(comparator_2_eq), .sel(subtractor_2_bout));
  Demultiplexer #(.enable("false")) demultiplexer_3 (
    .out0(demultiplexer_3_out0), .out1(demultiplexer_3_out1), .in(comparator_3_eq), .sel(subtractor_3_bout));
  Demultiplexer #(.enable("false")) demultiplexer_4 (
    .out0(priority_encoder_1_p7), .out1(priority_encoder_1_p6), .in(comparator_4_eq), .sel(subtractor_4_bout));
  Subtractor #(.width(5)) subtractor_6 (
    .a(5'b01110), .b(bit_extender_1_out), .out(subtractor_6_out), .bout(subtractor_6_bout));  // open: bin
  Subtractor #(.width(5)) subtractor_7 (
    .a(bit_extender_1_out), .b(5'b01110), .out(subtractor_7_out));  // open: bin, bout
  Subtractor #(.width(5)) subtractor_8 (
    .a(5'b10001), .b(bit_extender_3_out), .out(subtractor_8_out), .bout(subtractor_8_bout));  // open: bin
  Subtractor #(.width(5)) subtractor_9 (
    .a(bit_extender_3_out), .b(5'b10001), .out(subtractor_9_out), .bout(subtractor_9_bout));  // open: bin
  or or_1 (or_1_out, demultiplexer_1_out0, demultiplexer_2_out0, demultiplexer_3_out0);
  or or_2 (or_2_out, demultiplexer_1_out1, demultiplexer_2_out1, demultiplexer_3_out1);
  Multiplexer #(.width(5), .enable("false")) multiplexer_7 (
    .in0(subtractor_6_out), .in1(5'b11110), .out(multiplexer_7_out), .sel(subtractor_6_bout));
  Multiplexer #(.width(5), .enable("false")) multiplexer_8 (
    .in0(subtractor_8_out), .in1(5'b11110), .out(multiplexer_8_out), .sel(subtractor_8_bout));
  Multiplexer #(.width(5), .enable("false")) multiplexer_9 (
    .in0(subtractor_9_out), .in1(5'b11110), .out(multiplexer_9_out), .sel(subtractor_9_bout));
  Shifter #(.width(32)) shifter_4 (.in(shifter_1_out), .\dist (multiplexer_7_out), .out(shifter_4_out));
  assign or_3_out = shifter_4_out | shifter_5_out;  // OR_Gate or_3, 32 bits wide
  Shifter #(.width(32), .shift("lr")) shifter_5 (.in(shifter_1_out), .\dist (subtractor_7_out), .out(shifter_5_out));
  Shifter #(.width(32)) shifter_6 (.in(shifter_2_out), .\dist (multiplexer_8_out), .out(shifter_6_out));
  assign or_4_out = shifter_6_out | shifter_7_out;  // OR_Gate or_4, 32 bits wide
  Shifter #(.width(32), .shift("lr")) shifter_7 (.in(shifter_2_out), .\dist (multiplexer_9_out), .out(shifter_7_out));
  Multiplexer #(.width(32), .enable("false")) multiplexer_10 (
    .in0(or_3_out), .in1({32{1'b0}}), .out(multiplexer_10_out), .sel(x[5]));
  Multiplexer #(.width(32), .enable("false")) multiplexer_11 (
    .in0(or_4_out), .in1({32{1'b0}}), .out(multiplexer_11_out), .sel(subtractor_5_bout));
  Multiplexer #(.width(32), .enable("false")) multiplexer_12 (
    .in0(multiplexer_11_out), .in1(shifter_3_out), .out(multiplexer_12_out), .sel(and_1_out));
  assign xor_1_out = in_1 ^ multiplexer_12_out;  // XOR_Gate xor_1, 32 bits wide
  assign xor_2_out = in_3 ^ multiplexer_10_out;  // XOR_Gate xor_2, 32 bits wide
  assign xor_3_out = in_5 ^ multiplexer_10_out;  // XOR_Gate xor_3, 32 bits wide
  assign xor_4_out = in_6 ^ multiplexer_12_out;  // XOR_Gate xor_4, 32 bits wide
  assign or_5_out = in_1 | multiplexer_12_out;  // OR_Gate or_5, 32 bits wide
  assign or_6_out = in_3 | multiplexer_10_out;  // OR_Gate or_6, 32 bits wide
  assign or_7_out = in_5 | multiplexer_10_out;  // OR_Gate or_7, 32 bits wide
  assign or_8_out = in_6 | multiplexer_12_out;  // OR_Gate or_8, 32 bits wide
  Multiplexer #(.width(32), .enable("false")) multiplexer_13 (.in0(in_1), .in1(or_5_out), .out(out_13), .sel(or_2_out));
  Multiplexer #(.width(32), .enable("false")) multiplexer_14 (.in0(in_3), .in1(or_6_out), .out(out_14), .sel(or_2_out));
  Multiplexer #(.width(32), .enable("false")) multiplexer_15 (.in0(in_5), .in1(or_7_out), .out(out_15), .sel(or_1_out));
  Multiplexer #(.width(32), .enable("false")) multiplexer_16 (.in0(in_6), .in1(or_8_out), .out(out_16), .sel(or_1_out));
  D_Flip_Flop d_ff_1 (.clk(clock), .D(or_2_out), .Q(d_ff_1_q));  // open: Qn, preset, en, reset
  D_Flip_Flop d_ff_2 (.clk(clock), .D(or_1_out), .Q(d_ff_2_q));  // open: Qn, preset, en, reset
  Register #(.width(32), .trigger("falling")) register_1 (
    .D(or_5_out), .Q(register_1_q), .clk(clock));  // open: en, clr
  Comparator #(.width(32), .mode("unsigned")) comparator_5 (
    .a(register_1_q), .b(register_2_q), .eq(comparator_5_eq));  // open: gt, lt
  assign controlled_inverter_1_out = d_ff_1_q ? ~comparator_5_eq : 1'bz;  // Controlled_Inverter controlled_inverter_1
  Register #(.width(32), .trigger("falling")) register_2 (
    .D(xor_1_out), .Q(register_2_q), .clk(clock));  // open: en, clr
  Register #(.width(32), .trigger("falling")) register_3 (
    .D(or_6_out), .Q(register_3_q), .clk(clock));  // open: en, clr
  Comparator #(.width(32), .mode("unsigned")) comparator_6 (
    .a(register_3_q), .b(register_4_q), .eq(comparator_6_eq));  // open: gt, lt
  assign controlled_inverter_2_out = d_ff_1_q ? ~comparator_6_eq : 1'bz;  // Controlled_Inverter controlled_inverter_2
  Register #(.width(32), .trigger("falling")) register_4 (
    .D(xor_2_out), .Q(register_4_q), .clk(clock));  // open: en, clr
  Register #(.width(32), .trigger("falling")) register_5 (
    .D(or_7_out), .Q(register_5_q), .clk(clock));  // open: en, clr
  assign controlled_inverter_3_out = d_ff_2_q ? ~comparator_7_eq : 1'bz;  // Controlled_Inverter controlled_inverter_3
  Comparator #(.width(32), .mode("unsigned")) comparator_7 (
    .a(register_5_q), .b(register_6_q), .eq(comparator_7_eq));  // open: gt, lt
  Register #(.width(32), .trigger("falling")) register_6 (
    .D(xor_3_out), .Q(register_6_q), .clk(clock));  // open: en, clr
  Register #(.width(32), .trigger("falling")) register_7 (
    .D(or_8_out), .Q(register_7_q), .clk(clock));  // open: en, clr
  assign controlled_inverter_4_out = d_ff_2_q ? ~comparator_8_eq : 1'bz;  // Controlled_Inverter controlled_inverter_4
  Comparator #(.width(32), .mode("unsigned")) comparator_8 (
    .a(register_7_q), .b(register_8_q), .eq(comparator_8_eq));  // open: gt, lt
  Register #(.width(32), .trigger("falling")) register_8 (
    .D(xor_4_out), .Q(register_8_q), .clk(clock));  // open: en, clr
  Pull_Resistor pull_resistor_1 (.node(controlled_inverter_1_out));
  Pull_Resistor pull_resistor_2 (.node(controlled_inverter_2_out));
  Pull_Resistor pull_resistor_3 (.node(controlled_inverter_3_out));
  Pull_Resistor pull_resistor_4 (.node(controlled_inverter_4_out));
  and and_2 (and_2_out, ~clock32[0], ~clock32[1], ~clock32[2], ~clock32[3], ~clock32[4]);  // AND_Gate
  buf buffer_1 (buffer_1_out, buffer_2_out);
  buf buffer_2 (buffer_2_out, and_2_out);
  or or_9 (or_9_out, and_2_out, or_10_out);
  or or_10 (or_10_out, controlled_inverter_1_out, controlled_inverter_2_out, controlled_inverter_3_out, controlled_inverter_4_out);
  D_Flip_Flop d_ff_3 (.clk(buffer_1_out), .D(d_ff_4_q), .Q(out_17));  // open: Qn, preset, en, reset
  D_Flip_Flop d_ff_4 (.clk(or_9_out), .D(or_10_out), .Q(d_ff_4_q));  // open: Qn, preset, en, reset
endmodule

module character_module (
  input  in_1,
  input  [3:0] wasd,
  input  [4:0] clock32,
  output [5:0] x,
  output [5:0] y,
  output [3:0] out_6,
  output [3:0] out_7,
  output [3:0] out_8,
  output [3:0] out_9,
  output [3:0] out_10
);

  wire and_1_out, or_1_out, or_2_out;
  wire [3:0] counter_3_q;
  wire [5:0] counter_1_q, counter_2_q;

  Counter #(.width(6), .max('h2b), .ongoal("stay")) counter_1 (
    .load(wasd[1]), .count(or_1_out), .Q(counter_1_q), .clk(and_1_out));  // open: D, carry, clr
  or or_1 (or_1_out, wasd[1], wasd[3]);
  Adder #(.width(6)) adder_1 (.a(counter_1_q), .b(6'b001001), .out(x));  // open: cin, cout
  Counter #(.width(6), .max('h2b), .ongoal("stay")) counter_2 (
    .load(wasd[0]), .count(or_2_out), .Q(counter_2_q), .clk(and_1_out));  // open: D, carry, clr
  or or_2 (or_2_out, wasd[2], wasd[0]);
  Adder #(.width(6)) adder_2 (.a(counter_2_q), .b(6'b001001), .out(y));  // open: cin, cout
  Subtractor #(.width(4)) subtractor_1 (.a(4'b0001), .b(counter_3_q), .out(out_10));  // open: bin, bout
  Counter #(.width(4), .max('hf)) counter_3 (.Q(counter_3_q), .clk(in_1));  // open: load, D, count, carry, clr
  and and_1 (and_1_out, ~clock32[0], ~clock32[1], ~clock32[2], ~clock32[3], ~clock32[4]);  // AND_Gate

  assign out_6 = 4'b1010;
  assign out_7 = 4'b1110;
  assign out_8 = 4'b0100;
  assign out_9 = 4'b0000;
endmodule
module bullet_GPU (
  input  [31:0] in_1,
  input  in_2,
  input  [4:0] clock32,
  input  [31:0] in_4,
  input  [31:0] in_5,
  input  [31:0] in_6,
  input  [31:0] in_7,
  output [31:0] out_8,
  output [31:0] out_9,
  output [31:0] out_10,
  output [31:0] out_11
);

  wire bullet_module_1_working, bullet_module_2_working, bullet_module_3_working, bullet_module_4_working,
       bullet_module_5_working, bullet_module_6_working, bullet_module_7_working, bullet_module_8_working,
       bullet_module_9_working, bullet_module_10_working, bullet_module_11_working, bullet_module_12_working,
       bullet_module_13_working, bullet_module_14_working, bullet_module_15_working,
       bullet_module_16_working, bullet_module_17_working, bullet_module_18_working,
       bullet_module_19_working, bullet_module_20_working, bullet_module_21_working,
       bullet_module_22_working, bullet_module_23_working, bullet_module_24_working,
       bullet_module_25_working, bullet_module_26_working, bullet_module_27_working,
       bullet_module_28_working, bullet_module_29_working, bullet_module_30_working,
       bullet_module_31_working, d_ff_1_q, gpu_encoder_demultiplexpor_1_out_34,
       gpu_encoder_demultiplexpor_1_out_35, gpu_encoder_demultiplexpor_1_out_36,
       gpu_encoder_demultiplexpor_1_out_37, gpu_encoder_demultiplexpor_1_out_38,
       gpu_encoder_demultiplexpor_1_out_39, gpu_encoder_demultiplexpor_1_out_40,
       gpu_encoder_demultiplexpor_1_out_41, gpu_encoder_demultiplexpor_1_out_42,
       gpu_encoder_demultiplexpor_1_out_43, gpu_encoder_demultiplexpor_1_out_44,
       gpu_encoder_demultiplexpor_1_out_45, gpu_encoder_demultiplexpor_1_out_46,
       gpu_encoder_demultiplexpor_1_out_47, gpu_encoder_demultiplexpor_1_out_48,
       gpu_encoder_demultiplexpor_1_out_49, gpu_encoder_demultiplexpor_1_out_50,
       gpu_encoder_demultiplexpor_1_out_51, gpu_encoder_demultiplexpor_1_out_52,
       gpu_encoder_demultiplexpor_1_out_53, gpu_encoder_demultiplexpor_1_out_54,
       gpu_encoder_demultiplexpor_1_out_55, gpu_encoder_demultiplexpor_1_out_56,
       gpu_encoder_demultiplexpor_1_out_57, gpu_encoder_demultiplexpor_1_out_58,
       gpu_encoder_demultiplexpor_1_out_59, gpu_encoder_demultiplexpor_1_out_60,
       gpu_encoder_demultiplexpor_1_out_61, gpu_encoder_demultiplexpor_1_out_62,
       gpu_encoder_demultiplexpor_1_out_63, gpu_encoder_demultiplexpor_1_out_64;
  wire [3:0] bullet_module_1_out_4, bullet_module_1_out_5, bullet_module_1_out_6, bullet_module_1_out_7,
       bullet_module_2_out_4, bullet_module_2_out_5, bullet_module_2_out_6, bullet_module_2_out_7,
       bullet_module_3_out_4, bullet_module_3_out_5, bullet_module_3_out_6, bullet_module_3_out_7,
       bullet_module_4_out_4, bullet_module_4_out_5, bullet_module_4_out_6, bullet_module_4_out_7,
       bullet_module_5_out_4, bullet_module_5_out_5, bullet_module_5_out_6, bullet_module_5_out_7,
       bullet_module_6_out_4, bullet_module_6_out_5, bullet_module_6_out_6, bullet_module_6_out_7,
       bullet_module_7_out_4, bullet_module_7_out_5, bullet_module_7_out_6, bullet_module_7_out_7,
       bullet_module_8_out_4, bullet_module_8_out_5, bullet_module_8_out_6, bullet_module_8_out_7,
       bullet_module_9_out_4, bullet_module_9_out_5, bullet_module_9_out_6, bullet_module_9_out_7,
       bullet_module_10_out_4, bullet_module_10_out_5, bullet_module_10_out_6, bullet_module_10_out_7,
       bullet_module_11_out_4, bullet_module_11_out_5, bullet_module_11_out_6, bullet_module_11_out_7,
       bullet_module_12_out_4, bullet_module_12_out_5, bullet_module_12_out_6, bullet_module_12_out_7,
       bullet_module_13_out_4, bullet_module_13_out_5, bullet_module_13_out_6, bullet_module_13_out_7,
       bullet_module_14_out_4, bullet_module_14_out_5, bullet_module_14_out_6, bullet_module_14_out_7,
       bullet_module_15_out_4, bullet_module_15_out_5, bullet_module_15_out_6, bullet_module_15_out_7,
       bullet_module_16_out_4, bullet_module_16_out_5, bullet_module_16_out_6, bullet_module_16_out_7,
       bullet_module_17_out_4, bullet_module_17_out_5, bullet_module_17_out_6, bullet_module_17_out_7,
       bullet_module_18_out_4, bullet_module_18_out_5, bullet_module_18_out_6, bullet_module_18_out_7,
       bullet_module_19_out_4, bullet_module_19_out_5, bullet_module_19_out_6, bullet_module_19_out_7,
       bullet_module_20_out_4, bullet_module_20_out_5, bullet_module_20_out_6, bullet_module_20_out_7,
       bullet_module_21_out_4, bullet_module_21_out_5, bullet_module_21_out_6, bullet_module_21_out_7,
       bullet_module_22_out_4, bullet_module_22_out_5, bullet_module_22_out_6, bullet_module_22_out_7,
       bullet_module_23_out_4, bullet_module_23_out_5, bullet_module_23_out_6, bullet_module_23_out_7,
       bullet_module_24_out_4, bullet_module_24_out_5, bullet_module_24_out_6, bullet_module_24_out_7,
       bullet_module_25_out_4, bullet_module_25_out_5, bullet_module_25_out_6, bullet_module_25_out_7,
       bullet_module_26_out_4, bullet_module_26_out_5, bullet_module_26_out_6, bullet_module_26_out_7,
       bullet_module_27_out_4, bullet_module_27_out_5, bullet_module_27_out_6, bullet_module_27_out_7,
       bullet_module_28_out_4, bullet_module_28_out_5, bullet_module_28_out_6, bullet_module_28_out_7,
       bullet_module_29_out_4, bullet_module_29_out_5, bullet_module_29_out_6, bullet_module_29_out_7,
       bullet_module_30_out_4, bullet_module_30_out_5, bullet_module_30_out_6, bullet_module_30_out_7,
       bullet_module_31_out_4, bullet_module_31_out_5, bullet_module_31_out_6, bullet_module_31_out_7;
  wire [5:0] bullet_module_1_x, bullet_module_1_y, bullet_module_2_x, bullet_module_2_y, bullet_module_3_x,
       bullet_module_3_y, bullet_module_4_x, bullet_module_4_y, bullet_module_5_x, bullet_module_5_y,
       bullet_module_6_x, bullet_module_6_y, bullet_module_7_x, bullet_module_7_y, bullet_module_8_x,
       bullet_module_8_y, bullet_module_9_x, bullet_module_9_y, bullet_module_10_x, bullet_module_10_y,
       bullet_module_11_x, bullet_module_11_y, bullet_module_12_x, bullet_module_12_y, bullet_module_13_x,
       bullet_module_13_y, bullet_module_14_x, bullet_module_14_y, bullet_module_15_x, bullet_module_15_y,
       bullet_module_16_x, bullet_module_16_y, bullet_module_17_x, bullet_module_17_y, bullet_module_18_x,
       bullet_module_18_y, bullet_module_19_x, bullet_module_19_y, bullet_module_20_x, bullet_module_20_y,
       bullet_module_21_x, bullet_module_21_y, bullet_module_22_x, bullet_module_22_y, bullet_module_23_x,
       bullet_module_23_y, bullet_module_24_x, bullet_module_24_y, bullet_module_25_x, bullet_module_25_y,
       bullet_module_26_x, bullet_module_26_y, bullet_module_27_x, bullet_module_27_y, bullet_module_28_x,
       bullet_module_28_y, bullet_module_29_x, bullet_module_29_y, bullet_module_30_x, bullet_module_30_y,
       bullet_module_31_x, bullet_module_31_y;
  wire [31:0] task_drawer_1_out_13, task_drawer_1_out_14, task_drawer_1_out_15, task_drawer_1_out_16,
       task_drawer_2_out_13, task_drawer_2_out_14, task_drawer_2_out_15, task_drawer_2_out_16,
       task_drawer_3_out_13, task_drawer_3_out_14, task_drawer_3_out_15, task_drawer_3_out_16,
       task_drawer_4_out_13, task_drawer_4_out_14, task_drawer_4_out_15, task_drawer_4_out_16,
       task_drawer_5_out_13, task_drawer_5_out_14, task_drawer_5_out_15, task_drawer_5_out_16,
       task_drawer_6_out_13, task_drawer_6_out_14, task_drawer_6_out_15, task_drawer_6_out_16,
       task_drawer_7_out_13, task_drawer_7_out_14, task_drawer_7_out_15, task_drawer_7_out_16,
       task_drawer_8_out_13, task_drawer_8_out_14, task_drawer_8_out_15, task_drawer_8_out_16,
       task_drawer_9_out_13, task_drawer_9_out_14, task_drawer_9_out_15, task_drawer_9_out_16,
       task_drawer_10_out_13, task_drawer_10_out_14, task_drawer_10_out_15, task_drawer_10_out_16,
       task_drawer_11_out_13, task_drawer_11_out_14, task_drawer_11_out_15, task_drawer_11_out_16,
       task_drawer_12_out_13, task_drawer_12_out_14, task_drawer_12_out_15, task_drawer_12_out_16,
       task_drawer_13_out_13, task_drawer_13_out_14, task_drawer_13_out_15, task_drawer_13_out_16,
       task_drawer_14_out_13, task_drawer_14_out_14, task_drawer_14_out_15, task_drawer_14_out_16,
       task_drawer_15_out_13, task_drawer_15_out_14, task_drawer_15_out_15, task_drawer_15_out_16,
       task_drawer_16_out_13, task_drawer_16_out_14, task_drawer_16_out_15, task_drawer_16_out_16,
       task_drawer_17_out_13, task_drawer_17_out_14, task_drawer_17_out_15, task_drawer_17_out_16,
       task_drawer_18_out_13, task_drawer_18_out_14, task_drawer_18_out_15, task_drawer_18_out_16,
       task_drawer_19_out_13, task_drawer_19_out_14, task_drawer_19_out_15, task_drawer_19_out_16,
       task_drawer_20_out_13, task_drawer_20_out_14, task_drawer_20_out_15, task_drawer_20_out_16,
       task_drawer_21_out_13, task_drawer_21_out_14, task_drawer_21_out_15, task_drawer_21_out_16,
       task_drawer_22_out_13, task_drawer_22_out_14, task_drawer_22_out_15, task_drawer_22_out_16,
       task_drawer_23_out_13, task_drawer_23_out_14, task_drawer_23_out_15, task_drawer_23_out_16,
       task_drawer_24_out_13, task_drawer_24_out_14, task_drawer_24_out_15, task_drawer_24_out_16,
       task_drawer_25_out_13, task_drawer_25_out_14, task_drawer_25_out_15, task_drawer_25_out_16,
       task_drawer_26_out_13, task_drawer_26_out_14, task_drawer_26_out_15, task_drawer_26_out_16,
       task_drawer_27_out_13, task_drawer_27_out_14, task_drawer_27_out_15, task_drawer_27_out_16,
       task_drawer_28_out_13, task_drawer_28_out_14, task_drawer_28_out_15, task_drawer_28_out_16,
       task_drawer_29_out_13, task_drawer_29_out_14, task_drawer_29_out_15, task_drawer_29_out_16,
       task_drawer_30_out_13, task_drawer_30_out_14, task_drawer_30_out_15, task_drawer_30_out_16,
       task_drawer_31_out_13, task_drawer_31_out_14, task_drawer_31_out_15, task_drawer_31_out_16;

  D_Flip_Flop d_ff_1 (.clk(in_2), .D(in_2), .Q(d_ff_1_q), .reset(d_ff_1_q));  // open: Qn, preset, en
  bullet_module bullet_module_1 (
    .\input (in_1), .out_4(bullet_module_1_out_4), .out_5(bullet_module_1_out_5),
    .out_6(bullet_module_1_out_6), .y(bullet_module_1_y), .out_7(bullet_module_1_out_7),
    .x(bullet_module_1_x), .on(gpu_encoder_demultiplexpor_1_out_34), .working(bullet_module_1_working),
    .clock32(clock32));
  bullet_module bullet_module_2 (
    .\input (in_1), .out_4(bullet_module_2_out_4), .out_5(bullet_module_2_out_5),
    .out_6(bullet_module_2_out_6), .y(bullet_module_2_y), .out_7(bullet_module_2_out_7),
    .x(bullet_module_2_x), .on(gpu_encoder_demultiplexpor_1_out_35), .working(bullet_module_2_working),
    .clock32(clock32));
  gpu_encoder_demultiplexpor gpu_encoder_demultiplexpor_1 (
    .in_1(bullet_module_1_working), .in_2(bullet_module_2_working), .in_3(bullet_module_3_working),
    .in_4(bullet_module_4_working), .in_5(bullet_module_5_working), .in_6(bullet_module_6_working),
    .in_7(bullet_module_7_working), .in_8(bullet_module_8_working), .in_9(bullet_module_9_working),
    .in_10(bullet_module_10_working), .in_11(bullet_module_11_working), .in_12(bullet_module_12_working),
    .in_13(bullet_module_13_working), .in_14(bullet_module_14_working), .in_15(bullet_module_15_working),
    .in_16(bullet_module_16_working), .in_17(bullet_module_17_working), .in_18(bullet_module_18_working),
    .in_19(bullet_module_19_working), .in_20(bullet_module_20_working), .in_21(bullet_module_21_working),
    .in_22(bullet_module_22_working), .in_23(bullet_module_23_working), .in_24(bullet_module_24_working),
    .in_25(bullet_module_25_working), .in_26(bullet_module_26_working), .in_27(bullet_module_27_working),
    .in_28(bullet_module_28_working), .in_29(bullet_module_29_working), .in_30(bullet_module_30_working),
    .in_31(bullet_module_31_working), .out_34(gpu_encoder_demultiplexpor_1_out_34),
    .out_35(gpu_encoder_demultiplexpor_1_out_35), .out_36(gpu_encoder_demultiplexpor_1_out_36),
    .out_37(gpu_encoder_demultiplexpor_1_out_37), .out_38(gpu_encoder_demultiplexpor_1_out_38),
    .out_39(gpu_encoder_demultiplexpor_1_out_39), .out_40(gpu_encoder_demultiplexpor_1_out_40),
    .out_41(gpu_encoder_demultiplexpor_1_out_41), .out_42(gpu_encoder_demultiplexpor_1_out_42),
    .out_43(gpu_encoder_demultiplexpor_1_out_43), .out_44(gpu_encoder_demultiplexpor_1_out_44),
    .out_45(gpu_encoder_demultiplexpor_1_out_45), .out_46(gpu_encoder_demultiplexpor_1_out_46),
    .out_47(gpu_encoder_demultiplexpor_1_out_47), .out_48(gpu_encoder_demultiplexpor_1_out_48),
    .out_49(gpu_encoder_demultiplexpor_1_out_49), .out_50(gpu_encoder_demultiplexpor_1_out_50),
    .out_51(gpu_encoder_demultiplexpor_1_out_51), .out_52(gpu_encoder_demultiplexpor_1_out_52),
    .out_53(gpu_encoder_demultiplexpor_1_out_53), .out_54(gpu_encoder_demultiplexpor_1_out_54),
    .out_55(gpu_encoder_demultiplexpor_1_out_55), .out_56(gpu_encoder_demultiplexpor_1_out_56),
    .out_57(gpu_encoder_demultiplexpor_1_out_57), .out_58(gpu_encoder_demultiplexpor_1_out_58),
    .out_59(gpu_encoder_demultiplexpor_1_out_59), .out_60(gpu_encoder_demultiplexpor_1_out_60),
    .out_61(gpu_encoder_demultiplexpor_1_out_61), .out_62(gpu_encoder_demultiplexpor_1_out_62),
    .out_63(gpu_encoder_demultiplexpor_1_out_63), .out_64(gpu_encoder_demultiplexpor_1_out_64),
    .in_33(d_ff_1_q));  // open: in_32, out_65
  bullet_module bullet_module_3 (
    .\input (in_1), .out_4(bullet_module_3_out_4), .out_5(bullet_module_3_out_5),
    .out_6(bullet_module_3_out_6), .y(bullet_module_3_y), .out_7(bullet_module_3_out_7),
    .x(bullet_module_3_x), .on(gpu_encoder_demultiplexpor_1_out_36), .working(bullet_module_3_working),
    .clock32(clock32));
  bullet_module bullet_module_4 (
    .\input (in_1), .out_4(bullet_module_4_out_4), .out_5(bullet_module_4_out_5),
    .out_6(bullet_module_4_out_6), .y(bullet_module_4_y), .out_7(bullet_module_4_out_7),
    .x(bullet_module_4_x), .on(gpu_encoder_demultiplexpor_1_out_37), .working(bullet_module_4_working),
    .clock32(clock32));
  bullet_module bullet_module_5 (
    .\input (in_1), .out_4(bullet_module_5_out_4), .out_5(bullet_module_5_out_5),
    .out_6(bullet_module_5_out_6), .y(bullet_module_5_y), .out_7(bullet_module_5_out_7),
    .x(bullet_module_5_x), .on(gpu_encoder_demultiplexpor_1_out_38), .working(bullet_module_5_working),
    .clock32(clock32));
  bullet_module bullet_module_6 (
    .\input (in_1), .out_4(bullet_module_6_out_4), .out_5(bullet_module_6_out_5),
    .out_6(bullet_module_6_out_6), .y(bullet_module_6_y), .out_7(bullet_module_6_out_7),
    .x(bullet_module_6_x), .on(gpu_encoder_demultiplexpor_1_out_39), .working(bullet_module_6_working),
    .clock32(clock32));
  bullet_module bullet_module_7 (
    .\input (in_1), .out_4(bullet_module_7_out_4), .out_5(bullet_module_7_out_5),
    .out_6(bullet_module_7_out_6), .y(bullet_module_7_y), .out_7(bullet_module_7_out_7),
    .x(bullet_module_7_x), .on(gpu_encoder_demultiplexpor_1_out_40), .working(bullet_module_7_working),
    .clock32(clock32));
  bullet_module bullet_module_8 (
    .\input (in_1), .out_4(bullet_module_8_out_4), .out_5(bullet_module_8_out_5),
    .out_6(bullet_module_8_out_6), .y(bullet_module_8_y), .out_7(bullet_module_8_out_7),
    .x(bullet_module_8_x), .on(gpu_encoder_demultiplexpor_1_out_41), .working(bullet_module_8_working),
    .clock32(clock32));
  bullet_module bullet_module_9 (
    .\input (in_1), .out_4(bullet_module_9_out_4), .out_5(bullet_module_9_out_5),
    .out_6(bullet_module_9_out_6), .y(bullet_module_9_y), .out_7(bullet_module_9_out_7),
    .x(bullet_module_9_x), .on(gpu_encoder_demultiplexpor_1_out_42), .working(bullet_module_9_working),
    .clock32(clock32));
  bullet_module bullet_module_10 (
    .\input (in_1), .out_4(bullet_module_10_out_4), .out_5(bullet_module_10_out_5),
    .out_6(bullet_module_10_out_6), .y(bullet_module_10_y), .out_7(bullet_module_10_out_7),
    .x(bullet_module_10_x), .on(gpu_encoder_demultiplexpor_1_out_43), .working(bullet_module_10_working),
    .clock32(clock32));
  bullet_module bullet_module_11 (
    .\input (in_1), .out_4(bullet_module_11_out_4), .out_5(bullet_module_11_out_5),
    .out_6(bullet_module_11_out_6), .y(bullet_module_11_y), .out_7(bullet_module_11_out_7),
    .x(bullet_module_11_x), .on(gpu_encoder_demultiplexpor_1_out_44), .working(bullet_module_11_working),
    .clock32(clock32));
  bullet_module bullet_module_12 (
    .\input (in_1), .out_4(bullet_module_12_out_4), .out_5(bullet_module_12_out_5),
    .out_6(bullet_module_12_out_6), .y(bullet_module_12_y), .out_7(bullet_module_12_out_7),
    .x(bullet_module_12_x), .on(gpu_encoder_demultiplexpor_1_out_45), .working(bullet_module_12_working),
    .clock32(clock32));
  bullet_module bullet_module_13 (
    .\input (in_1), .out_4(bullet_module_13_out_4), .out_5(bullet_module_13_out_5),
    .out_6(bullet_module_13_out_6), .y(bullet_module_13_y), .out_7(bullet_module_13_out_7),
    .x(bullet_module_13_x), .on(gpu_encoder_demultiplexpor_1_out_46), .working(bullet_module_13_working),
    .clock32(clock32));
  bullet_module bullet_module_14 (
    .\input (in_1), .out_4(bullet_module_14_out_4), .out_5(bullet_module_14_out_5),
    .out_6(bullet_module_14_out_6), .y(bullet_module_14_y), .out_7(bullet_module_14_out_7),
    .x(bullet_module_14_x), .on(gpu_encoder_demultiplexpor_1_out_47), .working(bullet_module_14_working),
    .clock32(clock32));
  bullet_module bullet_module_15 (
    .\input (in_1), .out_4(bullet_module_15_out_4), .out_5(bullet_module_15_out_5),
    .out_6(bullet_module_15_out_6), .y(bullet_module_15_y), .out_7(bullet_module_15_out_7),
    .x(bullet_module_15_x), .on(gpu_encoder_demultiplexpor_1_out_48), .working(bullet_module_15_working),
    .clock32(clock32));
  bullet_module bullet_module_16 (
    .\input (in_1), .out_4(bullet_module_16_out_4), .out_5(bullet_module_16_out_5),
    .out_6(bullet_module_16_out_6), .y(bullet_module_16_y), .out_7(bullet_module_16_out_7),
    .x(bullet_module_16_x), .on(gpu_encoder_demultiplexpor_1_out_49), .working(bullet_module_16_working),
    .clock32(clock32));
  bullet_module bullet_module_17 (
    .\input (in_1), .out_4(bullet_module_17_out_4), .out_5(bullet_module_17_out_5),
    .out_6(bullet_module_17_out_6), .y(bullet_module_17_y), .out_7(bullet_module_17_out_7),
    .x(bullet_module_17_x), .on(gpu_encoder_demultiplexpor_1_out_50), .working(bullet_module_17_working),
    .clock32(clock32));
  bullet_module bullet_module_18 (
    .\input (in_1), .out_4(bullet_module_18_out_4), .out_5(bullet_module_18_out_5),
    .out_6(bullet_module_18_out_6), .y(bullet_module_18_y), .out_7(bullet_module_18_out_7),
    .x(bullet_module_18_x), .on(gpu_encoder_demultiplexpor_1_out_51), .working(bullet_module_18_working),
    .clock32(clock32));
  bullet_module bullet_module_19 (
    .\input (in_1), .out_4(bullet_module_19_out_4), .out_5(bullet_module_19_out_5),
    .out_6(bullet_module_19_out_6), .y(bullet_module_19_y), .out_7(bullet_module_19_out_7),
    .x(bullet_module_19_x), .on(gpu_encoder_demultiplexpor_1_out_52), .working(bullet_module_19_working),
    .clock32(clock32));
  bullet_module bullet_module_20 (
    .\input (in_1), .out_4(bullet_module_20_out_4), .out_5(bullet_module_20_out_5),
    .out_6(bullet_module_20_out_6), .y(bullet_module_20_y), .out_7(bullet_module_20_out_7),
    .x(bullet_module_20_x), .on(gpu_encoder_demultiplexpor_1_out_53), .working(bullet_module_20_working),
    .clock32(clock32));
  bullet_module bullet_module_21 (
    .\input (in_1), .out_4(bullet_module_21_out_4), .out_5(bullet_module_21_out_5),
    .out_6(bullet_module_21_out_6), .y(bullet_module_21_y), .out_7(bullet_module_21_out_7),
    .x(bullet_module_21_x), .on(gpu_encoder_demultiplexpor_1_out_54), .working(bullet_module_21_working),
    .clock32(clock32));
  bullet_module bullet_module_22 (
    .\input (in_1), .out_4(bullet_module_22_out_4), .out_5(bullet_module_22_out_5),
    .out_6(bullet_module_22_out_6), .y(bullet_module_22_y), .out_7(bullet_module_22_out_7),
    .x(bullet_module_22_x), .on(gpu_encoder_demultiplexpor_1_out_55), .working(bullet_module_22_working),
    .clock32(clock32));
  bullet_module bullet_module_23 (
    .\input (in_1), .out_4(bullet_module_23_out_4), .out_5(bullet_module_23_out_5),
    .out_6(bullet_module_23_out_6), .y(bullet_module_23_y), .out_7(bullet_module_23_out_7),
    .x(bullet_module_23_x), .on(gpu_encoder_demultiplexpor_1_out_56), .working(bullet_module_23_working),
    .clock32(clock32));
  bullet_module bullet_module_24 (
    .\input (in_1), .out_4(bullet_module_24_out_4), .out_5(bullet_module_24_out_5),
    .out_6(bullet_module_24_out_6), .y(bullet_module_24_y), .out_7(bullet_module_24_out_7),
    .x(bullet_module_24_x), .on(gpu_encoder_demultiplexpor_1_out_57), .working(bullet_module_24_working),
    .clock32(clock32));
  bullet_module bullet_module_25 (
    .\input (in_1), .out_4(bullet_module_25_out_4), .out_5(bullet_module_25_out_5),
    .out_6(bullet_module_25_out_6), .y(bullet_module_25_y), .out_7(bullet_module_25_out_7),
    .x(bullet_module_25_x), .on(gpu_encoder_demultiplexpor_1_out_58), .working(bullet_module_25_working),
    .clock32(clock32));
  bullet_module bullet_module_26 (
    .\input (in_1), .out_4(bullet_module_26_out_4), .out_5(bullet_module_26_out_5),
    .out_6(bullet_module_26_out_6), .y(bullet_module_26_y), .out_7(bullet_module_26_out_7),
    .x(bullet_module_26_x), .on(gpu_encoder_demultiplexpor_1_out_59), .working(bullet_module_26_working),
    .clock32(clock32));
  bullet_module bullet_module_27 (
    .\input (in_1), .out_4(bullet_module_27_out_4), .out_5(bullet_module_27_out_5),
    .out_6(bullet_module_27_out_6), .y(bullet_module_27_y), .out_7(bullet_module_27_out_7),
    .x(bullet_module_27_x), .on(gpu_encoder_demultiplexpor_1_out_60), .working(bullet_module_27_working),
    .clock32(clock32));
  bullet_module bullet_module_28 (
    .\input (in_1), .out_4(bullet_module_28_out_4), .out_5(bullet_module_28_out_5),
    .out_6(bullet_module_28_out_6), .y(bullet_module_28_y), .out_7(bullet_module_28_out_7),
    .x(bullet_module_28_x), .on(gpu_encoder_demultiplexpor_1_out_61), .working(bullet_module_28_working),
    .clock32(clock32));
  bullet_module bullet_module_29 (
    .\input (in_1), .out_4(bullet_module_29_out_4), .out_5(bullet_module_29_out_5),
    .out_6(bullet_module_29_out_6), .y(bullet_module_29_y), .out_7(bullet_module_29_out_7),
    .x(bullet_module_29_x), .on(gpu_encoder_demultiplexpor_1_out_62), .working(bullet_module_29_working),
    .clock32(clock32));
  bullet_module bullet_module_30 (
    .\input (in_1), .out_4(bullet_module_30_out_4), .out_5(bullet_module_30_out_5),
    .out_6(bullet_module_30_out_6), .y(bullet_module_30_y), .out_7(bullet_module_30_out_7),
    .x(bullet_module_30_x), .on(gpu_encoder_demultiplexpor_1_out_63), .working(bullet_module_30_working),
    .clock32(clock32));
  bullet_module bullet_module_31 (
    .\input (in_1), .out_4(bullet_module_31_out_4), .out_5(bullet_module_31_out_5),
    .out_6(bullet_module_31_out_6), .y(bullet_module_31_y), .out_7(bullet_module_31_out_7),
    .x(bullet_module_31_x), .on(gpu_encoder_demultiplexpor_1_out_64), .working(bullet_module_31_working),
    .clock32(clock32));
  BGPU_or_module bgpu_or_module_1 (
    ._1_33(out_8), ._1(task_drawer_1_out_13), ._1_2(task_drawer_2_out_13), ._1_3(task_drawer_3_out_13),
    ._1_4(task_drawer_4_out_13), ._1_5(task_drawer_5_out_13), ._1_6(task_drawer_6_out_13),
    ._1_7(task_drawer_7_out_13), ._1_8(task_drawer_8_out_13), ._1_9(task_drawer_9_out_13),
    ._1_10(task_drawer_10_out_13), ._1_11(task_drawer_11_out_13), ._1_12(task_drawer_12_out_13),
    ._1_13(task_drawer_13_out_13), ._1_14(task_drawer_14_out_13), ._1_15(task_drawer_15_out_13),
    ._1_16(task_drawer_16_out_13), ._1_17(task_drawer_17_out_13), ._1_18(task_drawer_18_out_13),
    ._1_19(task_drawer_19_out_13), ._1_20(task_drawer_20_out_13), ._1_21(task_drawer_21_out_13),
    ._1_22(task_drawer_22_out_13), ._1_23(task_drawer_23_out_13), ._1_24(task_drawer_24_out_13),
    ._1_25(task_drawer_25_out_13), ._1_26(task_drawer_26_out_13), ._1_27(task_drawer_27_out_13),
    ._1_28(task_drawer_28_out_13), ._1_29(task_drawer_29_out_13), ._1_30(task_drawer_30_out_13),
    ._1_31(task_drawer_31_out_13), ._1_32(in_4));
  BGPU_or_module bgpu_or_module_2 (
    ._1_33(out_9), ._1(task_drawer_1_out_14), ._1_2(task_drawer_2_out_14), ._1_3(task_drawer_3_out_14),
    ._1_4(task_drawer_4_out_14), ._1_5(task_drawer_5_out_14), ._1_6(task_drawer_6_out_14),
    ._1_7(task_drawer_7_out_14), ._1_8(task_drawer_8_out_14), ._1_9(task_drawer_9_out_14),
    ._1_10(task_drawer_10_out_14), ._1_11(task_drawer_11_out_14), ._1_12(task_drawer_12_out_14),
    ._1_13(task_drawer_13_out_14), ._1_14(task_drawer_14_out_14), ._1_15(task_drawer_15_out_14),
    ._1_16(task_drawer_16_out_14), ._1_17(task_drawer_17_out_14), ._1_18(task_drawer_18_out_14),
    ._1_19(task_drawer_19_out_14), ._1_20(task_drawer_20_out_14), ._1_21(task_drawer_21_out_14),
    ._1_22(task_drawer_22_out_14), ._1_23(task_drawer_23_out_14), ._1_24(task_drawer_24_out_14),
    ._1_25(task_drawer_25_out_14), ._1_26(task_drawer_26_out_14), ._1_27(task_drawer_27_out_14),
    ._1_28(task_drawer_28_out_14), ._1_29(task_drawer_29_out_14), ._1_30(task_drawer_30_out_14),
    ._1_31(task_drawer_31_out_14), ._1_32(in_5));
  BGPU_or_module bgpu_or_module_3 (
    ._1_33(out_10), ._1(task_drawer_1_out_15), ._1_2(task_drawer_2_out_15), ._1_3(task_drawer_3_out_15),
    ._1_4(task_drawer_4_out_15), ._1_5(task_drawer_5_out_15), ._1_6(task_drawer_6_out_15),
    ._1_7(task_drawer_7_out_15), ._1_8(task_drawer_8_out_15), ._1_9(task_drawer_9_out_15),
    ._1_10(task_drawer_10_out_15), ._1_11(task_drawer_11_out_15), ._1_12(task_drawer_12_out_15),
    ._1_13(task_drawer_13_out_15), ._1_14(task_drawer_14_out_15), ._1_15(task_drawer_15_out_15),
    ._1_16(task_drawer_16_out_15), ._1_17(task_drawer_17_out_15), ._1_18(task_drawer_18_out_15),
    ._1_19(task_drawer_19_out_15), ._1_20(task_drawer_20_out_15), ._1_21(task_drawer_21_out_15),
    ._1_22(task_drawer_22_out_15), ._1_23(task_drawer_23_out_15), ._1_24(task_drawer_24_out_15),
    ._1_25(task_drawer_25_out_15), ._1_26(task_drawer_26_out_15), ._1_27(task_drawer_27_out_15),
    ._1_28(task_drawer_28_out_15), ._1_29(task_drawer_29_out_15), ._1_30(task_drawer_30_out_15),
    ._1_31(task_drawer_31_out_15), ._1_32(in_6));
  BGPU_or_module bgpu_or_module_4 (
    ._1_33(out_11), ._1(task_drawer_1_out_16), ._1_2(task_drawer_2_out_16), ._1_3(task_drawer_3_out_16),
    ._1_4(task_drawer_4_out_16), ._1_5(task_drawer_5_out_16), ._1_6(task_drawer_6_out_16),
    ._1_7(task_drawer_7_out_16), ._1_8(task_drawer_8_out_16), ._1_9(task_drawer_9_out_16),
    ._1_10(task_drawer_10_out_16), ._1_11(task_drawer_11_out_16), ._1_12(task_drawer_12_out_16),
    ._1_13(task_drawer_13_out_16), ._1_14(task_drawer_14_out_16), ._1_15(task_drawer_15_out_16),
    ._1_16(task_drawer_16_out_16), ._1_17(task_drawer_17_out_16), ._1_18(task_drawer_18_out_16),
    ._1_19(task_drawer_19_out_16), ._1_20(task_drawer_20_out_16), ._1_21(task_drawer_21_out_16),
    ._1_22(task_drawer_22_out_16), ._1_23(task_drawer_23_out_16), ._1_24(task_drawer_24_out_16),
    ._1_25(task_drawer_25_out_16), ._1_26(task_drawer_26_out_16), ._1_27(task_drawer_27_out_16),
    ._1_28(task_drawer_28_out_16), ._1_29(task_drawer_29_out_16), ._1_30(task_drawer_30_out_16),
    ._1_31(task_drawer_31_out_16), ._1_32(in_7));
  task_drawer task_drawer_1 (
    .in_2(in_4), .clock32(clock32), .in_4(in_5), .y(bullet_module_1_y), .in_6(in_6), .in_7(in_7),
    .x(bullet_module_1_x), .in_9(bullet_module_1_out_4), .in_10(bullet_module_1_out_5),
    .in_11(bullet_module_1_out_6), .in_12(bullet_module_1_out_7), .out_13(task_drawer_1_out_13),
    .out_14(task_drawer_1_out_14), .out_15(task_drawer_1_out_15), .out_16(task_drawer_1_out_16),
    .in_1(bullet_module_1_working));
  task_drawer task_drawer_2 (
    .in_2(in_4), .clock32(clock32), .in_4(in_5), .y(bullet_module_2_y), .in_6(in_6), .in_7(in_7),
    .x(bullet_module_2_x), .in_9(bullet_module_2_out_4), .in_10(bullet_module_2_out_5),
    .in_11(bullet_module_2_out_6), .in_12(bullet_module_2_out_7), .out_13(task_drawer_2_out_13),
    .out_14(task_drawer_2_out_14), .out_15(task_drawer_2_out_15), .out_16(task_drawer_2_out_16),
    .in_1(bullet_module_2_working));
  task_drawer task_drawer_3 (
    .in_2(in_4), .clock32(clock32), .in_4(in_5), .y(bullet_module_3_y), .in_6(in_6), .in_7(in_7),
    .x(bullet_module_3_x), .in_9(bullet_module_3_out_4), .in_10(bullet_module_3_out_5),
    .in_11(bullet_module_3_out_6), .in_12(bullet_module_3_out_7), .out_13(task_drawer_3_out_13),
    .out_14(task_drawer_3_out_14), .out_15(task_drawer_3_out_15), .out_16(task_drawer_3_out_16),
    .in_1(bullet_module_3_working));
  task_drawer task_drawer_4 (
    .in_2(in_4), .clock32(clock32), .in_4(in_5), .y(bullet_module_4_y), .in_6(in_6), .in_7(in_7),
    .x(bullet_module_4_x), .in_9(bullet_module_4_out_4), .in_10(bullet_module_4_out_5),
    .in_11(bullet_module_4_out_6), .in_12(bullet_module_4_out_7), .out_13(task_drawer_4_out_13),
    .out_14(task_drawer_4_out_14), .out_15(task_drawer_4_out_15), .out_16(task_drawer_4_out_16),
    .in_1(bullet_module_4_working));
  task_drawer task_drawer_5 (
    .in_2(in_4), .clock32(clock32), .in_4(in_5), .y(bullet_module_5_y), .in_6(in_6), .in_7(in_7),
    .x(bullet_module_5_x), .in_9(bullet_module_5_out_4), .in_10(bullet_module_5_out_5),
    .in_11(bullet_module_5_out_6), .in_12(bullet_module_5_out_7), .out_13(task_drawer_5_out_13),
    .out_14(task_drawer_5_out_14), .out_15(task_drawer_5_out_15), .out_16(task_drawer_5_out_16),
    .in_1(bullet_module_5_working));
  task_drawer task_drawer_6 (
    .in_2(in_4), .clock32(clock32), .in_4(in_5), .y(bullet_module_6_y), .in_6(in_6), .in_7(in_7),
    .x(bullet_module_6_x), .in_9(bullet_module_6_out_4), .in_10(bullet_module_6_out_5),
    .in_11(bullet_module_6_out_6), .in_12(bullet_module_6_out_7), .out_13(task_drawer_6_out_13),
    .out_14(task_drawer_6_out_14), .out_15(task_drawer_6_out_15), .out_16(task_drawer_6_out_16),
    .in_1(bullet_module_6_working));
  task_drawer task_drawer_7 (
    .in_2(in_4), .clock32(clock32), .in_4(in_5), .y(bullet_module_7_y), .in_6(in_6), .in_7(in_7),
    .x(bullet_module_7_x), .in_9(bullet_module_7_out_4), .in_10(bullet_module_7_out_5),
    .in_11(bullet_module_7_out_6), .in_12(bullet_module_7_out_7), .out_13(task_drawer_7_out_13),
    .out_14(task_drawer_7_out_14), .out_15(task_drawer_7_out_15), .out_16(task_drawer_7_out_16),
    .in_1(bullet_module_7_working));
  task_drawer task_drawer_8 (
    .in_2(in_4), .clock32(clock32), .in_4(in_5), .y(bullet_module_8_y), .in_6(in_6), .in_7(in_7),
    .x(bullet_module_8_x), .in_9(bullet_module_8_out_4), .in_10(bullet_module_8_out_5),
    .in_11(bullet_module_8_out_6), .in_12(bullet_module_8_out_7), .out_13(task_drawer_8_out_13),
    .out_14(task_drawer_8_out_14), .out_15(task_drawer_8_out_15), .out_16(task_drawer_8_out_16),
    .in_1(bullet_module_8_working));
  task_drawer task_drawer_9 (
    .in_2(in_4), .clock32(clock32), .in_4(in_5), .y(bullet_module_9_y), .in_6(in_6), .in_7(in_7),
    .x(bullet_module_9_x), .in_9(bullet_module_9_out_4), .in_10(bullet_module_9_out_5),
    .in_11(bullet_module_9_out_6), .in_12(bullet_module_9_out_7), .out_13(task_drawer_9_out_13),
    .out_14(task_drawer_9_out_14), .out_15(task_drawer_9_out_15), .out_16(task_drawer_9_out_16),
    .in_1(bullet_module_9_working));
  task_drawer task_drawer_10 (
    .in_2(in_4), .clock32(clock32), .in_4(in_5), .y(bullet_module_10_y), .in_6(in_6), .in_7(in_7),
    .x(bullet_module_10_x), .in_9(bullet_module_10_out_4), .in_10(bullet_module_10_out_5),
    .in_11(bullet_module_10_out_6), .in_12(bullet_module_10_out_7), .out_13(task_drawer_10_out_13),
    .out_14(task_drawer_10_out_14), .out_15(task_drawer_10_out_15), .out_16(task_drawer_10_out_16),
    .in_1(bullet_module_10_working));
  task_drawer task_drawer_11 (
    .in_2(in_4), .clock32(clock32), .in_4(in_5), .y(bullet_module_11_y), .in_6(in_6), .in_7(in_7),
    .x(bullet_module_11_x), .in_9(bullet_module_11_out_4), .in_10(bullet_module_11_out_5),
    .in_11(bullet_module_11_out_6), .in_12(bullet_module_11_out_7), .out_13(task_drawer_11_out_13),
    .out_14(task_drawer_11_out_14), .out_15(task_drawer_11_out_15), .out_16(task_drawer_11_out_16),
    .in_1(bullet_module_11_working));
  task_drawer task_drawer_12 (
    .in_2(in_4), .clock32(clock32), .in_4(in_5), .y(bullet_module_12_y), .in_6(in_6), .in_7(in_7),
    .x(bullet_module_12_x), .in_9(bullet_module_12_out_4), .in_10(bullet_module_12_out_5),
    .in_11(bullet_module_12_out_6), .in_12(bullet_module_12_out_7), .out_13(task_drawer_12_out_13),
    .out_14(task_drawer_12_out_14), .out_15(task_drawer_12_out_15), .out_16(task_drawer_12_out_16),
    .in_1(bullet_module_12_working));
  task_drawer task_drawer_13 (
    .in_2(in_4), .clock32(clock32), .in_4(in_5), .y(bullet_module_13_y), .in_6(in_6), .in_7(in_7),
    .x(bullet_module_13_x), .in_9(bullet_module_13_out_4), .in_10(bullet_module_13_out_5),
    .in_11(bullet_module_13_out_6), .in_12(bullet_module_13_out_7), .out_13(task_drawer_13_out_13),
    .out_14(task_drawer_13_out_14), .out_15(task_drawer_13_out_15), .out_16(task_drawer_13_out_16),
    .in_1(bullet_module_13_working));
  task_drawer task_drawer_14 (
    .in_2(in_4), .clock32(clock32), .in_4(in_5), .y(bullet_module_14_y), .in_6(in_6), .in_7(in_7),
    .x(bullet_module_14_x), .in_9(bullet_module_14_out_4), .in_10(bullet_module_14_out_5),
    .in_11(bullet_module_14_out_6), .in_12(bullet_module_14_out_7), .out_13(task_drawer_14_out_13),
    .out_14(task_drawer_14_out_14), .out_15(task_drawer_14_out_15), .out_16(task_drawer_14_out_16),
    .in_1(bullet_module_14_working));
  task_drawer task_drawer_15 (
    .in_2(in_4), .clock32(clock32), .in_4(in_5), .y(bullet_module_15_y), .in_6(in_6), .in_7(in_7),
    .x(bullet_module_15_x), .in_9(bullet_module_15_out_4), .in_10(bullet_module_15_out_5),
    .in_11(bullet_module_15_out_6), .in_12(bullet_module_15_out_7), .out_13(task_drawer_15_out_13),
    .out_14(task_drawer_15_out_14), .out_15(task_drawer_15_out_15), .out_16(task_drawer_15_out_16),
    .in_1(bullet_module_15_working));
  task_drawer task_drawer_16 (
    .in_2(in_4), .clock32(clock32), .in_4(in_5), .y(bullet_module_16_y), .in_6(in_6), .in_7(in_7),
    .x(bullet_module_16_x), .in_9(bullet_module_16_out_4), .in_10(bullet_module_16_out_5),
    .in_11(bullet_module_16_out_6), .in_12(bullet_module_16_out_7), .out_13(task_drawer_16_out_13),
    .out_14(task_drawer_16_out_14), .out_15(task_drawer_16_out_15), .out_16(task_drawer_16_out_16),
    .in_1(bullet_module_16_working));
  task_drawer task_drawer_17 (
    .in_2(in_4), .clock32(clock32), .in_4(in_5), .y(bullet_module_17_y), .in_6(in_6), .in_7(in_7),
    .x(bullet_module_17_x), .in_9(bullet_module_17_out_4), .in_10(bullet_module_17_out_5),
    .in_11(bullet_module_17_out_6), .in_12(bullet_module_17_out_7), .out_13(task_drawer_17_out_13),
    .out_14(task_drawer_17_out_14), .out_15(task_drawer_17_out_15), .out_16(task_drawer_17_out_16),
    .in_1(bullet_module_17_working));
  task_drawer task_drawer_18 (
    .in_2(in_4), .clock32(clock32), .in_4(in_5), .y(bullet_module_18_y), .in_6(in_6), .in_7(in_7),
    .x(bullet_module_18_x), .in_9(bullet_module_18_out_4), .in_10(bullet_module_18_out_5),
    .in_11(bullet_module_18_out_6), .in_12(bullet_module_18_out_7), .out_13(task_drawer_18_out_13),
    .out_14(task_drawer_18_out_14), .out_15(task_drawer_18_out_15), .out_16(task_drawer_18_out_16),
    .in_1(bullet_module_18_working));
  task_drawer task_drawer_19 (
    .in_2(in_4), .clock32(clock32), .in_4(in_5), .y(bullet_module_19_y), .in_6(in_6), .in_7(in_7),
    .x(bullet_module_19_x), .in_9(bullet_module_19_out_4), .in_10(bullet_module_19_out_5),
    .in_11(bullet_module_19_out_6), .in_12(bullet_module_19_out_7), .out_13(task_drawer_19_out_13),
    .out_14(task_drawer_19_out_14), .out_15(task_drawer_19_out_15), .out_16(task_drawer_19_out_16),
    .in_1(bullet_module_19_working));
  task_drawer task_drawer_20 (
    .in_2(in_4), .clock32(clock32), .in_4(in_5), .y(bullet_module_20_y), .in_6(in_6), .in_7(in_7),
    .x(bullet_module_20_x), .in_9(bullet_module_20_out_4), .in_10(bullet_module_20_out_5),
    .in_11(bullet_module_20_out_6), .in_12(bullet_module_20_out_7), .out_13(task_drawer_20_out_13),
    .out_14(task_drawer_20_out_14), .out_15(task_drawer_20_out_15), .out_16(task_drawer_20_out_16),
    .in_1(bullet_module_20_working));
  task_drawer task_drawer_21 (
    .in_2(in_4), .clock32(clock32), .in_4(in_5), .y(bullet_module_21_y), .in_6(in_6), .in_7(in_7),
    .x(bullet_module_21_x), .in_9(bullet_module_21_out_4), .in_10(bullet_module_21_out_5),
    .in_11(bullet_module_21_out_6), .in_12(bullet_module_21_out_7), .out_13(task_drawer_21_out_13),
    .out_14(task_drawer_21_out_14), .out_15(task_drawer_21_out_15), .out_16(task_drawer_21_out_16),
    .in_1(bullet_module_21_working));
  task_drawer task_drawer_22 (
    .in_2(in_4), .clock32(clock32), .in_4(in_5), .y(bullet_module_22_y), .in_6(in_6), .in_7(in_7),
    .x(bullet_module_22_x), .in_9(bullet_module_22_out_4), .in_10(bullet_module_22_out_5),
    .in_11(bullet_module_22_out_6), .in_12(bullet_module_22_out_7), .out_13(task_drawer_22_out_13),
    .out_14(task_drawer_22_out_14), .out_15(task_drawer_22_out_15), .out_16(task_drawer_22_out_16),
    .in_1(bullet_module_22_working));
  task_drawer task_drawer_23 (
    .in_2(in_4), .clock32(clock32), .in_4(in_5), .y(bullet_module_23_y), .in_6(in_6), .in_7(in_7),
    .x(bullet_module_23_x), .in_9(bullet_module_23_out_4), .in_10(bullet_module_23_out_5),
    .in_11(bullet_module_23_out_6), .in_12(bullet_module_23_out_7), .out_13(task_drawer_23_out_13),
    .out_14(task_drawer_23_out_14), .out_15(task_drawer_23_out_15), .out_16(task_drawer_23_out_16),
    .in_1(bullet_module_23_working));
  task_drawer task_drawer_24 (
    .in_2(in_4), .clock32(clock32), .in_4(in_5), .y(bullet_module_24_y), .in_6(in_6), .in_7(in_7),
    .x(bullet_module_24_x), .in_9(bullet_module_24_out_4), .in_10(bullet_module_24_out_5),
    .in_11(bullet_module_24_out_6), .in_12(bullet_module_24_out_7), .out_13(task_drawer_24_out_13),
    .out_14(task_drawer_24_out_14), .out_15(task_drawer_24_out_15), .out_16(task_drawer_24_out_16),
    .in_1(bullet_module_24_working));
  task_drawer task_drawer_25 (
    .in_2(in_4), .clock32(clock32), .in_4(in_5), .y(bullet_module_25_y), .in_6(in_6), .in_7(in_7),
    .x(bullet_module_25_x), .in_9(bullet_module_25_out_4), .in_10(bullet_module_25_out_5),
    .in_11(bullet_module_25_out_6), .in_12(bullet_module_25_out_7), .out_13(task_drawer_25_out_13),
    .out_14(task_drawer_25_out_14), .out_15(task_drawer_25_out_15), .out_16(task_drawer_25_out_16),
    .in_1(bullet_module_25_working));
  task_drawer task_drawer_26 (
    .in_2(in_4), .clock32(clock32), .in_4(in_5), .y(bullet_module_26_y), .in_6(in_6), .in_7(in_7),
    .x(bullet_module_26_x), .in_9(bullet_module_26_out_4), .in_10(bullet_module_26_out_5),
    .in_11(bullet_module_26_out_6), .in_12(bullet_module_26_out_7), .out_13(task_drawer_26_out_13),
    .out_14(task_drawer_26_out_14), .out_15(task_drawer_26_out_15), .out_16(task_drawer_26_out_16),
    .in_1(bullet_module_26_working));
  task_drawer task_drawer_27 (
    .in_2(in_4), .clock32(clock32), .in_4(in_5), .y(bullet_module_27_y), .in_6(in_6), .in_7(in_7),
    .x(bullet_module_27_x), .in_9(bullet_module_27_out_4), .in_10(bullet_module_27_out_5),
    .in_11(bullet_module_27_out_6), .in_12(bullet_module_27_out_7), .out_13(task_drawer_27_out_13),
    .out_14(task_drawer_27_out_14), .out_15(task_drawer_27_out_15), .out_16(task_drawer_27_out_16),
    .in_1(bullet_module_27_working));
  task_drawer task_drawer_28 (
    .in_2(in_4), .clock32(clock32), .in_4(in_5), .y(bullet_module_28_y), .in_6(in_6), .in_7(in_7),
    .x(bullet_module_28_x), .in_9(bullet_module_28_out_4), .in_10(bullet_module_28_out_5),
    .in_11(bullet_module_28_out_6), .in_12(bullet_module_28_out_7), .out_13(task_drawer_28_out_13),
    .out_14(task_drawer_28_out_14), .out_15(task_drawer_28_out_15), .out_16(task_drawer_28_out_16),
    .in_1(bullet_module_28_working));
  task_drawer task_drawer_29 (
    .in_2(in_4), .clock32(clock32), .in_4(in_5), .y(bullet_module_29_y), .in_6(in_6), .in_7(in_7),
    .x(bullet_module_29_x), .in_9(bullet_module_29_out_4), .in_10(bullet_module_29_out_5),
    .in_11(bullet_module_29_out_6), .in_12(bullet_module_29_out_7), .out_13(task_drawer_29_out_13),
    .out_14(task_drawer_29_out_14), .out_15(task_drawer_29_out_15), .out_16(task_drawer_29_out_16),
    .in_1(bullet_module_29_working));
  task_drawer task_drawer_30 (
    .in_2(in_4), .clock32(clock32), .in_4(in_5), .y(bullet_module_30_y), .in_6(in_6), .in_7(in_7),
    .x(bullet_module_30_x), .in_9(bullet_module_30_out_4), .in_10(bullet_module_30_out_5),
    .in_11(bullet_module_30_out_6), .in_12(bullet_module_30_out_7), .out_13(task_drawer_30_out_13),
    .out_14(task_drawer_30_out_14), .out_15(task_drawer_30_out_15), .out_16(task_drawer_30_out_16),
    .in_1(bullet_module_30_working));
  task_drawer task_drawer_31 (
    .in_2(in_4), .clock32(clock32), .in_4(in_5), .y(bullet_module_31_y), .in_6(in_6), .in_7(in_7),
    .x(bullet_module_31_x), .in_9(bullet_module_31_out_4), .in_10(bullet_module_31_out_5),
    .in_11(bullet_module_31_out_6), .in_12(bullet_module_31_out_7), .out_13(task_drawer_31_out_13),
    .out_14(task_drawer_31_out_14), .out_15(task_drawer_31_out_15), .out_16(task_drawer_31_out_16),
    .in_1(bullet_module_31_working));
endmodule

module bullet_module (
  input  [31:0] \input ,
  input  [4:0] clock32,
  input  on,
  output [3:0] out_4,
  output [3:0] out_5,
  output [3:0] out_6,
  output [3:0] out_7,
  output [5:0] x,
  output [5:0] y,
  output working
);

  wire and_1_out, comparator_1_eq, comparator_1_gt, comparator_2_eq, comparator_2_gt,
       controlled_buffer_1_out, d_ff_1_q, d_ff_3_q, delay_1_out_2, multiplexer_6_out, multiplexer_8_out,
       not_1_out, or_1_out, or_2_out;
  wire [15:0] adder_1_out, adder_2_out, multiplexer_5_out, multiplexer_7_out, multiplexer_9_out,
       multiplexer_10_out, register_2_q, register_5_q, subtractor_1_out, subtractor_2_out;
  wire [31:0] register_1_q;

  // Probe on register_1_q
  Register #(.width(32)) register_1 (
    .D(\input ), .Q(register_1_q), .clk(on), .clr(controlled_buffer_1_out));  // open: en
  or or_1 (or_1_out, on, and_1_out);
  Multiplexer #(.select(2), .width(4), .enable("false")) multiplexer_1 (
    .in0(4'b0100), .in1(4'b0110), .in2(4'b0100), .in3(4'b0110), .out(out_4), .sel(register_1_q[1:0]));
  Multiplexer #(.select(2), .width(4), .enable("false")) multiplexer_2 (
    .in0(4'b1110), .in1(4'b1111), .in2(4'b1010), .in3(4'b1001), .out(out_5), .sel(register_1_q[1:0]));
  Multiplexer #(.select(2), .width(4), .enable("false")) multiplexer_3 (
    .in0(4'b0100), .in1(4'b1111), .in2(4'b0100), .in3(4'b1001), .out(out_6), .sel(register_1_q[1:0]));
  Multiplexer #(.select(2), .width(4), .enable("false")) multiplexer_4 (
    .in0(4'b0000), .in1(4'b0110), .in2(4'b0000), .in3(4'b0110), .out(out_7), .sel(register_1_q[1:0]));
  assign controlled_buffer_1_out = d_ff_3_q ? d_ff_3_q : 1'bz;  // Controlled_Buffer controlled_buffer_1
  D_Flip_Flop d_ff_1 (.clk(or_1_out), .D(on), .Q(d_ff_1_q));  // open: Qn, preset, en, reset
  delay delay_1 (.in_1(working), .out_2(delay_1_out_2));
  D_Flip_Flop d_ff_2 (.clk(on), .D(on), .Q(working), .reset(d_ff_3_q));  // open: Qn, preset, en
  // Probe on register_1_q[23:19]
  Multiplexer #(.width(16), .enable("false")) multiplexer_5 (
    .in0(multiplexer_9_out), .in1({register_1_q[7:2], {10{1'b0}}}), .out(multiplexer_5_out), .sel(d_ff_1_q));
  Multiplexer #(.enable("false")) multiplexer_6 (
    .in0(on), .in1(and_1_out), .out(multiplexer_6_out), .sel(delay_1_out_2));
  Multiplexer #(.width(16), .enable("false")) multiplexer_7 (
    .in0(multiplexer_10_out), .in1({register_1_q[13:8], {10{1'b0}}}), .out(multiplexer_7_out), .sel(d_ff_1_q));
  Multiplexer #(.enable("false")) multiplexer_8 (
    .in0(on), .in1(and_1_out), .out(multiplexer_8_out), .sel(delay_1_out_2));
  and and_1 (and_1_out, ~clock32[0], ~clock32[1], ~clock32[2], ~clock32[3], ~clock32[4]);  // AND_Gate
  Subtractor #(.width(16)) subtractor_1 (
    .a(register_2_q), .b({{5{1'b0}}, register_1_q[17:14], {7{1'b0}}}), .out(subtractor_1_out));  // open: bin, bout
  Adder #(.width(16)) adder_1 (
    .a(register_2_q), .b({{5{1'b0}}, register_1_q[17:14], {7{1'b0}}}), .out(adder_1_out));  // open: cin, cout
  Multiplexer #(.width(16), .enable("false")) multiplexer_9 (
    .in0(adder_1_out), .in1(subtractor_1_out), .out(multiplexer_9_out), .sel(register_1_q[18]));
  Register #(.width(16)) register_2 (
    .D(multiplexer_5_out), .Q(register_2_q), .clk(multiplexer_6_out));  // open: en, clr
  Register #(.width(6)) register_3 (.D(register_2_q[15:10]), .Q(x), .clk(and_1_out));  // open: en, clr
  Subtractor #(.width(16)) subtractor_2 (
    .a(register_5_q), .b({{5{1'b0}}, register_1_q[22:19], {7{1'b0}}}), .out(subtractor_2_out));  // open: bin, bout
  Adder #(.width(16)) adder_2 (
    .a(register_5_q), .b({{5{1'b0}}, register_1_q[22:19], {7{1'b0}}}), .out(adder_2_out));  // open: cin, cout
  Multiplexer #(.width(16), .enable("false")) multiplexer_10 (
    .in0(adder_2_out), .in1(subtractor_2_out), .out(multiplexer_10_out), .sel(register_1_q[23]));
  Register #(.width(6)) register_4 (.D(register_5_q[15:10]), .Q(y), .clk(and_1_out));  // open: en, clr
  Register #(.width(16)) register_5 (
    .D(multiplexer_7_out), .Q(register_5_q), .clk(multiplexer_8_out));  // open: en, clr
  Comparator #(.width(6), .mode("unsigned")) comparator_1 (
    .a(x), .b(6'b111110), .gt(comparator_1_gt), .eq(comparator_1_eq));  // open: lt
  Comparator #(.width(6), .mode("unsigned")) comparator_2 (
    .a(y), .b(6'b111110), .gt(comparator_2_gt), .eq(comparator_2_eq));  // open: lt
  or or_2 (or_2_out, comparator_1_gt, comparator_1_eq, comparator_2_gt, comparator_2_eq);
  D_Flip_Flop d_ff_3 (
    .clk(or_2_out), .D(or_2_out), .Q(d_ff_3_q), .en(not_1_out), .reset(d_ff_3_q));  // open: Qn, preset
  not not_1 (not_1_out, on);
endmodule

module delay (
  input  in_1,
  output out_2
);

  wire buffer_1_out, buffer_2_out, buffer_3_out, buffer_4_out, buffer_5_out, buffer_6_out, buffer_7_out;

  buf buffer_1 (buffer_1_out, in_1);
  buf buffer_2 (buffer_2_out, buffer_3_out);
  buf buffer_3 (buffer_3_out, buffer_1_out);
  buf buffer_4 (buffer_4_out, buffer_2_out);
  buf buffer_5 (buffer_5_out, buffer_7_out);
  buf buffer_6 (buffer_6_out, buffer_4_out);
  buf buffer_7 (buffer_7_out, buffer_6_out);
  buf buffer_8 (out_2, buffer_5_out);
endmodule

module buffer2_0 (
  input  [4:0] clock32,
  input  [31:0] in_2,
  output [31:0] out_3,
  output [31:0] out_4,
  output [31:0] out_5,
  output [31:0] out_6,
  output [31:0] out_7,
  output [31:0] out_8,
  output [31:0] out_9,
  output [31:0] out_10,
  output [31:0] out_11,
  output [31:0] out_12,
  output [31:0] out_13,
  output [31:0] out_14,
  output [31:0] out_15,
  output [31:0] out_16,
  output [31:0] out_17,
  output [31:0] out_18,
  output [31:0] out_19,
  output [31:0] out_20,
  output [31:0] out_21,
  output [31:0] out_22,
  output [31:0] out_23,
  output [31:0] out_24,
  output [31:0] out_25,
  output [31:0] out_26,
  output [31:0] out_27,
  output [31:0] out_28,
  output [31:0] out_29,
  output [31:0] out_30,
  output [31:0] out_31,
  output [31:0] out_32,
  output [31:0] out_33,
  output [31:0] out_34
);

  wire and_1_out, buffer_1_out, buffer_2_out, buffer_3_out, buffer_4_out, buffer_5_out, buffer_6_out,
       buffer_7_out, buffer_8_out, buffer_9_out, buffer_10_out, buffer_11_out, buffer_12_out, buffer_13_out,
       buffer_14_out, buffer_15_out, buffer_16_out, buffer_17_out, buffer_18_out, buffer_19_out,
       buffer_20_out, buffer_21_out, buffer_22_out, buffer_23_out, buffer_24_out, buffer_25_out,
       buffer_26_out, buffer_27_out, buffer_28_out, buffer_29_out, buffer_30_out, buffer_31_out,
       buffer_32_out, decoder_1_out0, decoder_1_out1, decoder_1_out2, decoder_1_out3, decoder_1_out4,
       decoder_1_out5, decoder_1_out6, decoder_1_out7, decoder_1_out8, decoder_1_out9, decoder_1_out10,
       decoder_1_out11, decoder_1_out12, decoder_1_out13, decoder_1_out14, decoder_1_out15, decoder_1_out16,
       decoder_1_out17, decoder_1_out18, decoder_1_out19, decoder_1_out20, decoder_1_out21, decoder_1_out22,
       decoder_1_out23, decoder_1_out24, decoder_1_out25, decoder_1_out26, decoder_1_out27, decoder_1_out28,
       decoder_1_out29, decoder_1_out30, decoder_1_out31, delay_1_out_2;
  wire [31:0] register_1_q, register_2_q, register_3_q, register_4_q, register_5_q, register_6_q,
       register_7_q, register_8_q, register_9_q, register_10_q, register_11_q, register_12_q, register_13_q,
       register_14_q, register_15_q, register_16_q, register_17_q, register_18_q, register_19_q,
       register_20_q, register_21_q, register_22_q, register_23_q, register_24_q, register_25_q,
       register_26_q, register_27_q, register_28_q, register_29_q, register_30_q, register_31_q,
       register_32_q;

  Decoder #(.select(5), .enable("false")) decoder_1 (
    .out0(decoder_1_out0), .out1(decoder_1_out1), .out2(decoder_1_out2), .out3(decoder_1_out3),
    .out4(decoder_1_out4), .out5(decoder_1_out5), .out6(decoder_1_out6), .out7(decoder_1_out7),
    .out8(decoder_1_out8), .out9(decoder_1_out9), .out10(decoder_1_out10), .out11(decoder_1_out11),
    .out12(decoder_1_out12), .out13(decoder_1_out13), .out14(decoder_1_out14), .out15(decoder_1_out15),
    .out16(decoder_1_out16), .out17(decoder_1_out17), .out18(decoder_1_out18), .out19(decoder_1_out19),
    .out20(decoder_1_out20), .out21(decoder_1_out21), .out22(decoder_1_out22), .out23(decoder_1_out23),
    .out24(decoder_1_out24), .out25(decoder_1_out25), .out26(decoder_1_out26), .out27(decoder_1_out27),
    .out28(decoder_1_out28), .out29(decoder_1_out29), .out30(decoder_1_out30), .out31(decoder_1_out31),
    .sel(clock32));
  and and_1 (and_1_out, ~clock32[0], ~clock32[1], ~clock32[2], ~clock32[3], ~clock32[4]);  // AND_Gate
  delay delay_1 (.in_1(and_1_out), .out_2(delay_1_out_2));
  Register #(.width(32), .trigger("falling")) register_1 (
    .D(in_2), .en(buffer_1_out), .Q(register_1_q), .clk(decoder_1_out31));  // open: clr
  buf buffer_1 (buffer_1_out, decoder_1_out31);
  Register #(.width(32), .trigger("falling")) register_2 (
    .D(in_2), .en(buffer_2_out), .Q(register_2_q), .clk(decoder_1_out30));  // open: clr
  buf buffer_2 (buffer_2_out, decoder_1_out30);
  Register #(.width(32), .trigger("falling")) register_3 (
    .D(in_2), .en(buffer_3_out), .Q(register_3_q), .clk(decoder_1_out29));  // open: clr
  buf buffer_3 (buffer_3_out, decoder_1_out29);
  Register #(.width(32), .trigger("falling")) register_4 (
    .D(in_2), .en(buffer_4_out), .Q(register_4_q), .clk(decoder_1_out28));  // open: clr
  buf buffer_4 (buffer_4_out, decoder_1_out28);
  Register #(.width(32), .trigger("falling")) register_5 (
    .D(in_2), .en(buffer_5_out), .Q(register_5_q), .clk(decoder_1_out27));  // open: clr
  buf buffer_5 (buffer_5_out, decoder_1_out27);
  Register #(.width(32), .trigger("falling")) register_6 (
    .D(in_2), .en(buffer_6_out), .Q(register_6_q), .clk(decoder_1_out26));  // open: clr
  buf buffer_6 (buffer_6_out, decoder_1_out26);
  Register #(.width(32), .trigger("falling")) register_7 (
    .D(in_2), .en(buffer_7_out), .Q(register_7_q), .clk(decoder_1_out25));  // open: clr
  buf buffer_7 (buffer_7_out, decoder_1_out25);
  Register #(.width(32), .trigger("falling")) register_8 (
    .D(in_2), .en(buffer_8_out), .Q(register_8_q), .clk(decoder_1_out24));  // open: clr
  buf buffer_8 (buffer_8_out, decoder_1_out24);
  Register #(.width(32), .trigger("falling")) register_9 (
    .D(in_2), .en(buffer_9_out), .Q(register_9_q), .clk(decoder_1_out23));  // open: clr
  buf buffer_9 (buffer_9_out, decoder_1_out23);
  Register #(.width(32), .trigger("falling")) register_10 (
    .D(in_2), .en(buffer_10_out), .Q(register_10_q), .clk(decoder_1_out22));  // open: clr
  buf buffer_10 (buffer_10_out, decoder_1_out22);
  Register #(.width(32), .trigger("falling")) register_11 (
    .D(in_2), .en(buffer_11_out), .Q(register_11_q), .clk(decoder_1_out21));  // open: clr
  buf buffer_11 (buffer_11_out, decoder_1_out21);
  Register #(.width(32), .trigger("falling")) register_12 (
    .D(in_2), .en(buffer_12_out), .Q(register_12_q), .clk(decoder_1_out20));  // open: clr
  buf buffer_12 (buffer_12_out, decoder_1_out20);
  Register #(.width(32), .trigger("falling")) register_13 (
    .D(in_2), .en(buffer_13_out), .Q(register_13_q), .clk(decoder_1_out19));  // open: clr
  buf buffer_13 (buffer_13_out, decoder_1_out19);
  Register #(.width(32), .trigger("falling")) register_14 (
    .D(in_2), .en(buffer_14_out), .Q(register_14_q), .clk(decoder_1_out18));  // open: clr
  buf buffer_14 (buffer_14_out, decoder_1_out18);
  Register #(.width(32), .trigger("falling")) register_15 (
    .D(in_2), .en(buffer_15_out), .Q(register_15_q), .clk(decoder_1_out17));  // open: clr
  buf buffer_15 (buffer_15_out, decoder_1_out17);
  Register #(.width(32), .trigger("falling")) register_16 (
    .D(in_2), .en(buffer_16_out), .Q(register_16_q), .clk(decoder_1_out16));  // open: clr
  buf buffer_16 (buffer_16_out, decoder_1_out16);
  Register #(.width(32), .trigger("falling")) register_17 (
    .D(in_2), .en(buffer_17_out), .Q(register_17_q), .clk(decoder_1_out15));  // open: clr
  buf buffer_17 (buffer_17_out, decoder_1_out15);
  Register #(.width(32), .trigger("falling")) register_18 (
    .D(in_2), .en(buffer_18_out), .Q(register_18_q), .clk(decoder_1_out14));  // open: clr
  buf buffer_18 (buffer_18_out, decoder_1_out14);
  Register #(.width(32), .trigger("falling")) register_19 (
    .D(in_2), .en(buffer_19_out), .Q(register_19_q), .clk(decoder_1_out13));  // open: clr
  buf buffer_19 (buffer_19_out, decoder_1_out13);
  Register #(.width(32), .trigger("falling")) register_20 (
    .D(in_2), .en(buffer_20_out), .Q(register_20_q), .clk(decoder_1_out12));  // open: clr
  buf buffer_20 (buffer_20_out, decoder_1_out12);
  Register #(.width(32), .trigger("falling")) register_21 (
    .D(in_2), .en(buffer_21_out), .Q(register_21_q), .clk(decoder_1_out11));  // open: clr
  buf buffer_21 (buffer_21_out, decoder_1_out11);
  Register #(.width(32), .trigger("falling")) register_22 (
    .D(in_2), .en(buffer_22_out), .Q(register_22_q), .clk(decoder_1_out10));  // open: clr
  buf buffer_22 (buffer_22_out, decoder_1_out10);
  Register #(.width(32), .trigger("falling")) register_23 (
    .D(in_2), .en(buffer_23_out), .Q(register_23_q), .clk(decoder_1_out9));  // open: clr
  buf buffer_23 (buffer_23_out, decoder_1_out9);
  Register #(.width(32), .trigger("falling")) register_24 (
    .D(in_2), .en(buffer_24_out), .Q(register_24_q), .clk(decoder_1_out8));  // open: clr
  buf buffer_24 (buffer_24_out, decoder_1_out8);
  Register #(.width(32), .trigger("falling")) register_25 (
    .D(in_2), .en(buffer_25_out), .Q(register_25_q), .clk(decoder_1_out7));  // open: clr
  buf buffer_25 (buffer_25_out, decoder_1_out7);
  Register #(.width(32), .trigger("falling")) register_26 (
    .D(in_2), .en(buffer_26_out), .Q(register_26_q), .clk(decoder_1_out6));  // open: clr
  buf buffer_26 (buffer_26_out, decoder_1_out6);
  Register #(.width(32), .trigger("falling")) register_27 (
    .D(in_2), .en(buffer_27_out), .Q(register_27_q), .clk(decoder_1_out5));  // open: clr
  buf buffer_27 (buffer_27_out, decoder_1_out5);
  Register #(.width(32), .trigger("falling")) register_28 (
    .D(in_2), .en(buffer_28_out), .Q(register_28_q), .clk(decoder_1_out4));  // open: clr
  buf buffer_28 (buffer_28_out, decoder_1_out4);
  Register #(.width(32), .trigger("falling")) register_29 (
    .D(in_2), .en(buffer_29_out), .Q(register_29_q), .clk(decoder_1_out3));  // open: clr
  buf buffer_29 (buffer_29_out, decoder_1_out3);
  Register #(.width(32), .trigger("falling")) register_30 (
    .D(in_2), .en(buffer_30_out), .Q(register_30_q), .clk(decoder_1_out2));  // open: clr
  buf buffer_30 (buffer_30_out, decoder_1_out2);
  Register #(.width(32), .trigger("falling")) register_31 (
    .D(in_2), .en(buffer_31_out), .Q(register_31_q), .clk(decoder_1_out1));  // open: clr
  buf buffer_31 (buffer_31_out, decoder_1_out1);
  Register #(.width(32), .trigger("falling")) register_32 (
    .D(in_2), .en(buffer_32_out), .Q(register_32_q), .clk(decoder_1_out0));  // open: clr
  buf buffer_32 (buffer_32_out, decoder_1_out0);
  assign out_3 = delay_1_out_2 ? register_1_q : 32'bz;  // Controlled_Buffer controlled_buffer_1
  Pull_Resistor pull_resistor_1 (.node(out_3));
  Pull_Resistor pull_resistor_2 (.node(out_4));
  assign out_4 = delay_1_out_2 ? register_2_q : 32'bz;  // Controlled_Buffer controlled_buffer_2
  assign out_5 = delay_1_out_2 ? register_3_q : 32'bz;  // Controlled_Buffer controlled_buffer_3
  Pull_Resistor pull_resistor_3 (.node(out_5));
  Pull_Resistor pull_resistor_4 (.node(out_6));
  assign out_6 = delay_1_out_2 ? register_4_q : 32'bz;  // Controlled_Buffer controlled_buffer_4
  Pull_Resistor pull_resistor_5 (.node(out_7));
  assign out_7 = delay_1_out_2 ? register_5_q : 32'bz;  // Controlled_Buffer controlled_buffer_5
  Pull_Resistor pull_resistor_6 (.node(out_8));
  assign out_8 = delay_1_out_2 ? register_6_q : 32'bz;  // Controlled_Buffer controlled_buffer_6
  assign out_9 = delay_1_out_2 ? register_7_q : 32'bz;  // Controlled_Buffer controlled_buffer_7
  Pull_Resistor pull_resistor_7 (.node(out_9));
  assign out_10 = delay_1_out_2 ? register_8_q : 32'bz;  // Controlled_Buffer controlled_buffer_8
  Pull_Resistor pull_resistor_8 (.node(out_10));
  Pull_Resistor pull_resistor_9 (.node(out_11));
  assign out_11 = delay_1_out_2 ? register_9_q : 32'bz;  // Controlled_Buffer controlled_buffer_9
  Pull_Resistor pull_resistor_10 (.node(out_12));
  assign out_12 = delay_1_out_2 ? register_10_q : 32'bz;  // Controlled_Buffer controlled_buffer_10
  Pull_Resistor pull_resistor_11 (.node(out_13));
  assign out_13 = delay_1_out_2 ? register_11_q : 32'bz;  // Controlled_Buffer controlled_buffer_11
  Pull_Resistor pull_resistor_12 (.node(out_14));
  assign out_14 = delay_1_out_2 ? register_12_q : 32'bz;  // Controlled_Buffer controlled_buffer_12
  assign out_15 = delay_1_out_2 ? register_13_q : 32'bz;  // Controlled_Buffer controlled_buffer_13
  Pull_Resistor pull_resistor_13 (.node(out_15));
  assign out_16 = delay_1_out_2 ? register_14_q : 32'bz;  // Controlled_Buffer controlled_buffer_14
  Pull_Resistor pull_resistor_14 (.node(out_16));
  Pull_Resistor pull_resistor_15 (.node(out_17));
  assign out_17 = delay_1_out_2 ? register_15_q : 32'bz;  // Controlled_Buffer controlled_buffer_15
  Pull_Resistor pull_resistor_16 (.node(out_18));
  assign out_18 = delay_1_out_2 ? register_16_q : 32'bz;  // Controlled_Buffer controlled_buffer_16
  assign out_19 = delay_1_out_2 ? register_17_q : 32'bz;  // Controlled_Buffer controlled_buffer_17
  Pull_Resistor pull_resistor_17 (.node(out_19));
  Pull_Resistor pull_resistor_18 (.node(out_20));
  assign out_20 = delay_1_out_2 ? register_18_q : 32'bz;  // Controlled_Buffer controlled_buffer_18
  assign out_21 = delay_1_out_2 ? register_19_q : 32'bz;  // Controlled_Buffer controlled_buffer_19
  Pull_Resistor pull_resistor_19 (.node(out_21));
  Pull_Resistor pull_resistor_20 (.node(out_22));
  assign out_22 = delay_1_out_2 ? register_20_q : 32'bz;  // Controlled_Buffer controlled_buffer_20
  Pull_Resistor pull_resistor_21 (.node(out_23));
  assign out_23 = delay_1_out_2 ? register_21_q : 32'bz;  // Controlled_Buffer controlled_buffer_21
  assign out_24 = delay_1_out_2 ? register_22_q : 32'bz;  // Controlled_Buffer controlled_buffer_22
  Pull_Resistor pull_resistor_22 (.node(out_24));
  assign out_25 = delay_1_out_2 ? register_23_q : 32'bz;  // Controlled_Buffer controlled_buffer_23
  Pull_Resistor pull_resistor_23 (.node(out_25));
  assign out_26 = delay_1_out_2 ? register_24_q : 32'bz;  // Controlled_Buffer controlled_buffer_24
  Pull_Resistor pull_resistor_24 (.node(out_26));
  assign out_27 = delay_1_out_2 ? register_25_q : 32'bz;  // Controlled_Buffer controlled_buffer_25
  Pull_Resistor pull_resistor_25 (.node(out_27));
  assign out_28 = delay_1_out_2 ? register_26_q : 32'bz;  // Controlled_Buffer controlled_buffer_26
  Pull_Resistor pull_resistor_26 (.node(out_28));
  assign out_29 = delay_1_out_2 ? register_27_q : 32'bz;  // Controlled_Buffer controlled_buffer_27
  Pull_Resistor pull_resistor_27 (.node(out_29));
  Pull_Resistor pull_resistor_28 (.node(out_30));
  assign out_30 = delay_1_out_2 ? register_28_q : 32'bz;  // Controlled_Buffer controlled_buffer_28
  Pull_Resistor pull_resistor_29 (.node(out_31));
  assign out_31 = delay_1_out_2 ? register_29_q : 32'bz;  // Controlled_Buffer controlled_buffer_29
  Pull_Resistor pull_resistor_30 (.node(out_32));
  assign out_32 = delay_1_out_2 ? register_30_q : 32'bz;  // Controlled_Buffer controlled_buffer_30
  assign out_33 = delay_1_out_2 ? register_31_q : 32'bz;  // Controlled_Buffer controlled_buffer_31
  Pull_Resistor pull_resistor_31 (.node(out_33));
  assign out_34 = delay_1_out_2 ? register_32_q : 32'bz;  // Controlled_Buffer controlled_buffer_32
  Pull_Resistor pull_resistor_32 (.node(out_34));
endmodule

module buffer2_0_mirr (
  input  [4:0] clock32,
  input  [31:0] in_2,
  output [31:0] out_3,
  output [31:0] out_4,
  output [31:0] out_5,
  output [31:0] out_6,
  output [31:0] out_7,
  output [31:0] out_8,
  output [31:0] out_9,
  output [31:0] out_10,
  output [31:0] out_11,
  output [31:0] out_12,
  output [31:0] out_13,
  output [31:0] out_14,
  output [31:0] out_15,
  output [31:0] out_16,
  output [31:0] out_17,
  output [31:0] out_18,
  output [31:0] out_19,
  output [31:0] out_20,
  output [31:0] out_21,
  output [31:0] out_22,
  output [31:0] out_23,
  output [31:0] out_24,
  output [31:0] out_25,
  output [31:0] out_26,
  output [31:0] out_27,
  output [31:0] out_28,
  output [31:0] out_29,
  output [31:0] out_30,
  output [31:0] out_31,
  output [31:0] out_32,
  output [31:0] out_33,
  output [31:0] out_34
);

  wire and_1_out, buffer_1_out, buffer_2_out, buffer_3_out, buffer_4_out, buffer_5_out, buffer_6_out,
       buffer_7_out, buffer_8_out, buffer_9_out, buffer_10_out, buffer_11_out, buffer_12_out, buffer_13_out,
       buffer_14_out, buffer_15_out, buffer_16_out, buffer_17_out, buffer_18_out, buffer_19_out,
       buffer_20_out, buffer_21_out, buffer_22_out, buffer_23_out, buffer_24_out, buffer_25_out,
       buffer_26_out, buffer_27_out, buffer_28_out, buffer_29_out, buffer_30_out, buffer_31_out,
       buffer_32_out, decoder_1_out0, decoder_1_out1, decoder_1_out2, decoder_1_out3, decoder_1_out4,
       decoder_1_out5, decoder_1_out6, decoder_1_out7, decoder_1_out8, decoder_1_out9, decoder_1_out10,
       decoder_1_out11, decoder_1_out12, decoder_1_out13, decoder_1_out14, decoder_1_out15, decoder_1_out16,
       decoder_1_out17, decoder_1_out18, decoder_1_out19, decoder_1_out20, decoder_1_out21, decoder_1_out22,
       decoder_1_out23, decoder_1_out24, decoder_1_out25, decoder_1_out26, decoder_1_out27, decoder_1_out28,
       decoder_1_out29, decoder_1_out30, decoder_1_out31, delay_1_out_2;
  wire [31:0] register_1_q, register_2_q, register_3_q, register_4_q, register_5_q, register_6_q,
       register_7_q, register_8_q, register_9_q, register_10_q, register_11_q, register_12_q, register_13_q,
       register_14_q, register_15_q, register_16_q, register_17_q, register_18_q, register_19_q,
       register_20_q, register_21_q, register_22_q, register_23_q, register_24_q, register_25_q,
       register_26_q, register_27_q, register_28_q, register_29_q, register_30_q, register_31_q,
       register_32_q;

  Decoder #(.select(5), .enable("false")) decoder_1 (
    .out0(decoder_1_out0), .out1(decoder_1_out1), .out2(decoder_1_out2), .out3(decoder_1_out3),
    .out4(decoder_1_out4), .out5(decoder_1_out5), .out6(decoder_1_out6), .out7(decoder_1_out7),
    .out8(decoder_1_out8), .out9(decoder_1_out9), .out10(decoder_1_out10), .out11(decoder_1_out11),
    .out12(decoder_1_out12), .out13(decoder_1_out13), .out14(decoder_1_out14), .out15(decoder_1_out15),
    .out16(decoder_1_out16), .out17(decoder_1_out17), .out18(decoder_1_out18), .out19(decoder_1_out19),
    .out20(decoder_1_out20), .out21(decoder_1_out21), .out22(decoder_1_out22), .out23(decoder_1_out23),
    .out24(decoder_1_out24), .out25(decoder_1_out25), .out26(decoder_1_out26), .out27(decoder_1_out27),
    .out28(decoder_1_out28), .out29(decoder_1_out29), .out30(decoder_1_out30), .out31(decoder_1_out31),
    .sel(clock32));
  and and_1 (and_1_out, ~clock32[0], ~clock32[1], ~clock32[2], ~clock32[3], ~clock32[4]);  // AND_Gate
  delay delay_1 (.in_1(and_1_out), .out_2(delay_1_out_2));
  Register #(.width(32), .trigger("falling")) register_1 (
    .D(in_2), .en(buffer_1_out), .Q(register_1_q), .clk(decoder_1_out31));  // open: clr
  buf buffer_1 (buffer_1_out, decoder_1_out31);
  Register #(.width(32), .trigger("falling")) register_2 (
    .D(in_2), .en(buffer_2_out), .Q(register_2_q), .clk(decoder_1_out30));  // open: clr
  buf buffer_2 (buffer_2_out, decoder_1_out30);
  Register #(.width(32), .trigger("falling")) register_3 (
    .D(in_2), .en(buffer_3_out), .Q(register_3_q), .clk(decoder_1_out29));  // open: clr
  buf buffer_3 (buffer_3_out, decoder_1_out29);
  Register #(.width(32), .trigger("falling")) register_4 (
    .D(in_2), .en(buffer_4_out), .Q(register_4_q), .clk(decoder_1_out28));  // open: clr
  buf buffer_4 (buffer_4_out, decoder_1_out28);
  Register #(.width(32), .trigger("falling")) register_5 (
    .D(in_2), .en(buffer_5_out), .Q(register_5_q), .clk(decoder_1_out27));  // open: clr
  buf buffer_5 (buffer_5_out, decoder_1_out27);
  Register #(.width(32), .trigger("falling")) register_6 (
    .D(in_2), .en(buffer_6_out), .Q(register_6_q), .clk(decoder_1_out26));  // open: clr
  buf buffer_6 (buffer_6_out, decoder_1_out26);
  Register #(.width(32), .trigger("falling")) register_7 (
    .D(in_2), .en(buffer_7_out), .Q(register_7_q), .clk(decoder_1_out25));  // open: clr
  buf buffer_7 (buffer_7_out, decoder_1_out25);
  Register #(.width(32), .trigger("falling")) register_8 (
    .D(in_2), .en(buffer_8_out), .Q(register_8_q), .clk(decoder_1_out24));  // open: clr
  buf buffer_8 (buffer_8_out, decoder_1_out24);
  Register #(.width(32), .trigger("falling")) register_9 (
    .D(in_2), .en(buffer_9_out), .Q(register_9_q), .clk(decoder_1_out23));  // open: clr
  buf buffer_9 (buffer_9_out, decoder_1_out23);
  Register #(.width(32), .trigger("falling")) register_10 (
    .D(in_2), .en(buffer_10_out), .Q(register_10_q), .clk(decoder_1_out22));  // open: clr
  buf buffer_10 (buffer_10_out, decoder_1_out22);
  Register #(.width(32), .trigger("falling")) register_11 (
    .D(in_2), .en(buffer_11_out), .Q(register_11_q), .clk(decoder_1_out21));  // open: clr
  buf buffer_11 (buffer_11_out, decoder_1_out21);
  Register #(.width(32), .trigger("falling")) register_12 (
    .D(in_2), .en(buffer_12_out), .Q(register_12_q), .clk(decoder_1_out20));  // open: clr
  buf buffer_12 (buffer_12_out, decoder_1_out20);
  Register #(.width(32), .trigger("falling")) register_13 (
    .D(in_2), .en(buffer_13_out), .Q(register_13_q), .clk(decoder_1_out19));  // open: clr
  buf buffer_13 (buffer_13_out, decoder_1_out19);
  Register #(.width(32), .trigger("falling")) register_14 (
    .D(in_2), .en(buffer_14_out), .Q(register_14_q), .clk(decoder_1_out18));  // open: clr
  buf buffer_14 (buffer_14_out, decoder_1_out18);
  Register #(.width(32), .trigger("falling")) register_15 (
    .D(in_2), .en(buffer_15_out), .Q(register_15_q), .clk(decoder_1_out17));  // open: clr
  buf buffer_15 (buffer_15_out, decoder_1_out17);
  Register #(.width(32), .trigger("falling")) register_16 (
    .D(in_2), .en(buffer_16_out), .Q(register_16_q), .clk(decoder_1_out16));  // open: clr
  buf buffer_16 (buffer_16_out, decoder_1_out16);
  Register #(.width(32), .trigger("falling")) register_17 (
    .D(in_2), .en(buffer_17_out), .Q(register_17_q), .clk(decoder_1_out15));  // open: clr
  buf buffer_17 (buffer_17_out, decoder_1_out15);
  Register #(.width(32), .trigger("falling")) register_18 (
    .D(in_2), .en(buffer_18_out), .Q(register_18_q), .clk(decoder_1_out14));  // open: clr
  buf buffer_18 (buffer_18_out, decoder_1_out14);
  Register #(.width(32), .trigger("falling")) register_19 (
    .D(in_2), .en(buffer_19_out), .Q(register_19_q), .clk(decoder_1_out13));  // open: clr
  buf buffer_19 (buffer_19_out, decoder_1_out13);
  Register #(.width(32), .trigger("falling")) register_20 (
    .D(in_2), .en(buffer_20_out), .Q(register_20_q), .clk(decoder_1_out12));  // open: clr
  buf buffer_20 (buffer_20_out, decoder_1_out12);
  Register #(.width(32), .trigger("falling")) register_21 (
    .D(in_2), .en(buffer_21_out), .Q(register_21_q), .clk(decoder_1_out11));  // open: clr
  buf buffer_21 (buffer_21_out, decoder_1_out11);
  Register #(.width(32), .trigger("falling")) register_22 (
    .D(in_2), .en(buffer_22_out), .Q(register_22_q), .clk(decoder_1_out10));  // open: clr
  buf buffer_22 (buffer_22_out, decoder_1_out10);
  Register #(.width(32), .trigger("falling")) register_23 (
    .D(in_2), .en(buffer_23_out), .Q(register_23_q), .clk(decoder_1_out9));  // open: clr
  buf buffer_23 (buffer_23_out, decoder_1_out9);
  Register #(.width(32), .trigger("falling")) register_24 (
    .D(in_2), .en(buffer_24_out), .Q(register_24_q), .clk(decoder_1_out8));  // open: clr
  buf buffer_24 (buffer_24_out, decoder_1_out8);
  Register #(.width(32), .trigger("falling")) register_25 (
    .D(in_2), .en(buffer_25_out), .Q(register_25_q), .clk(decoder_1_out7));  // open: clr
  buf buffer_25 (buffer_25_out, decoder_1_out7);
  Register #(.width(32), .trigger("falling")) register_26 (
    .D(in_2), .en(buffer_26_out), .Q(register_26_q), .clk(decoder_1_out6));  // open: clr
  buf buffer_26 (buffer_26_out, decoder_1_out6);
  Register #(.width(32), .trigger("falling")) register_27 (
    .D(in_2), .en(buffer_27_out), .Q(register_27_q), .clk(decoder_1_out5));  // open: clr
  buf buffer_27 (buffer_27_out, decoder_1_out5);
  Register #(.width(32), .trigger("falling")) register_28 (
    .D(in_2), .en(buffer_28_out), .Q(register_28_q), .clk(decoder_1_out4));  // open: clr
  buf buffer_28 (buffer_28_out, decoder_1_out4);
  Register #(.width(32), .trigger("falling")) register_29 (
    .D(in_2), .en(buffer_29_out), .Q(register_29_q), .clk(decoder_1_out3));  // open: clr
  buf buffer_29 (buffer_29_out, decoder_1_out3);
  Register #(.width(32), .trigger("falling")) register_30 (
    .D(in_2), .en(buffer_30_out), .Q(register_30_q), .clk(decoder_1_out2));  // open: clr
  buf buffer_30 (buffer_30_out, decoder_1_out2);
  Register #(.width(32), .trigger("falling")) register_31 (
    .D(in_2), .en(buffer_31_out), .Q(register_31_q), .clk(decoder_1_out1));  // open: clr
  buf buffer_31 (buffer_31_out, decoder_1_out1);
  Register #(.width(32), .trigger("falling")) register_32 (
    .D(in_2), .en(buffer_32_out), .Q(register_32_q), .clk(decoder_1_out0));  // open: clr
  buf buffer_32 (buffer_32_out, decoder_1_out0);
  assign out_3 = delay_1_out_2 ? register_1_q : 32'bz;  // Controlled_Buffer controlled_buffer_1
  Pull_Resistor pull_resistor_1 (.node(out_3));
  Pull_Resistor pull_resistor_2 (.node(out_4));
  assign out_4 = delay_1_out_2 ? register_2_q : 32'bz;  // Controlled_Buffer controlled_buffer_2
  Pull_Resistor pull_resistor_3 (.node(out_5));
  assign out_5 = delay_1_out_2 ? register_3_q : 32'bz;  // Controlled_Buffer controlled_buffer_3
  assign out_6 = delay_1_out_2 ? register_4_q : 32'bz;  // Controlled_Buffer controlled_buffer_4
  Pull_Resistor pull_resistor_4 (.node(out_6));
  Pull_Resistor pull_resistor_5 (.node(out_7));
  assign out_7 = delay_1_out_2 ? register_5_q : 32'bz;  // Controlled_Buffer controlled_buffer_5
  assign out_8 = delay_1_out_2 ? register_6_q : 32'bz;  // Controlled_Buffer controlled_buffer_6
  Pull_Resistor pull_resistor_6 (.node(out_8));
  Pull_Resistor pull_resistor_7 (.node(out_9));
  assign out_9 = delay_1_out_2 ? register_7_q : 32'bz;  // Controlled_Buffer controlled_buffer_7
  Pull_Resistor pull_resistor_8 (.node(out_10));
  assign out_10 = delay_1_out_2 ? register_8_q : 32'bz;  // Controlled_Buffer controlled_buffer_8
  Pull_Resistor pull_resistor_9 (.node(out_11));
  assign out_11 = delay_1_out_2 ? register_9_q : 32'bz;  // Controlled_Buffer controlled_buffer_9
  Pull_Resistor pull_resistor_10 (.node(out_12));
  assign out_12 = delay_1_out_2 ? register_10_q : 32'bz;  // Controlled_Buffer controlled_buffer_10
  Pull_Resistor pull_resistor_11 (.node(out_13));
  assign out_13 = delay_1_out_2 ? register_11_q : 32'bz;  // Controlled_Buffer controlled_buffer_11
  Pull_Resistor pull_resistor_12 (.node(out_14));
  assign out_14 = delay_1_out_2 ? register_12_q : 32'bz;  // Controlled_Buffer controlled_buffer_12
  Pull_Resistor pull_resistor_13 (.node(out_15));
  assign out_15 = delay_1_out_2 ? register_13_q : 32'bz;  // Controlled_Buffer controlled_buffer_13
  assign out_16 = delay_1_out_2 ? register_14_q : 32'bz;  // Controlled_Buffer controlled_buffer_14
  Pull_Resistor pull_resistor_14 (.node(out_16));
  assign out_17 = delay_1_out_2 ? register_15_q : 32'bz;  // Controlled_Buffer controlled_buffer_15
  Pull_Resistor pull_resistor_15 (.node(out_17));
  Pull_Resistor pull_resistor_16 (.node(out_18));
  assign out_18 = delay_1_out_2 ? register_16_q : 32'bz;  // Controlled_Buffer controlled_buffer_16
  assign out_19 = delay_1_out_2 ? register_17_q : 32'bz;  // Controlled_Buffer controlled_buffer_17
  Pull_Resistor pull_resistor_17 (.node(out_19));
  assign out_20 = delay_1_out_2 ? register_18_q : 32'bz;  // Controlled_Buffer controlled_buffer_18
  Pull_Resistor pull_resistor_18 (.node(out_20));
  Pull_Resistor pull_resistor_19 (.node(out_21));
  assign out_21 = delay_1_out_2 ? register_19_q : 32'bz;  // Controlled_Buffer controlled_buffer_19
  Pull_Resistor pull_resistor_20 (.node(out_22));
  assign out_22 = delay_1_out_2 ? register_20_q : 32'bz;  // Controlled_Buffer controlled_buffer_20
  assign out_23 = delay_1_out_2 ? register_21_q : 32'bz;  // Controlled_Buffer controlled_buffer_21
  Pull_Resistor pull_resistor_21 (.node(out_23));
  Pull_Resistor pull_resistor_22 (.node(out_24));
  assign out_24 = delay_1_out_2 ? register_22_q : 32'bz;  // Controlled_Buffer controlled_buffer_22
  Pull_Resistor pull_resistor_23 (.node(out_25));
  assign out_25 = delay_1_out_2 ? register_23_q : 32'bz;  // Controlled_Buffer controlled_buffer_23
  Pull_Resistor pull_resistor_24 (.node(out_26));
  assign out_26 = delay_1_out_2 ? register_24_q : 32'bz;  // Controlled_Buffer controlled_buffer_24
  Pull_Resistor pull_resistor_25 (.node(out_27));
  assign out_27 = delay_1_out_2 ? register_25_q : 32'bz;  // Controlled_Buffer controlled_buffer_25
  Pull_Resistor pull_resistor_26 (.node(out_28));
  assign out_28 = delay_1_out_2 ? register_26_q : 32'bz;  // Controlled_Buffer controlled_buffer_26
  assign out_29 = delay_1_out_2 ? register_27_q : 32'bz;  // Controlled_Buffer controlled_buffer_27
  Pull_Resistor pull_resistor_27 (.node(out_29));
  Pull_Resistor pull_resistor_28 (.node(out_30));
  assign out_30 = delay_1_out_2 ? register_28_q : 32'bz;  // Controlled_Buffer controlled_buffer_28
  assign out_31 = delay_1_out_2 ? register_29_q : 32'bz;  // Controlled_Buffer controlled_buffer_29
  Pull_Resistor pull_resistor_29 (.node(out_31));
  assign out_32 = delay_1_out_2 ? register_30_q : 32'bz;  // Controlled_Buffer controlled_buffer_30
  Pull_Resistor pull_resistor_30 (.node(out_32));
  assign out_33 = delay_1_out_2 ? register_31_q : 32'bz;  // Controlled_Buffer controlled_buffer_31
  Pull_Resistor pull_resistor_31 (.node(out_33));
  assign out_34 = delay_1_out_2 ? register_32_q : 32'bz;  // Controlled_Buffer controlled_buffer_32
  Pull_Resistor pull_resistor_32 (.node(out_34));
endmodule

module task_drawer (
  input  in_1,
  input  [31:0] in_2,
  input  [4:0] clock32,
  input  [31:0] in_4,
  input  [5:0] y,
  input  [31:0] in_6,
  input  [31:0] in_7,
  input  [5:0] x,
  input  [3:0] in_9,
  input  [3:0] in_10,
  input  [3:0] in_11,
  input  [3:0] in_12,
  output [31:0] out_13,
  output [31:0] out_14,
  output [31:0] out_15,
  output [31:0] out_16
);

  wire and_1_out, and_2_out, and_3_out, comparator_1_eq, comparator_2_eq, comparator_3_eq, comparator_4_eq,
       demultiplexer_1_out0, demultiplexer_1_out1, demultiplexer_2_out0, demultiplexer_2_out1,
       demultiplexer_3_out0, demultiplexer_3_out1, demultiplexer_4_out0, demultiplexer_4_out1, or_1_out,
       or_2_out, priority_encoder_1_p1, subtractor_1_bout, subtractor_2_bout, subtractor_3_bout,
       subtractor_4_bout, subtractor_5_bout, subtractor_6_bout, subtractor_8_bout, subtractor_9_bout;
  wire [1:0] multiplexer_6_out, priority_encoder_1_p4;
  wire [3:0] multiplexer_1_out;
  wire [4:0] bit_extender_1_out, bit_extender_3_out, bit_extender_5_out, multiplexer_7_out,
       multiplexer_8_out, multiplexer_9_out, subtractor_6_out, subtractor_7_out, subtractor_8_out,
       subtractor_9_out;
  wire [5:0] adder_1_out, adder_2_out, adder_3_out, multiplexer_2_out, multiplexer_3_out, multiplexer_4_out,
       multiplexer_5_out, subtractor_1_out, subtractor_2_out, subtractor_3_out, subtractor_4_out,
       subtractor_5_out;
  wire [31:0] bit_extender_2_out, bit_extender_4_out, multiplexer_10_out, multiplexer_11_out,
       multiplexer_12_out, or_3_out, or_4_out, or_5_out, or_6_out, or_7_out, or_8_out, shifter_1_out,
       shifter_2_out, shifter_3_out, shifter_4_out, shifter_5_out, shifter_6_out, shifter_7_out;

  Adder #(.width(6)) adder_1 (.a(y), .b(6'b000001), .out(adder_1_out));  // open: cin, cout
  Adder #(.width(6)) adder_2 (.a(y), .b(6'b000010), .out(adder_2_out));  // open: cin, cout
  Adder #(.width(6)) adder_3 (.a(y), .b(6'b000011), .out(adder_3_out));  // open: cin, cout
  Multiplexer #(.select(2), .width(4), .enable("false")) multiplexer_1 (
    .in0(in_9), .in1(in_10), .in2(in_11), .in3(in_12), .out(multiplexer_1_out), .sel(multiplexer_6_out));
  and and_1 (and_1_out, x[5], x[4], x[3], x[2]);
  Subtractor #(.width(6)) subtractor_1 (
    .a(y), .b(6'b100000), .out(subtractor_1_out), .bout(subtractor_1_bout));  // open: bin
  Multiplexer #(.width(6), .enable("false")) multiplexer_2 (
    .in0(subtractor_1_out), .in1(y), .out(multiplexer_2_out), .sel(subtractor_1_bout));
  Subtractor #(.width(6)) subtractor_2 (
    .a(adder_1_out), .b(6'b100000), .out(subtractor_2_out), .bout(subtractor_2_bout));  // open: bin
  Multiplexer #(.width(6), .enable("false")) multiplexer_3 (
    .in0(subtractor_2_out), .in1(adder_1_out), .out(multiplexer_3_out), .sel(subtractor_2_bout));
  Multiplexer #(.width(6), .enable("false")) multiplexer_4 (
    .in0(subtractor_3_out), .in1(adder_2_out), .out(multiplexer_4_out), .sel(subtractor_3_bout));
  Subtractor #(.width(6)) subtractor_3 (
    .a(adder_2_out), .b(6'b100000), .out(subtractor_3_out), .bout(subtractor_3_bout));  // open: bin
  Multiplexer #(.width(6), .enable("false")) multiplexer_5 (
    .in0(subtractor_4_out), .in1(adder_3_out), .out(multiplexer_5_out), .sel(subtractor_4_bout));
  Subtractor #(.width(6)) subtractor_4 (
    .a(adder_3_out), .b(6'b100000), .out(subtractor_4_out), .bout(subtractor_4_bout));  // open: bin
  // Probe on multiplexer_6_out
  Multiplexer #(.width(2), .enable("false")) multiplexer_6 (
    .in0(priority_encoder_1_p4), .in1(2'b00), .out(multiplexer_6_out), .sel(priority_encoder_1_p1));
  // Probe on multiplexer_1_out
  Subtractor #(.width(6)) subtractor_5 (
    .a(x), .b(6'b011101), .out(subtractor_5_out), .bout(subtractor_5_bout));  // open: bin
  Comparator #(.width(6), .mode("unsigned")) comparator_1 (
    .a(multiplexer_2_out), .b({1'b0, clock32}), .eq(comparator_1_eq));  // open: gt, lt
  Comparator #(.width(6), .mode("unsigned")) comparator_2 (
    .a(multiplexer_3_out), .b({1'b0, clock32}), .eq(comparator_2_eq));  // open: gt, lt
  Comparator #(.width(6), .mode("unsigned")) comparator_3 (
    .a(multiplexer_4_out), .b({1'b0, clock32}), .eq(comparator_3_eq));  // open: gt, lt
  Comparator #(.width(6), .mode("unsigned")) comparator_4 (
    .a(multiplexer_5_out), .b({1'b0, clock32}), .eq(comparator_4_eq));  // open: gt, lt
  // Priority_Encoder #(.select(2)) priority_encoder_1: pin names not known; wires that end beside it: priority_encoder_1_p1, comparator_1_eq, comparator_2_eq, priority_encoder_1_p4, comparator_3_eq, comparator_4_eq
  Bit_Extender #(.in_width(6), .out_width(5)) bit_extender_1 (.in(x), .out(bit_extender_1_out));
  assign bit_extender_2_out = {{28{1'b0}}, multiplexer_1_out};  // Bit_Extender bit_extender_2
  Shifter #(.width(32)) shifter_1 (.in(bit_extender_2_out), .\dist (5'b01110), .out(shifter_1_out));
  Bit_Extender #(.in_width(6), .out_width(5)) bit_extender_3 (.in(subtractor_5_out), .out(bit_extender_3_out));
  assign bit_extender_4_out = {{28{1'b0}}, multiplexer_1_out};  // Bit_Extender bit_extender_4
  Shifter #(.width(32)) shifter_2 (.in(bit_extender_4_out), .\dist (5'b01110), .out(shifter_2_out));
  Shifter #(.width(32), .shift("lr")) shifter_3 (
    .in(bit_extender_4_out), .\dist (bit_extender_5_out), .out(shifter_3_out));
  assign bit_extender_5_out = {{3{1'b0}}, x[1:0]};  // Bit_Extender bit_extender_5
  Demultiplexer #(.enable("false")) demultiplexer_1 (
    .out0(demultiplexer_1_out0), .out1(demultiplexer_1_out1), .in(comparator_1_eq), .sel(subtractor_1_bout));
  Demultiplexer #(.enable("false")) demultiplexer_2 (
    .out0(demultiplexer_2_out0), .out1(demultiplexer_2_out1), .in(comparator_2_eq), .sel(subtractor_2_bout));
  Demultiplexer #(.enable("false")) demultiplexer_3 (
    .out0(demultiplexer_3_out0), .out1(demultiplexer_3_out1), .in(comparator_3_eq), .sel(subtractor_3_bout));
  Demultiplexer #(.enable("false")) demultiplexer_4 (
    .out0(demultiplexer_4_out0), .out1(demultiplexer_4_out1), .in(comparator_4_eq), .sel(subtractor_4_bout));
  Subtractor #(.width(5)) subtractor_6 (
    .a(5'b01110), .b(bit_extender_1_out), .out(subtractor_6_out), .bout(subtractor_6_bout));  // open: bin
  Subtractor #(.width(5)) subtractor_7 (
    .a(bit_extender_1_out), .b(5'b01110), .out(subtractor_7_out));  // open: bin, bout
  Subtractor #(.width(5)) subtractor_8 (
    .a(5'b10001), .b(bit_extender_3_out), .out(subtractor_8_out), .bout(subtractor_8_bout));  // open: bin
  Subtractor #(.width(5)) subtractor_9 (
    .a(bit_extender_3_out), .b(5'b10001), .out(subtractor_9_out), .bout(subtractor_9_bout));  // open: bin
  or or_1 (or_1_out, demultiplexer_1_out0, demultiplexer_2_out0, demultiplexer_3_out0, demultiplexer_4_out0);
  or or_2 (or_2_out, demultiplexer_1_out1, demultiplexer_2_out1, demultiplexer_3_out1, demultiplexer_4_out1);
  Multiplexer #(.width(5), .enable("false")) multiplexer_7 (
    .in0(subtractor_6_out), .in1(5'b11110), .out(multiplexer_7_out), .sel(subtractor_6_bout));
  Multiplexer #(.width(5), .enable("false")) multiplexer_8 (
    .in0(subtractor_8_out), .in1(5'b11110), .out(multiplexer_8_out), .sel(subtractor_8_bout));
  Multiplexer #(.width(5), .enable("false")) multiplexer_9 (
    .in0(subtractor_9_out), .in1(5'b11110), .out(multiplexer_9_out), .sel(subtractor_9_bout));
  Shifter #(.width(32)) shifter_4 (.in(shifter_1_out), .\dist (multiplexer_7_out), .out(shifter_4_out));
  assign or_3_out = shifter_4_out | shifter_5_out;  // OR_Gate or_3, 32 bits wide
  Shifter #(.width(32), .shift("lr")) shifter_5 (.in(shifter_1_out), .\dist (subtractor_7_out), .out(shifter_5_out));
  Shifter #(.width(32)) shifter_6 (.in(shifter_2_out), .\dist (multiplexer_8_out), .out(shifter_6_out));
  assign or_4_out = shifter_6_out | shifter_7_out;  // OR_Gate or_4, 32 bits wide
  Shifter #(.width(32), .shift("lr")) shifter_7 (.in(shifter_2_out), .\dist (multiplexer_9_out), .out(shifter_7_out));
  Multiplexer #(.width(32), .enable("false")) multiplexer_10 (
    .in0(or_3_out), .in1({32{1'b0}}), .out(multiplexer_10_out), .sel(x[5]));
  Multiplexer #(.width(32), .enable("false")) multiplexer_11 (
    .in0(or_4_out), .in1({32{1'b0}}), .out(multiplexer_11_out), .sel(subtractor_5_bout));
  Multiplexer #(.width(32), .enable("false")) multiplexer_12 (
    .in0(multiplexer_11_out), .in1(shifter_3_out), .out(multiplexer_12_out), .sel(and_1_out));
  and and_2 (and_2_out, or_1_out, in_1);
  and and_3 (and_3_out, in_1, or_2_out);
  Multiplexer #(.width(32), .enable("false")) multiplexer_13 (
    .in0(in_2), .in1(or_5_out), .out(out_13), .sel(and_3_out));
  assign or_5_out = in_2 | multiplexer_12_out;  // OR_Gate or_5, 32 bits wide
  Multiplexer #(.width(32), .enable("false")) multiplexer_14 (
    .in0(in_4), .in1(or_6_out), .out(out_14), .sel(and_3_out));
  assign or_6_out = in_4 | multiplexer_10_out;  // OR_Gate or_6, 32 bits wide
  Multiplexer #(.width(32), .enable("false")) multiplexer_15 (
    .in0(in_6), .in1(or_7_out), .out(out_15), .sel(and_2_out));
  assign or_7_out = in_6 | multiplexer_10_out;  // OR_Gate or_7, 32 bits wide
  Multiplexer #(.width(32), .enable("false")) multiplexer_16 (
    .in0(in_7), .in1(or_8_out), .out(out_16), .sel(and_2_out));
  assign or_8_out = in_7 | multiplexer_12_out;  // OR_Gate or_8, 32 bits wide
endmodule

module laser_drawer (
  input  [31:0] in_1,
  input  [31:0] in_2,
  input  [31:0] in_3,
  input  [31:0] in_4,
  input  [31:0] in_5,
  input  [4:0] clock32,
  output [31:0] out_7,
  output [31:0] out_8,
  output [31:0] out_9,
  output [31:0] out_10
);

  wire and_1_out, comparator_1_gt, comparator_2_gt, d_ff_1_q, not_1_out, or_1_out, or_2_out, or_7_out,
       or_8_out, or_9_out, or_10_out, subtractor_1_bout, subtractor_2_bout, subtractor_3_bout,
       subtractor_4_bout, subtractor_8_bout, subtractor_9_bout, subtractor_10_bout, subtractor_12_bout,
       subtractor_13_bout, subtractor_14_bout, subtractor_16_bout, subtractor_17_bout;
  wire [4:0] bit_extender_1_out, bit_extender_2_out, bit_extender_3_out, bit_extender_4_out,
       multiplexer_9_out, multiplexer_10_out, multiplexer_11_out, multiplexer_12_out, multiplexer_13_out,
       multiplexer_14_out, multiplexer_15_out, multiplexer_16_out, subtractor_10_out, subtractor_11_out,
       subtractor_12_out, subtractor_13_out, subtractor_14_out, subtractor_15_out, subtractor_16_out,
       subtractor_17_out, undriven;
  wire [5:0] adder_1_out, adder_2_out, divider_1_out, multiplexer_1_out, multiplexer_2_out,
       multiplexer_3_out, multiplexer_4_out, multiplexer_5_out, multiplexer_6_out, multiplexer_7_out,
       multiplexer_8_out, multiplier_1_cout, multiplier_1_out, multiplier_2_cout, multiplier_2_out,
       negator_1_out, negator_2_out, subtractor_1_out, subtractor_2_out, subtractor_3_out, subtractor_4_out,
       subtractor_5_out, subtractor_6_out, subtractor_7_out, subtractor_8_out, subtractor_9_out;
  wire [7:0] counter_1_q;
  wire [31:0] invertor_1_out_3, invertor_1_out_4, invertor_2_out_3, invertor_2_out_4, multiplexer_17_out,
       multiplexer_18_out, multiplexer_19_out, multiplexer_20_out, multiplexer_21_out, multiplexer_22_out,
       multiplexer_23_out, multiplexer_24_out, or_3_out, or_4_out, or_5_out, or_6_out, or_11_out, or_12_out,
       or_13_out, or_14_out, shifter_1_out, shifter_2_out, shifter_3_out, shifter_4_out, shifter_5_out,
       shifter_6_out, shifter_7_out, shifter_8_out, shifter_9_out, shifter_10_out, shifter_11_out,
       shifter_12_out, shifter_13_out;

  and and_1 (and_1_out, ~clock32[0], ~clock32[1], ~clock32[2], ~clock32[3], ~clock32[4]);  // AND_Gate
  and and_2 (and_1_out, ~undriven[0], ~undriven[1], ~undriven[2], ~undriven[3], ~undriven[4]);  // AND_Gate
  Subtractor #(.width(6)) subtractor_1 (
    .a(in_4[5:0]), .b(in_4[17:12]), .out(subtractor_1_out), .bout(subtractor_1_bout));  // open: bin
  Subtractor #(.width(6)) subtractor_2 (
    .a(in_4[11:6]), .b(in_4[23:18]), .out(subtractor_2_out), .bout(subtractor_2_bout));  // open: bin
  Comparator #(.width(6), .mode("unsigned")) comparator_1 (
    .a(in_4[11:6]), .b(in_4[23:18]), .gt(comparator_1_gt));  // open: eq, lt
  Multiplexer #(.width(6), .enable("false")) multiplexer_1 (
    .in0(in_4[11:6]), .in1(in_4[23:18]), .out(multiplexer_1_out), .sel(comparator_1_gt));
  D_Flip_Flop d_ff_1 (.clk(and_1_out), .D(and_1_out), .Q(d_ff_1_q), .reset(d_ff_1_q));  // open: Qn, preset, en
  Negator #(.width(6)) negator_1 (.in(subtractor_1_out), .out(negator_1_out));
  Negator #(.width(6)) negator_2 (.in(subtractor_2_out), .out(negator_2_out));
  Multiplexer #(.width(6), .enable("false")) multiplexer_2 (
    .in0(in_4[5:0]), .in1(in_4[17:12]), .out(multiplexer_2_out), .sel(comparator_1_gt));
  Multiplexer #(.width(6), .enable("false")) multiplexer_3 (
    .in0(in_4[17:12]), .in1(in_4[5:0]), .out(multiplexer_3_out), .sel(comparator_1_gt));
  Subtractor #(.width(6)) subtractor_3 (
    .a({1'b0, clock32}), .b(multiplexer_1_out), .out(subtractor_3_out), .bout(subtractor_3_bout));  // open: bin
  Subtractor #(.width(6)) subtractor_4 (
    .a({1'b1, clock32}), .b(multiplexer_1_out), .out(subtractor_4_out), .bout(subtractor_4_bout));  // open: bin
  Counter #(.ongoal("stay")) counter_1 (.Q(counter_1_q), .clk(d_ff_1_q));  // open: load, D, count, carry, clr
  Multiplexer #(.width(6), .enable("false")) multiplexer_4 (
    .in0(subtractor_1_out), .in1(negator_1_out), .out(multiplexer_4_out), .sel(subtractor_1_bout));
  Multiplexer #(.width(6), .enable("false")) multiplexer_5 (
    .in0(subtractor_2_out), .in1(negator_2_out), .out(multiplexer_5_out), .sel(subtractor_2_bout));
  Subtractor #(.width(6)) subtractor_5 (
    .a({6{1'b1}}), .b(multiplexer_2_out), .out(subtractor_5_out));  // open: bin, bout
  Multiplexer #(.width(6), .enable("false")) multiplexer_6 (
    .in0(subtractor_5_out), .in1(multiplexer_2_out), .out(multiplexer_6_out), .sel(not_1_out));
  not not_1 (not_1_out, comparator_2_gt);
  Comparator #(.width(6), .mode("unsigned")) comparator_2 (
    .a(multiplexer_2_out), .b(multiplexer_3_out), .gt(comparator_2_gt));  // open: eq, lt
  Multiplexer #(.width(6), .enable("false")) multiplexer_7 (
    .in0(subtractor_3_out), .in1({6{1'b1}}), .out(multiplexer_7_out), .sel(subtractor_3_bout));
  Multiplexer #(.width(6), .enable("false")) multiplexer_8 (
    .in0(subtractor_4_out), .in1({6{1'b1}}), .out(multiplexer_8_out), .sel(subtractor_4_bout));
  Comparator comparator_3 (.a(in_4[31:24]), .b(counter_1_q));  // open: gt, eq, lt
  Divider #(.width(6)) divider_1 (
    .a(multiplexer_4_out), .b(multiplexer_5_out), .out(divider_1_out));  // open: upper, rem
  Multiplier #(.width(6)) multiplier_1 (
    .a(divider_1_out), .b(multiplexer_7_out), .out(multiplier_1_out), .cout(multiplier_1_cout));  // open: cin
  Adder #(.width(6)) adder_1 (.a(multiplexer_6_out), .b(multiplier_1_out), .out(adder_1_out));  // open: cin, cout
  or or_1 (or_1_out, multiplier_1_cout[0], multiplier_1_cout[1], multiplier_1_cout[2], multiplier_1_cout[4], multiplier_1_cout[5], multiplier_1_cout[3]);
  Multiplier #(.width(6)) multiplier_2 (
    .a(divider_1_out), .b(multiplexer_8_out), .out(multiplier_2_out), .cout(multiplier_2_cout));  // open: cin
  Adder #(.width(6)) adder_2 (.a(multiplier_2_out), .b(multiplexer_6_out), .out(adder_2_out));  // open: cin, cout
  or or_2 (or_2_out, multiplier_2_cout[0], multiplier_2_cout[1], multiplier_2_cout[2], multiplier_2_cout[4], multiplier_2_cout[5], multiplier_2_cout[3]);
  Subtractor #(.width(6)) subtractor_6 (.a(6'b100000), .b(divider_1_out), .out(subtractor_6_out));  // open: bin, bout
  Shifter #(.width(32)) shifter_1 (.in({32{1'b1}}), .\dist (subtractor_6_out[4:0]), .out(shifter_1_out));
  Subtractor #(.width(6)) subtractor_7 (.a(6'b100001), .b(divider_1_out), .out(subtractor_7_out));  // open: bin, bout
  Multiplexer #(.width(5), .enable("false")) multiplexer_9 (
    .in0(divider_1_out[4:0]), .in1(5'b00001), .out(multiplexer_9_out), .sel(divider_1_out[5]));
  Subtractor #(.width(6)) subtractor_8 (
    .a(adder_1_out), .b(subtractor_7_out), .out(subtractor_8_out), .bout(subtractor_8_bout));  // open: bin
  Multiplexer #(.width(5), .enable("false")) multiplexer_10 (
    .in0(divider_1_out[4:0]), .in1(5'b00001), .out(multiplexer_10_out), .sel(divider_1_out[5]));
  Subtractor #(.width(6)) subtractor_9 (
    .a(adder_2_out), .b(subtractor_7_out), .out(subtractor_9_out), .bout(subtractor_9_bout));  // open: bin
  Bit_Extender #(.in_width(6), .out_width(5)) bit_extender_1 (.in(adder_1_out), .out(bit_extender_1_out));
  Bit_Extender #(.in_width(6), .out_width(5)) bit_extender_2 (.in(subtractor_8_out), .out(bit_extender_2_out));
  Bit_Extender #(.in_width(6), .out_width(5)) bit_extender_3 (.in(adder_2_out), .out(bit_extender_3_out));
  Bit_Extender #(.in_width(6), .out_width(5)) bit_extender_4 (.in(subtractor_9_out), .out(bit_extender_4_out));
  Shifter #(.width(32), .shift("lr")) shifter_2 (.in(shifter_1_out), .\dist (5'b00001), .out(shifter_2_out));
  Shifter #(.width(32), .shift("lr")) shifter_3 (.in(shifter_1_out), .\dist (5'b00001), .out(shifter_3_out));
  Shifter #(.width(32), .shift("lr")) shifter_4 (.in(shifter_1_out), .\dist (5'b00001), .out(shifter_4_out));
  Shifter #(.width(32), .shift("lr")) shifter_5 (.in(shifter_1_out), .\dist (5'b00001), .out(shifter_5_out));
  Multiplexer #(.width(5), .enable("false")) multiplexer_11 (
    .in0(subtractor_10_out), .in1({5{1'b1}}), .out(multiplexer_11_out), .sel(subtractor_10_bout));
  Subtractor #(.width(5)) subtractor_10 (
    .a(5'b00001), .b(bit_extender_1_out), .out(subtractor_10_out), .bout(subtractor_10_bout));  // open: bin
  Subtractor #(.width(5)) subtractor_11 (
    .a(bit_extender_1_out), .b(5'b00001), .out(subtractor_11_out));  // open: bin, bout
  Multiplexer #(.width(5), .enable("false")) multiplexer_12 (
    .in0(subtractor_12_out), .in1({5{1'b1}}), .out(multiplexer_12_out), .sel(subtractor_12_bout));
  Subtractor #(.width(5)) subtractor_12 (
    .a(multiplexer_9_out), .b(bit_extender_2_out), .out(subtractor_12_out), .bout(subtractor_12_bout));  // open: bin
  Subtractor #(.width(5)) subtractor_13 (
    .a(bit_extender_2_out), .b(multiplexer_9_out), .out(subtractor_13_out), .bout(subtractor_13_bout));  // open: bin
  Multiplexer #(.width(5), .enable("false")) multiplexer_13 (
    .in0(subtractor_13_out), .in1({5{1'b1}}), .out(multiplexer_13_out), .sel(subtractor_13_bout));
  Subtractor #(.width(5)) subtractor_14 (
    .a(5'b00001), .b(bit_extender_3_out), .out(subtractor_14_out), .bout(subtractor_14_bout));  // open: bin
  Multiplexer #(.width(5), .enable("false")) multiplexer_14 (
    .in0(subtractor_14_out), .in1({5{1'b1}}), .out(multiplexer_14_out), .sel(subtractor_14_bout));
  Subtractor #(.width(5)) subtractor_15 (
    .a(bit_extender_3_out), .b(5'b00001), .out(subtractor_15_out));  // open: bin, bout
  Subtractor #(.width(5)) subtractor_16 (
    .a(multiplexer_10_out), .b(bit_extender_4_out), .out(subtractor_16_out), .bout(subtractor_16_bout));  // open: bin
  Multiplexer #(.width(5), .enable("false")) multiplexer_15 (
    .in0(subtractor_16_out), .in1({5{1'b1}}), .out(multiplexer_15_out), .sel(subtractor_16_bout));
  Subtractor #(.width(5)) subtractor_17 (
    .a(bit_extender_4_out), .b(multiplexer_10_out), .out(subtractor_17_out), .bout(subtractor_17_bout));  // open: bin
  Multiplexer #(.width(5), .enable("false")) multiplexer_16 (
    .in0(subtractor_17_out), .in1({5{1'b1}}), .out(multiplexer_16_out), .sel(subtractor_17_bout));
  Shifter #(.width(32)) shifter_6 (.in(shifter_2_out), .\dist (multiplexer_11_out), .out(shifter_6_out));
  Shifter #(.width(32), .shift("lr")) shifter_7 (.in(shifter_2_out), .\dist (subtractor_11_out), .out(shifter_7_out));
  Shifter #(.width(32)) shifter_8 (.in(shifter_3_out), .\dist (multiplexer_12_out), .out(shifter_8_out));
  Shifter #(.width(32), .shift("lr")) shifter_9 (.in(shifter_3_out), .\dist (multiplexer_13_out), .out(shifter_9_out));
  Shifter #(.width(32)) shifter_10 (.in(shifter_4_out), .\dist (multiplexer_14_out), .out(shifter_10_out));
  Shifter #(.width(32), .shift("lr")) shifter_11 (.in(shifter_4_out), .\dist (subtractor_15_out), .out(shifter_11_out));
  Shifter #(.width(32)) shifter_12 (.in(shifter_5_out), .\dist (multiplexer_15_out), .out(shifter_12_out));
  Shifter #(.width(32), .shift("lr")) shifter_13 (
    .in(shifter_5_out), .\dist (multiplexer_16_out), .out(shifter_13_out));
  assign or_3_out = shifter_6_out | shifter_7_out;  // OR_Gate or_3, 32 bits wide
  assign or_4_out = shifter_8_out | shifter_9_out;  // OR_Gate or_4, 32 bits wide
  assign or_5_out = shifter_10_out | shifter_11_out;  // OR_Gate or_5, 32 bits wide
  assign or_6_out = shifter_12_out | shifter_13_out;  // OR_Gate or_6, 32 bits wide
  Multiplexer #(.width(32), .enable("false")) multiplexer_17 (
    .in0(or_3_out), .in1({32{1'b0}}), .out(multiplexer_17_out), .sel(or_7_out));
  or or_7 (or_7_out, adder_1_out[5], or_1_out);
  Multiplexer #(.width(32), .enable("false")) multiplexer_18 (
    .in0(or_4_out), .in1({32{1'b0}}), .out(multiplexer_18_out), .sel(or_8_out));
  or or_8 (or_8_out, subtractor_8_bout, or_1_out);
  Multiplexer #(.width(32), .enable("false")) multiplexer_19 (
    .in0(or_5_out), .in1({32{1'b0}}), .out(multiplexer_19_out), .sel(or_9_out));
  or or_9 (or_9_out, adder_2_out[5], or_2_out);
  Multiplexer #(.width(32), .enable("false")) multiplexer_20 (
    .in0(or_6_out), .in1({32{1'b0}}), .out(multiplexer_20_out), .sel(or_10_out));
  or or_10 (or_10_out, subtractor_9_bout, or_2_out);
  Multiplexer #(.width(32), .enable("false")) multiplexer_21 (
    .in0(multiplexer_17_out), .in1(invertor_1_out_3), .out(multiplexer_21_out), .sel(comparator_2_gt));
  invertor invertor_1 (
    .in_1(multiplexer_18_out), .in_2(multiplexer_17_out), .out_3(invertor_1_out_3), .out_4(invertor_1_out_4));
  Multiplexer #(.width(32), .enable("false")) multiplexer_22 (
    .in0(multiplexer_18_out), .in1(invertor_1_out_4), .out(multiplexer_22_out), .sel(comparator_2_gt));
  Multiplexer #(.width(32), .enable("false")) multiplexer_23 (
    .in0(multiplexer_19_out), .in1(invertor_2_out_3), .out(multiplexer_23_out), .sel(comparator_2_gt));
  invertor invertor_2 (
    .in_1(multiplexer_20_out), .in_2(multiplexer_19_out), .out_3(invertor_2_out_3), .out_4(invertor_2_out_4));
  Multiplexer #(.width(32), .enable("false")) multiplexer_24 (
    .in0(multiplexer_20_out), .in1(invertor_2_out_4), .out(multiplexer_24_out), .sel(comparator_2_gt));
  Multiplexer #(.width(32), .enable("false")) multiplexer_25 (.in0(in_1), .in1(or_11_out), .out(out_7), .sel(1'b1));
  assign or_11_out = in_1 | multiplexer_22_out;  // OR_Gate or_11, 32 bits wide
  Multiplexer #(.width(32), .enable("false")) multiplexer_26 (.in0(in_2), .in1(or_12_out), .out(out_8), .sel(1'b1));
  assign or_12_out = in_2 | multiplexer_21_out;  // OR_Gate or_12, 32 bits wide
  Multiplexer #(.width(32), .enable("false")) multiplexer_27 (.in0(in_3), .in1(or_13_out), .out(out_9), .sel(1'b1));
  assign or_13_out = in_3 | multiplexer_23_out;  // OR_Gate or_13, 32 bits wide
  Multiplexer #(.width(32), .enable("false")) multiplexer_28 (.in0(in_5), .in1(or_14_out), .out(out_10), .sel(1'b1));
  assign or_14_out = in_5 | multiplexer_24_out;  // OR_Gate or_14, 32 bits wide
  // Probe on multiplexer_22_out
  // Probe on multiplexer_21_out
  // Probe on multiplexer_23_out
  // Probe on multiplexer_24_out
endmodule
module invertor (
  input  [31:0] in_1,
  input  [31:0] in_2,
  output [31:0] out_3,
  output [31:0] out_4
);


  assign out_3 = {in_1[0], in_1[1], in_1[2], in_1[3], in_1[4], in_1[5], in_1[6], in_1[7], in_1[8], in_1[9], in_1[10], in_1[11], in_1[12], in_1[13], in_1[14], in_1[15], in_1[16], in_1[17], in_1[18], in_1[19], in_1[20], in_1[21], in_1[22], in_1[23], in_1[24], in_1[25], in_1[26], in_1[27], in_1[28], in_1[29], in_1[30], in_1[31]};
  assign out_4 = {in_2[0], in_2[1], in_2[2], in_2[3], in_2[4], in_2[5], in_2[6], in_2[7], in_2[8], in_2[9], in_2[10], in_2[11], in_2[12], in_2[13], in_2[14], in_2[15], in_2[16], in_2[17], in_2[18], in_2[19], in_2[20], in_2[21], in_2[22], in_2[23], in_2[24], in_2[25], in_2[26], in_2[27], in_2[28], in_2[29], in_2[30], in_2[31]};
endmodule

module laser_drawer_2_0 (
  input  [31:0] in_1,
  input  [31:0] in_2,
  input  [31:0] in_3,
  input  [31:0] in_4,
  input  [31:0] in_5,
  input  [4:0] clock32,
  output [31:0] out_7,
  output [31:0] out_8,
  output [31:0] out_9,
  output [31:0] out_10
);

  wire adder_6_cout, adder_7_cout, comparator_1_gt, comparator_2_gt, comparator_3_lt, comparator_4_gt,
       comparator_5_gt, comparator_6_gt, comparator_7_gt, comparator_8_gt, comparator_9_gt, not_1_out,
       or_1_out, or_2_out, or_3_out, or_4_out, or_9_out, or_10_out, or_11_out, or_12_out, subtractor_1_bout,
       subtractor_2_bout, subtractor_5_bout, subtractor_6_bout, subtractor_8_bout, subtractor_10_bout,
       subtractor_15_bout, subtractor_16_bout, subtractor_17_bout, subtractor_19_bout, subtractor_20_bout,
       subtractor_21_bout, subtractor_23_bout, subtractor_24_bout;
  wire [4:0] bit_extender_4_out, bit_extender_5_out, bit_extender_6_out, bit_extender_7_out,
       multiplexer_8_out, multiplexer_9_out, multiplexer_11_out, multiplexer_13_out, multiplexer_14_out,
       multiplexer_15_out, multiplexer_16_out, multiplexer_17_out, multiplexer_18_out, multiplexer_19_out,
       subtractor_17_out, subtractor_18_out, subtractor_19_out, subtractor_20_out, subtractor_21_out,
       subtractor_22_out, subtractor_23_out, subtractor_24_out;
  wire [5:0] adder_4_out, adder_5_out, adder_6_out, adder_7_out, multiplexer_1_out, multiplexer_2_out,
       multiplexer_3_out, multiplexer_4_out, multiplexer_5_out, multiplexer_6_out, multiplexer_7_out,
       negator_1_out, negator_2_out, subtractor_1_out, subtractor_2_out, subtractor_3_out, subtractor_4_out,
       subtractor_7_out, subtractor_8_out, subtractor_9_out, subtractor_10_out, subtractor_11_out,
       subtractor_12_out, subtractor_13_out, subtractor_14_out, subtractor_15_out, subtractor_16_out;
  wire [5:5] multiplexer_8_out_2, multiplexer_9_out_2;
  wire [15:0] adder_1_out, adder_2_out, adder_3_out, bit_extender_1_out, bit_extender_2_out,
       bit_extender_3_out, divider_1_out, multiplier_1_cout, multiplier_1_out, multiplier_2_cout,
       multiplier_2_out, multiplier_3_cout, multiplier_3_out, multiplier_4_cout, multiplier_4_out,
       shifter_1_out, subtractor_5_out, subtractor_6_out;
  wire [31:0] invertor_1_out_3, invertor_1_out_4, invertor_2_out_3, invertor_2_out_4, multiplexer_10_out,
       multiplexer_12_out, multiplexer_20_out, multiplexer_21_out, multiplexer_22_out, multiplexer_23_out,
       multiplexer_24_out, multiplexer_25_out, multiplexer_26_out, multiplexer_27_out, multiplexer_28_out,
       multiplexer_29_out, multiplexer_30_out, multiplexer_31_out, or_5_out, or_6_out, or_7_out, or_8_out,
       or_13_out, or_14_out, or_15_out, or_16_out, shifter_2_out, shifter_3_out, shifter_4_out,
       shifter_5_out, shifter_6_out, shifter_7_out, shifter_8_out, shifter_9_out, shifter_10_out,
       shifter_11_out, shifter_12_out, shifter_13_out, shifter_14_out, shifter_15_out;

  assign bit_extender_1_out = {{11{1'b0}}, clock32};  // Bit_Extender bit_extender_1
  Subtractor #(.width(6)) subtractor_1 (
    .a(in_3[5:0]), .b(in_3[17:12]), .out(subtractor_1_out), .bout(subtractor_1_bout));  // open: bin
  Subtractor #(.width(6)) subtractor_2 (
    .a(in_3[11:6]), .b(in_3[23:18]), .out(subtractor_2_out), .bout(subtractor_2_bout));  // open: bin
  Comparator #(.width(6), .mode("unsigned")) comparator_1 (
    .a(in_3[11:6]), .b(in_3[23:18]), .gt(comparator_1_gt));  // open: eq, lt
  Multiplexer #(.width(6), .enable("false")) multiplexer_1 (
    .in0(in_3[5:0]), .in1(in_3[17:12]), .out(multiplexer_1_out), .sel(comparator_1_gt));
  Multiplexer #(.width(6), .enable("false")) multiplexer_2 (
    .in0(in_3[17:12]), .in1(in_3[5:0]), .out(multiplexer_2_out), .sel(comparator_1_gt));
  Multiplexer #(.width(6), .enable("false")) multiplexer_3 (
    .in0(in_3[11:6]), .in1(in_3[23:18]), .out(multiplexer_3_out), .sel(comparator_1_gt));
  Negator #(.width(6)) negator_1 (.in(subtractor_1_out), .out(negator_1_out));
  Negator #(.width(6)) negator_2 (.in(subtractor_2_out), .out(negator_2_out));
  Subtractor #(.width(6)) subtractor_3 (
    .a({6{1'b1}}), .b(multiplexer_1_out), .out(subtractor_3_out));  // open: bin, bout
  Comparator #(.width(6), .mode("unsigned")) comparator_2 (
    .a(multiplexer_1_out), .b(multiplexer_2_out), .gt(comparator_2_gt));  // open: eq, lt
  Subtractor #(.width(6)) subtractor_4 (
    .a({6{1'b1}}), .b(multiplexer_2_out), .out(subtractor_4_out));  // open: bin, bout
  assign bit_extender_2_out = {{10{1'b0}}, multiplexer_4_out};  // Bit_Extender bit_extender_2
  Multiplexer #(.width(6), .enable("false")) multiplexer_4 (
    .in0(subtractor_1_out), .in1(negator_1_out), .out(multiplexer_4_out), .sel(subtractor_1_bout));
  Comparator #(.width(6), .mode("unsigned")) comparator_3 (
    .a(6'b000001), .b(multiplexer_5_out), .lt(comparator_3_lt));  // open: gt, eq
  not not_1 (not_1_out, comparator_3_lt);
  assign bit_extender_3_out = {{10{1'b0}}, multiplexer_5_out};  // Bit_Extender bit_extender_3
  Multiplexer #(.width(6), .enable("false")) multiplexer_5 (
    .in0(subtractor_2_out), .in1(negator_2_out), .out(multiplexer_5_out), .sel(subtractor_2_bout));
  Multiplexer #(.width(6), .enable("false")) multiplexer_6 (
    .in0(multiplexer_1_out), .in1(subtractor_3_out), .out(multiplexer_6_out), .sel(comparator_2_gt));
  Multiplexer #(.width(6), .enable("false")) multiplexer_7 (
    .in0(multiplexer_2_out), .in1(subtractor_4_out), .out(multiplexer_7_out), .sel(comparator_2_gt));
  Shifter #(.width(16)) shifter_1 (.in(bit_extender_2_out), .\dist (4'b1010), .out(shifter_1_out));
  Divider #(.width(16)) divider_1 (.a(shifter_1_out), .b(bit_extender_3_out), .out(divider_1_out));  // open: upper, rem
  Subtractor #(.width(16)) subtractor_5 (
    .a(bit_extender_1_out), .b({{10{1'b0}}, multiplexer_3_out}), .out(subtractor_5_out),
    .bout(subtractor_5_bout));  // open: bin
  Adder #(.width(16)) adder_1 (.a(16'h1), .b(subtractor_5_out), .out(adder_1_out));  // open: cin, cout
  Multiplier #(.width(16)) multiplier_1 (
    .a(adder_1_out), .b(divider_1_out), .out(multiplier_1_out), .cout(multiplier_1_cout));  // open: cin
  Multiplier #(.width(16)) multiplier_2 (
    .a(subtractor_5_out), .b(divider_1_out), .out(multiplier_2_out), .cout(multiplier_2_cout));  // open: cin
  Comparator #(.width(16), .mode("unsigned")) comparator_4 (
    .a(multiplier_1_cout), .b({16{1'b0}}), .gt(comparator_4_gt));  // open: eq, lt
  Comparator #(.width(16), .mode("unsigned")) comparator_5 (
    .a(multiplier_2_cout), .b({16{1'b0}}), .gt(comparator_5_gt));  // open: eq, lt
  Adder #(.width(16)) adder_2 (.a(bit_extender_1_out), .b(16'h20), .out(adder_2_out));  // open: cin, cout
  Subtractor #(.width(16)) subtractor_6 (
    .a(adder_2_out), .b({{10{1'b0}}, multiplexer_3_out}), .out(subtractor_6_out), .bout(subtractor_6_bout));  // open: bin
  Adder #(.width(16)) adder_3 (.a(16'h1), .b(subtractor_6_out), .out(adder_3_out));  // open: cin, cout
  Multiplier #(.width(16)) multiplier_3 (
    .a(adder_3_out), .b(divider_1_out), .out(multiplier_3_out), .cout(multiplier_3_cout));  // open: cin
  Multiplier #(.width(16)) multiplier_4 (
    .a(subtractor_6_out), .b(divider_1_out), .out(multiplier_4_out), .cout(multiplier_4_cout));  // open: cin
  Comparator #(.width(16), .mode("unsigned")) comparator_6 (
    .a(multiplier_3_cout), .b({16{1'b0}}), .gt(comparator_6_gt));  // open: eq, lt
  Comparator #(.width(16), .mode("unsigned")) comparator_7 (
    .a(multiplier_4_cout), .b({16{1'b0}}), .gt(comparator_7_gt));  // open: eq, lt
  Subtractor #(.width(6)) subtractor_7 (
    .a(multiplier_1_out[15:10]), .b(multiplier_2_out[15:10]), .out(subtractor_7_out));  // open: bin, bout
  Subtractor #(.width(6)) subtractor_8 (
    .a(multiplexer_7_out), .b(multiplier_2_out[15:10]), .out(subtractor_8_out), .bout(subtractor_8_bout));  // open: bin
  Comparator #(.width(6), .mode("unsigned")) comparator_8 (
    .a(multiplier_2_out[15:10]), .b(multiplexer_7_out), .gt(comparator_8_gt));  // open: eq, lt
  Subtractor #(.width(6)) subtractor_9 (
    .a(multiplier_3_out[15:10]), .b(multiplier_4_out[15:10]), .out(subtractor_9_out));  // open: bin, bout
  Subtractor #(.width(6)) subtractor_10 (
    .a(multiplexer_7_out), .b(multiplier_4_out[15:10]), .out(subtractor_10_out), .bout(subtractor_10_bout));  // open: bin
  Comparator #(.width(6), .mode("unsigned")) comparator_9 (
    .a(multiplier_4_out[15:10]), .b(multiplexer_7_out), .gt(comparator_9_gt));  // open: eq, lt
  Multiplexer #(.width(6), .enable("false")) multiplexer_8 (
    .in0(subtractor_7_out), .in1(adder_4_out), .out({multiplexer_8_out_2[5], multiplexer_8_out}),
    .sel(or_1_out));
  Adder #(.width(6)) adder_4 (.a(6'b000001), .b(subtractor_8_out), .out(adder_4_out));  // open: cin, cout
  or or_1 (or_1_out, comparator_8_gt, comparator_4_gt);
  Multiplexer #(.width(6), .enable("false")) multiplexer_9 (
    .in0(subtractor_9_out), .in1(adder_5_out), .out({multiplexer_9_out_2[5], multiplexer_9_out}),
    .sel(or_2_out));
  Adder #(.width(6)) adder_5 (.a(6'b000001), .b(subtractor_10_out), .out(adder_5_out));  // open: cin, cout
  or or_2 (or_2_out, comparator_9_gt, comparator_6_gt);
  Subtractor #(.width(6)) subtractor_11 (
    .a(6'b100000), .b({multiplexer_8_out_2[5], multiplexer_8_out}), .out(subtractor_11_out));  // open: bin, bout
  Adder #(.width(6)) adder_6 (
    .a(multiplier_2_out[15:10]), .b(multiplexer_6_out), .out(adder_6_out), .cout(adder_6_cout));  // open: cin
  or or_3 (or_3_out, subtractor_8_bout, adder_6_cout, comparator_5_gt, subtractor_5_bout);
  Subtractor #(.width(6)) subtractor_12 (
    .a(6'b100000), .b({multiplexer_9_out_2[5], multiplexer_9_out}), .out(subtractor_12_out));  // open: bin, bout
  Adder #(.width(6)) adder_7 (
    .a(multiplier_4_out[15:10]), .b(multiplexer_6_out), .out(adder_7_out), .cout(adder_7_cout));  // open: cin
  or or_4 (or_4_out, subtractor_10_bout, adder_7_cout, subtractor_6_bout, comparator_7_gt);
  Subtractor #(.width(6)) subtractor_13 (
    .a(6'b100001), .b({multiplexer_8_out_2[5], multiplexer_8_out}), .out(subtractor_13_out));  // open: bin, bout
  Subtractor #(.width(6)) subtractor_14 (
    .a(6'b100001), .b({multiplexer_9_out_2[5], multiplexer_9_out}), .out(subtractor_14_out));  // open: bin, bout
  Shifter #(.width(32)) shifter_2 (.in({32{1'b1}}), .\dist (subtractor_11_out[4:0]), .out(shifter_2_out));
  Shifter #(.width(32)) shifter_3 (.in({32{1'b1}}), .\dist (subtractor_12_out[4:0]), .out(shifter_3_out));
  Multiplexer #(.width(32), .enable("false")) multiplexer_10 (
    .in0(shifter_2_out), .in1(32'h80000000), .out(multiplexer_10_out), .sel(subtractor_11_out[5]));
  Multiplexer #(.width(5), .enable("false")) multiplexer_11 (
    .in0(multiplexer_8_out), .in1(5'b00001), .out(multiplexer_11_out), .sel(multiplexer_8_out_2[5]));
  Subtractor #(.width(6)) subtractor_15 (
    .a(adder_6_out), .b(subtractor_13_out), .out(subtractor_15_out), .bout(subtractor_15_bout));  // open: bin
  Multiplexer #(.width(32), .enable("false")) multiplexer_12 (
    .in0(shifter_3_out), .in1(32'h80000000), .out(multiplexer_12_out), .sel(subtractor_12_out[5]));
  Multiplexer #(.width(5), .enable("false")) multiplexer_13 (
    .in0(multiplexer_9_out), .in1(5'b00001), .out(multiplexer_13_out), .sel(multiplexer_9_out_2[5]));
  Subtractor #(.width(6)) subtractor_16 (
    .a(adder_7_out), .b(subtractor_14_out), .out(subtractor_16_out), .bout(subtractor_16_bout));  // open: bin
  Bit_Extender #(.in_width(6), .out_width(5)) bit_extender_4 (.in(adder_6_out), .out(bit_extender_4_out));
  Shifter #(.width(32), .shift("lr")) shifter_4 (.in(multiplexer_10_out), .\dist (5'b00001), .out(shifter_4_out));
  Bit_Extender #(.in_width(6), .out_width(5)) bit_extender_5 (.in(subtractor_15_out), .out(bit_extender_5_out));
  Shifter #(.width(32), .shift("lr")) shifter_5 (.in(multiplexer_10_out), .\dist (5'b00001), .out(shifter_5_out));
  Bit_Extender #(.in_width(6), .out_width(5)) bit_extender_6 (.in(adder_7_out), .out(bit_extender_6_out));
  Shifter #(.width(32), .shift("lr")) shifter_6 (.in(multiplexer_12_out), .\dist (5'b00001), .out(shifter_6_out));
  Bit_Extender #(.in_width(6), .out_width(5)) bit_extender_7 (.in(subtractor_16_out), .out(bit_extender_7_out));
  Shifter #(.width(32), .shift("lr")) shifter_7 (.in(multiplexer_12_out), .\dist (5'b00001), .out(shifter_7_out));
  Subtractor #(.width(5)) subtractor_17 (
    .a(5'b00001), .b(bit_extender_4_out), .out(subtractor_17_out), .bout(subtractor_17_bout));  // open: bin
  Subtractor #(.width(5)) subtractor_18 (
    .a(bit_extender_4_out), .b(5'b00001), .out(subtractor_18_out));  // open: bin, bout
  Subtractor #(.width(5)) subtractor_19 (
    .a(multiplexer_11_out), .b(bit_extender_5_out), .out(subtractor_19_out), .bout(subtractor_19_bout));  // open: bin
  Subtractor #(.width(5)) subtractor_20 (
    .a(bit_extender_5_out), .b(multiplexer_11_out), .out(subtractor_20_out), .bout(subtractor_20_bout));  // open: bin
  Subtractor #(.width(5)) subtractor_21 (
    .a(5'b00001), .b(bit_extender_6_out), .out(subtractor_21_out), .bout(subtractor_21_bout));  // open: bin
  Subtractor #(.width(5)) subtractor_22 (
    .a(bit_extender_6_out), .b(5'b00001), .out(subtractor_22_out));  // open: bin, bout
  Subtractor #(.width(5)) subtractor_23 (
    .a(multiplexer_13_out), .b(bit_extender_7_out), .out(subtractor_23_out), .bout(subtractor_23_bout));  // open: bin
  Subtractor #(.width(5)) subtractor_24 (
    .a(bit_extender_7_out), .b(multiplexer_13_out), .out(subtractor_24_out), .bout(subtractor_24_bout));  // open: bin
  Multiplexer #(.width(5), .enable("false")) multiplexer_14 (
    .in0(subtractor_17_out), .in1({5{1'b1}}), .out(multiplexer_14_out), .sel(subtractor_17_bout));
  Multiplexer #(.width(5), .enable("false")) multiplexer_15 (
    .in0(subtractor_19_out), .in1({5{1'b1}}), .out(multiplexer_15_out), .sel(subtractor_19_bout));
  Multiplexer #(.width(5), .enable("false")) multiplexer_16 (
    .in0(subtractor_20_out), .in1({5{1'b1}}), .out(multiplexer_16_out), .sel(subtractor_20_bout));
  Multiplexer #(.width(5), .enable("false")) multiplexer_17 (
    .in0(subtractor_21_out), .in1({5{1'b1}}), .out(multiplexer_17_out), .sel(subtractor_21_bout));
  Multiplexer #(.width(5), .enable("false")) multiplexer_18 (
    .in0(subtractor_23_out), .in1({5{1'b1}}), .out(multiplexer_18_out), .sel(subtractor_23_bout));
  Multiplexer #(.width(5), .enable("false")) multiplexer_19 (
    .in0(subtractor_24_out), .in1({5{1'b1}}), .out(multiplexer_19_out), .sel(subtractor_24_bout));
  Shifter #(.width(32)) shifter_8 (.in(shifter_4_out), .\dist (multiplexer_14_out), .out(shifter_8_out));
  assign or_5_out = shifter_8_out | shifter_9_out;  // OR_Gate or_5, 32 bits wide
  Shifter #(.width(32), .shift("lr")) shifter_9 (.in(shifter_4_out), .\dist (subtractor_18_out), .out(shifter_9_out));
  Shifter #(.width(32)) shifter_10 (.in(shifter_5_out), .\dist (multiplexer_15_out), .out(shifter_10_out));
  assign or_6_out = shifter_10_out | shifter_11_out;  // OR_Gate or_6, 32 bits wide
  Shifter #(.width(32), .shift("lr")) shifter_11 (
    .in(shifter_5_out), .\dist (multiplexer_16_out), .out(shifter_11_out));
  Shifter #(.width(32)) shifter_12 (.in(shifter_6_out), .\dist (multiplexer_17_out), .out(shifter_12_out));
  assign or_7_out = shifter_12_out | shifter_13_out;  // OR_Gate or_7, 32 bits wide
  Shifter #(.width(32), .shift("lr")) shifter_13 (.in(shifter_6_out), .\dist (subtractor_22_out), .out(shifter_13_out));
  Shifter #(.width(32)) shifter_14 (.in(shifter_7_out), .\dist (multiplexer_18_out), .out(shifter_14_out));
  assign or_8_out = shifter_14_out | shifter_15_out;  // OR_Gate or_8, 32 bits wide
  Shifter #(.width(32), .shift("lr")) shifter_15 (
    .in(shifter_7_out), .\dist (multiplexer_19_out), .out(shifter_15_out));
  Multiplexer #(.width(32), .enable("false")) multiplexer_20 (
    .in0(or_5_out), .in1({32{1'b1}}), .out(multiplexer_20_out), .sel(not_1_out));
  Multiplexer #(.width(32), .enable("false")) multiplexer_21 (
    .in0(or_6_out), .in1({32{1'b1}}), .out(multiplexer_21_out), .sel(not_1_out));
  Multiplexer #(.width(32), .enable("false")) multiplexer_22 (
    .in0(or_7_out), .in1({32{1'b1}}), .out(multiplexer_22_out), .sel(not_1_out));
  Multiplexer #(.width(32), .enable("false")) multiplexer_23 (
    .in0(or_8_out), .in1({32{1'b1}}), .out(multiplexer_23_out), .sel(not_1_out));
  Multiplexer #(.width(32), .enable("false")) multiplexer_24 (
    .in0(multiplexer_20_out), .in1({32{1'b0}}), .out(multiplexer_24_out), .sel(or_9_out));
  or or_9 (or_9_out, adder_6_out[5], or_3_out);
  Multiplexer #(.width(32), .enable("false")) multiplexer_25 (
    .in0(multiplexer_21_out), .in1({32{1'b0}}), .out(multiplexer_25_out), .sel(or_10_out));
  or or_10 (or_10_out, subtractor_15_bout, or_3_out);
  Multiplexer #(.width(32), .enable("false")) multiplexer_26 (
    .in0(multiplexer_22_out), .in1({32{1'b0}}), .out(multiplexer_26_out), .sel(or_11_out));
  or or_11 (or_11_out, adder_7_out[5], or_4_out);
  Multiplexer #(.width(32), .enable("false")) multiplexer_27 (
    .in0(multiplexer_23_out), .in1({32{1'b0}}), .out(multiplexer_27_out), .sel(or_12_out));
  or or_12 (or_12_out, subtractor_16_bout, or_4_out);
  Multiplexer #(.width(32), .enable("false")) multiplexer_28 (
    .in0(multiplexer_24_out), .in1(invertor_1_out_3), .out(multiplexer_28_out), .sel(comparator_2_gt));
  invertor invertor_1 (
    .in_1(multiplexer_25_out), .in_2(multiplexer_24_out), .out_3(invertor_1_out_3), .out_4(invertor_1_out_4));
  Multiplexer #(.width(32), .enable("false")) multiplexer_29 (
    .in0(multiplexer_25_out), .in1(invertor_1_out_4), .out(multiplexer_29_out), .sel(comparator_2_gt));
  Multiplexer #(.width(32), .enable("false")) multiplexer_30 (
    .in0(multiplexer_26_out), .in1(invertor_2_out_3), .out(multiplexer_30_out), .sel(comparator_2_gt));
  invertor invertor_2 (
    .in_1(multiplexer_27_out), .in_2(multiplexer_26_out), .out_3(invertor_2_out_3), .out_4(invertor_2_out_4));
  Multiplexer #(.width(32), .enable("false")) multiplexer_31 (
    .in0(multiplexer_27_out), .in1(invertor_2_out_4), .out(multiplexer_31_out), .sel(comparator_2_gt));
  Multiplexer #(.width(32), .enable("false")) multiplexer_32 (.in0(in_1), .in1(or_13_out), .out(out_7), .sel(1'b1));
  assign or_13_out = in_1 | multiplexer_29_out;  // OR_Gate or_13, 32 bits wide
  Multiplexer #(.width(32), .enable("false")) multiplexer_33 (.in0(in_2), .in1(or_14_out), .out(out_8), .sel(1'b1));
  assign or_14_out = in_2 | multiplexer_28_out;  // OR_Gate or_14, 32 bits wide
  Multiplexer #(.width(32), .enable("false")) multiplexer_34 (.in0(in_4), .in1(or_15_out), .out(out_9), .sel(1'b1));
  assign or_15_out = in_4 | multiplexer_30_out;  // OR_Gate or_15, 32 bits wide
  Multiplexer #(.width(32), .enable("false")) multiplexer_35 (.in0(in_5), .in1(or_16_out), .out(out_10), .sel(1'b1));
  assign or_16_out = in_5 | multiplexer_31_out;  // OR_Gate or_16, 32 bits wide
  // Probe on multiplexer_29_out
  // Probe on multiplexer_28_out
  // Probe on multiplexer_30_out
  // Probe on multiplexer_31_out
endmodule

module BGPU_or_module (
  input  [31:0] _1,
  input  [31:0] _1_2,
  input  [31:0] _1_3,
  input  [31:0] _1_4,
  input  [31:0] _1_5,
  input  [31:0] _1_6,
  input  [31:0] _1_7,
  input  [31:0] _1_8,
  input  [31:0] _1_9,
  input  [31:0] _1_10,
  input  [31:0] _1_11,
  input  [31:0] _1_12,
  input  [31:0] _1_13,
  input  [31:0] _1_14,
  input  [31:0] _1_15,
  input  [31:0] _1_16,
  input  [31:0] _1_17,
  input  [31:0] _1_18,
  input  [31:0] _1_19,
  input  [31:0] _1_20,
  input  [31:0] _1_21,
  input  [31:0] _1_22,
  input  [31:0] _1_23,
  input  [31:0] _1_24,
  input  [31:0] _1_25,
  input  [31:0] _1_26,
  input  [31:0] _1_27,
  input  [31:0] _1_28,
  input  [31:0] _1_29,
  input  [31:0] _1_30,
  input  [31:0] _1_31,
  input  [31:0] _1_32,
  output [31:0] _1_33
);

  assign _1_33 = _1 | _1_2 | _1_3 | _1_4 | _1_5 | _1_6 | _1_7 | _1_8 | _1_9 | _1_10 | _1_11 | _1_12 | _1_13 | _1_14 | _1_15 | _1_16 | _1_17 | _1_18 | _1_19 | _1_20 | _1_21 | _1_22 | _1_23 | _1_24 | _1_25 | _1_26 | _1_27 | _1_28 | _1_29 | _1_30 | _1_31 | _1_32;  // OR_Gate _1, 32 bits wide
endmodule

module score (
  input  [4:0] in_1,
  output [7:0] bus_0,
  output [3:0] out_3,
  output [3:0] out_4,
  output [3:0] out_5
);

  wire and_1_out, and_2_out;
  wire [4:0] counter_1_q;
  wire [9:0] counter_2_q, divider_1_out, divider_1_rem, divider_2_out, divider_2_rem;

  and and_1 (and_1_out, ~in_1[0], ~in_1[1], ~in_1[2], ~in_1[3], ~in_1[4]);  // AND_Gate
  Counter #(.width(5), .max('h18)) counter_1 (.Q(counter_1_q), .clk(and_1_out));  // open: load, D, count, carry, clr
  Bit_Extender #(.in_width(10), .out_width(8)) bit_extender_1 (.in(counter_2_q), .out(bus_0));
  Counter #(.width(10), .max('h3e7)) counter_2 (.Q(counter_2_q), .clk(and_2_out));  // open: load, D, count, carry, clr
  and and_2 (and_2_out, counter_1_q[3], counter_1_q[4]);
  Divider #(.width(10)) divider_1 (
    .a(counter_2_q), .b(10'h64), .out(divider_1_out), .rem(divider_1_rem));  // open: upper
  Divider #(.width(10)) divider_2 (
    .a(divider_1_rem), .b(10'ha), .out(divider_2_out), .rem(divider_2_rem));  // open: upper
  Bit_Extender #(.in_width(10), .out_width(4)) bit_extender_2 (.in(divider_1_out), .out(out_3));
  Bit_Extender #(.in_width(10), .out_width(4)) bit_extender_3 (.in(divider_2_out), .out(out_4));
  Bit_Extender #(.in_width(10), .out_width(4)) bit_extender_4 (.in(divider_2_rem), .out(out_5));
endmodule

module attack_controller (
  input  [5:0] in_1,
  input  in_2,
  input  [5:0] in_3,
  input  [4:0] in_4,
  input  in_5,
  output [31:0] out_6,
  output out_7
);

  wire and_1_out, comparator_1_gt, comparator_2_eq, comparator_3_eq, controlled_buffer_1_out,
       controlled_buffer_2_out, d_ff_1_q, d_ff_2_q, d_ff_3_q, delay_1_out_2;
  wire [3:0] counter_1_q, register_1_q;
  wire [7:0] controlled_buffer_3_out, counter_2_q;
  wire [31:0] shift_register_1_q0, shift_register_1_q1, shift_register_1_q2, shift_register_1_q3,
       shift_register_1_q4, shift_register_1_q5, shift_register_1_q6, shift_register_1_q7;

  assign controlled_buffer_1_out = in_5 ? in_2 : 1'bz;  // Controlled_Buffer controlled_buffer_1
  assign controlled_buffer_2_out = in_5 ? and_1_out : 1'bz;  // Controlled_Buffer controlled_buffer_2
  and and_1 (and_1_out, ~in_4[0], ~in_4[1], ~in_4[2], ~in_4[3], ~in_4[4]);  // AND_Gate
  D_Flip_Flop d_ff_1 (.clk(in_5), .D(in_5), .Q(d_ff_1_q), .reset(delay_1_out_2));  // open: Qn, preset, en
  delay delay_1 (.in_1(d_ff_1_q), .out_2(delay_1_out_2));
  Counter #(.width(4), .max('hf)) counter_1 (
    .Q(counter_1_q), .clk(d_ff_3_q), .clr(d_ff_2_q));  // open: load, D, count, carry
  Comparator #(.width(4), .mode("unsigned")) comparator_1 (
    .a(counter_1_q), .b(register_1_q), .gt(comparator_1_gt));  // open: eq, lt
  Register #(.width(4)) register_1 (.D(counter_1_q), .Q(register_1_q), .clk(comparator_1_gt));  // open: en, clr
  ROM #(.addrWidth(4), .dataWidth(32)) rom_1 (.addr(counter_1_q), .data(out_6));  // open: sel
  Comparator #(.width(32), .mode("unsigned")) comparator_2 (
    .a(out_6), .b({32{1'b0}}), .eq(comparator_2_eq));  // open: gt, lt
  assign controlled_buffer_3_out = controlled_buffer_1_out ? out_6[31:24] : 8'bz;  // Controlled_Buffer controlled_buffer_3
  Comparator #(.mode("unsigned")) comparator_3 (
    .a(controlled_buffer_3_out), .b(counter_2_q), .eq(comparator_3_eq));  // open: gt, lt
  Counter #(.ongoal("stay")) counter_2 (
    .Q(counter_2_q), .clk(controlled_buffer_2_out), .clr(d_ff_3_q));  // open: load, D, count, carry
  D_Flip_Flop d_ff_2 (.clk(controlled_buffer_1_out), .D(comparator_2_eq), .Q(d_ff_2_q));  // open: Qn, preset, en, reset
  D_Flip_Flop #(.trigger("high")) d_ff_3 (
    .clk(controlled_buffer_1_out), .D(comparator_3_eq), .Q(d_ff_3_q));  // open: Qn, preset, en, reset
  Pull_Resistor pull_resistor_1 (.node(comparator_3_eq));
  Shift_Register #(.width(32), .length(14)) shift_register_1 (
    .in(out_6), .q0(shift_register_1_q0), .q1(shift_register_1_q1), .q2(shift_register_1_q2),
    .q3(shift_register_1_q3), .q4(shift_register_1_q4), .q5(shift_register_1_q5), .q6(shift_register_1_q6),
    .q7(shift_register_1_q7));  // open: shift, clk, out, load, clr, d0, d1, d2, d3, d4, d5, d6, d7, d8, q8, d9, q9, d10, q10, d11, q11, d12, q12, d13, q13
  // Probe on shift_register_1_q0
  // Probe on shift_register_1_q1
  // Probe on shift_register_1_q2
  // Probe on shift_register_1_q3
  // Probe on shift_register_1_q4
  // Probe on shift_register_1_q5
  // Probe on shift_register_1_q6
  // Probe on shift_register_1_q7
  or or_1 (out_7, comparator_1_gt, d_ff_1_q);

  // Notes on the sheet:
  //   contents of rom_1 (hex, n*v repeats v):
  //   23000 22800 22000 21800 21000 20800 634f0 62cf0 624f0 61cf0 614f0 41060cf0
endmodule

module gpu_encoder_demultiplexpor (
  input  in_1,
  input  in_2,
  input  in_3,
  input  in_4,
  input  in_5,
  input  in_6,
  input  in_7,
  input  in_8,
  input  in_9,
  input  in_10,
  input  in_11,
  input  in_12,
  input  in_13,
  input  in_14,
  input  in_15,
  input  in_16,
  input  in_17,
  input  in_18,
  input  in_19,
  input  in_20,
  input  in_21,
  input  in_22,
  input  in_23,
  input  in_24,
  input  in_25,
  input  in_26,
  input  in_27,
  input  in_28,
  input  in_29,
  input  in_30,
  input  in_31,
  input  in_32,
  input  in_33,
  output out_34,
  output out_35,
  output out_36,
  output out_37,
  output out_38,
  output out_39,
  output out_40,
  output out_41,
  output out_42,
  output out_43,
  output out_44,
  output out_45,
  output out_46,
  output out_47,
  output out_48,
  output out_49,
  output out_50,
  output out_51,
  output out_52,
  output out_53,
  output out_54,
  output out_55,
  output out_56,
  output out_57,
  output out_58,
  output out_59,
  output out_60,
  output out_61,
  output out_62,
  output out_63,
  output out_64,
  output out_65
);

  wire [4:0] priority_encoder_1_p1;

  // NOT_Gate not_1 has open pins: in=in_2, out=open
  // NOT_Gate not_2 has open pins: in=in_3, out=open
  // NOT_Gate not_3 has open pins: in=in_4, out=open
  // NOT_Gate not_4 has open pins: in=in_5, out=open
  // NOT_Gate not_5 has open pins: in=in_1, out=open
  // NOT_Gate not_6 has open pins: in=in_9, out=open
  // NOT_Gate not_7 has open pins: in=in_11, out=open
  // NOT_Gate not_8 has open pins: in=in_10, out=open
  // NOT_Gate not_9 has open pins: in=in_6, out=open
  // NOT_Gate not_10 has open pins: in=in_8, out=open
  // NOT_Gate not_11 has open pins: in=in_13, out=open
  // NOT_Gate not_12 has open pins: in=in_12, out=open
  // NOT_Gate not_13 has open pins: in=in_7, out=open
  // NOT_Gate not_14 has open pins: in=in_16, out=open
  // NOT_Gate not_15 has open pins: in=in_18, out=open
  // NOT_Gate not_16 has open pins: in=in_17, out=open
  // NOT_Gate not_17 has open pins: in=in_19, out=open
  // NOT_Gate not_18 has open pins: in=in_21, out=open
  // NOT_Gate not_19 has open pins: in=in_20, out=open
  // NOT_Gate not_20 has open pins: in=in_15, out=open
  // NOT_Gate not_21 has open pins: in=in_14, out=open
  // Priority_Encoder #(.select(5)) priority_encoder_1: pin names not known; wires that end beside it: priority_encoder_1_p1
  // NOT_Gate not_22 has open pins: in=in_26, out=open
  // NOT_Gate not_23 has open pins: in=in_25, out=open
  // NOT_Gate not_24 has open pins: in=in_24, out=open
  // NOT_Gate not_25 has open pins: in=in_29, out=open
  // NOT_Gate not_26 has open pins: in=in_28, out=open
  // NOT_Gate not_27 has open pins: in=in_27, out=open
  // NOT_Gate not_28 has open pins: in=in_23, out=open
  // NOT_Gate not_29 has open pins: in=in_22, out=open
  // NOT_Gate not_30 has open pins: in=in_31, out=open
  // NOT_Gate not_31 has open pins: in=in_30, out=open
  // NOT_Gate not_32 has open pins: in=in_32, out=open
  Demultiplexer #(.select(5), .disabled(0), .enable("false")) demultiplexer_1 (
    .out0(out_34), .out1(out_35), .out2(out_36), .out3(out_37), .out4(out_38), .out5(out_39), .out6(out_40),
    .out7(out_41), .out8(out_42), .out9(out_43), .out10(out_44), .out11(out_45), .out12(out_46),
    .out13(out_47), .out14(out_48), .out15(out_49), .out16(out_50), .out17(out_51), .out18(out_52),
    .out19(out_53), .out20(out_54), .out21(out_55), .out22(out_56), .out23(out_57), .out24(out_58),
    .out25(out_59), .out26(out_60), .out27(out_61), .out28(out_62), .out29(out_63), .out30(out_64),
    .out31(out_65), .in(in_33), .sel(priority_encoder_1_p1));
endmodule
